// Logisim project cpu_dynamic_branch_predict.circ as structural Verilog: 20 circuits, main circuit ◇单周期MIPS
module \单周期MIPS  (
);

  wire and_1_out, and_4_out, and_5_out, and_6_out, bltz, ByteOrWord, CLK, comparator_1_eq, comparator_2_lt,
       condbranch, display, Go, JAL, JMP, JR, mips_alu_1_equal, not_1_out, not_3_out, not_4_out, not_5_out,
       pause, pcable, RST, shamtsrc, SignedExt, syscall, \硬布线控制器_1_alu_src , \硬布线控制器_1_beq , \硬布线控制器_1_bne ,
       \硬布线控制器_1_memtoreg , \硬布线控制器_1_memwrite , \硬布线控制器_1_regdst , \硬布线控制器_1_regwrite ;
  wire [1:0] bytechoose;
  wire [3:0] \硬布线控制器_1_alu_op ;
  wire [4:0] multiplexer_4_out, multiplexer_5_out, multiplexer_7_out, multiplexer_9_out, multiplexer_12_out;
  wire [5:0] F, OP;
  wire [15:0] \总周期数 , \无条件分支数 , \条件分支成功数 ;
  wire [27:0] adder_1_out;
  wire [31:0] and_7_out, beqbneaddr, bit_extender_1_out, bit_extender_2_out, LedData, memdata,
       multiplexer_1_out, multiplexer_2_out, multiplexer_3_out, multiplexer_6_out, multiplexer_8_out,
       multiplexer_10_out, multiplexer_11_out, multiplexer_13_out, PC_q, shifter_1_out, shifter_2_out,
       syspara, sysreg;
  wire [31:2] mips_alu_1_result;
  wire [31:8] rom_1_data;

  Button \u_总复位  (.out(RST));
  Button \u_继续运行  (.out(Go));
  Clock clock_1 (.out(CLK));
  not not_1 (not_1_out, Go);
  Register #(.width(32)) PC (.D(multiplexer_3_out), .en(pcable), .Q(PC_q), .clk(CLK), .clr(RST));
  not not_2 (pcable, and_1_out);
  and and_1 (and_1_out, not_1_out, pause);
  Hex_Digit_Display hex_digit_display_1 (.value(LedData[27:24]));  // open: dp
  Hex_Digit_Display hex_digit_display_2 (.value(LedData[31:28]));  // open: dp
  Multiplexer #(.width(32), .enable("false")) multiplexer_1 (
    .in0({rom_1_data, F, 2'b00}), .in1(sysreg), .out(multiplexer_1_out), .sel(JR));
  Comparator #(.width(32)) comparator_1 (.a(syspara), .b(32'h22), .eq(comparator_1_eq));  // open: gt, lt
  not not_3 (not_3_out, comparator_1_eq);
  Hex_Digit_Display hex_digit_display_3 (.value(LedData[23:20]));  // open: dp
  Hex_Digit_Display hex_digit_display_4 (.value(LedData[19:16]));  // open: dp
  Multiplexer #(.width(32), .enable("false")) multiplexer_2 (
    .in0({rom_1_data[31:28], adder_1_out}), .in1(beqbneaddr), .out(multiplexer_2_out), .sel(condbranch));
  Adder #(.width(32)) adder_1 (.a(PC_q), .b(32'h4), .out({rom_1_data[31:28], adder_1_out}));  // open: cin, cout
  and and_2 (display, comparator_1_eq, syscall);
  and and_3 (pause, syscall, not_3_out);
  Hex_Digit_Display hex_digit_display_5 (.value(LedData[11:8]));  // open: dp
  Hex_Digit_Display hex_digit_display_6 (.value(LedData[15:12]));  // open: dp
  Multiplexer #(.width(32), .enable("false")) multiplexer_3 (
    .in0(multiplexer_2_out), .in1(multiplexer_1_out), .out(multiplexer_3_out), .sel(JMP));
  Counter #(.width(16), .max('hffff)) counter_1 (
    .count(pcable), .Q(\总周期数 ), .clk(CLK), .clr(RST));  // open: load, D, carry
  Hex_Digit_Display hex_digit_display_7 (.value(LedData[7:4]));  // open: dp
  Hex_Digit_Display hex_digit_display_8 (.value(LedData[3:0]));  // open: dp
  ROM #(.addrWidth(10), .dataWidth(32)) rom_1 (.addr(PC_q[11:2]), .data({OP, rom_1_data[27:8], F}));  // open: sel
  Adder #(.width(32)) adder_2 (
    .a(shifter_1_out), .b({rom_1_data[31:28], adder_1_out}), .out(beqbneaddr));  // open: cin, cout
  Multiplexer #(.width(5), .enable("false")) multiplexer_4 (
    .in0(rom_1_data[27:23]), .in1(5'b00100), .out(multiplexer_4_out), .sel(syscall));
  Multiplexer #(.width(5), .enable("false")) multiplexer_5 (
    .in0(rom_1_data[22:18]), .in1(rom_1_data[17:13]), .out(multiplexer_5_out), .sel(\硬布线控制器_1_regdst ));
  Multiplexer #(.width(32), .enable("false")) multiplexer_6 (
    .in0(multiplexer_8_out), .in1({rom_1_data[31:28], adder_1_out}), .out(multiplexer_6_out), .sel(JAL));
  Shifter #(.width(32)) shifter_1 (.in(bit_extender_1_out), .\dist (5'b00010), .out(shifter_1_out));
  // newcontrol newcontrol_1: pin names not known; wires that end beside it: OP[0], OP[1], OP[2], OP[3], OP[4], OP[5], F[0], F[1], F[2], F[3], F[4], F[5], shamtsrc, ByteOrWord, bltz
  Register #(.width(32)) register_1 (.D(sysreg), .en(display), .Q(LedData), .clk(CLK), .clr(RST));
  // Probe on \总周期数 
  // Probe on \无条件分支数 
  // Probe on \条件分支成功数 
  \硬布线控制器  \u_硬布线控制器_1  (
    .Func(F), .OP(OP), .ALU_OP(\硬布线控制器_1_alu_op ), .MemToReg(\硬布线控制器_1_memtoreg ),
    .MemWrite(\硬布线控制器_1_memwrite ), .ALU_SRC(\硬布线控制器_1_alu_src ), .RegWrite(\硬布线控制器_1_regwrite ),
    .SysCALL(syscall), .SignedExt(SignedExt), .RegDst(\硬布线控制器_1_regdst ), .JR(JR), .JMP(JMP),
    .Beq(\硬布线控制器_1_beq ), .JAL(JAL), .Bne(\硬布线控制器_1_bne ));
  Multiplexer #(.width(5), .enable("false")) multiplexer_7 (
    .in0(multiplexer_5_out), .in1({5{1'b1}}), .out(multiplexer_7_out), .sel(JAL));
  Multiplexer #(.width(32), .enable("false")) multiplexer_8 (
    .in0({mips_alu_1_result, bytechoose}), .in1(multiplexer_13_out), .out(multiplexer_8_out),
    .sel(\硬布线控制器_1_memtoreg ));
  Multiplexer #(.width(5), .enable("false")) multiplexer_9 (
    .in0(rom_1_data[22:18]), .in1(5'b00010), .out(multiplexer_9_out), .sel(syscall));
  assign bit_extender_1_out = {{16{rom_1_data[17]}}, {rom_1_data[17:8], F}};  // Bit_Extender bit_extender_1
  assign bit_extender_2_out = {{16{1'b0}}, {rom_1_data[17:8], F}};  // Bit_Extender bit_extender_2
  MIPS_Regifile mips_regifile_1 (
    .Din(multiplexer_6_out), .Clk(CLK), .R1(syspara), .R2(sysreg), .WE(\硬布线控制器_1_regwrite ),
    .W_num(multiplexer_7_out), .R1_num(multiplexer_9_out), .R2_num(multiplexer_4_out));
  Counter #(.width(16), .max('hffff)) counter_2 (
    .count(JMP), .Q(\无条件分支数 ), .clk(CLK), .clr(RST));  // open: load, D, carry
  Multiplexer #(.width(32), .enable("false")) multiplexer_10 (
    .in0(bit_extender_2_out), .in1(bit_extender_1_out), .out(multiplexer_10_out), .sel(SignedExt));
  and and_4 (and_4_out, \硬布线控制器_1_beq , mips_alu_1_equal);
  Multiplexer #(.width(32), .enable("false")) multiplexer_11 (
    .in0(syspara), .in1(multiplexer_10_out), .out(multiplexer_11_out), .sel(\硬布线控制器_1_alu_src ));
  Multiplexer #(.width(5), .enable("false")) multiplexer_12 (
    .in0(rom_1_data[12:8]), .in1(sysreg[4:0]), .out(multiplexer_12_out), .sel(shamtsrc));
  or or_1 (condbranch, and_4_out, and_5_out, and_6_out);
  and and_5 (and_5_out, not_4_out, \硬布线控制器_1_bne );
  not not_4 (not_4_out, mips_alu_1_equal);
  MIPS_ALU mips_alu_1 (
    .X(sysreg), .Y(multiplexer_11_out), .AluOP(\硬布线控制器_1_alu_op ), .Equal(mips_alu_1_equal),
    .Result({mips_alu_1_result, bytechoose}), .shamt(multiplexer_12_out));  // open: Result_2
  and and_6 (and_6_out, bltz, comparator_2_lt);
  not not_5 (not_5_out, \硬布线控制器_1_memwrite );
  Counter #(.width(16), .max('hffff)) counter_3 (
    .count(condbranch), .Q(\条件分支成功数 ), .clk(CLK), .clr(RST));  // open: load, D, carry
  Comparator #(.width(32)) comparator_2 (.a(sysreg), .b({32{1'b0}}), .lt(comparator_2_lt));  // open: gt, eq
  Multiplexer #(.width(32), .enable("false")) multiplexer_13 (
    .in0(memdata), .in1(and_7_out), .out(multiplexer_13_out), .sel(ByteOrWord));
  RAM #(.addrWidth(10), .dataWidth(32), .bus("separate")) ram_1 (
    .addr(mips_alu_1_result[11:2]), .din(syspara), .data(memdata), .str(\硬布线控制器_1_memwrite ), .clk(CLK),
    .ld(not_5_out), .clr(RST));  // open: sel
  assign and_7_out = 32'hff & shifter_2_out;  // AND_Gate and_7, 32 bits wide
  Shifter #(.width(32), .shift("lr")) shifter_2 (.in(memdata), .\dist ({bytechoose, 3'b000}), .out(shifter_2_out));

  // Notes on the sheet:
  //   JR
  //   J
  //   +1
  //   JAL
  //   数码管输出应该用寄存器锁存，否则显示数据只能一闪而过
  //   可以通过项目增加Logisim库的方式将前几次实验完成的电路作为子电路引入到本电路中使用
  //   beq
  //   指令存储器
  //   bne
  //   数码管输出
  //   OP
  //   Func
  //   rs
  //   contents of rom_1 (hex, n*v repeats v):
  //   20110001 8000c05 20110001 20120002 20130003 8000c09 20110001 20120002 20130003 8000c0d 20110001
  //   20120002 20130003 8000c11 20110001 20120002 20130003 c000cbb 20100001 20110001 118fc0 112020
  //   20020022 c 118882 12200001 8000c15 112020 20020022 c 20110001 118880 112020 20020022 c 12200001
  //   8000c1f 20110001 118fc0 112020 20020022 c 1188c3 112020 20020022 c 118903 112020 20020022 c 118903
  //   112020 20020022 c 118903 112020 20020022 c 118903 112020 20020022 c 118903 112020 20020022 c 118903
  //   112020 20020022 c 118903 112020 20020022 c 20100001 109fc0 139fc3 8021 2012000c 24160003 26100001
  //   3210000f 20080008 20090001 139900 2709825 132020 20020022 c 1094022 1500fff9 22100001 2018000f
  //   2188024 108700 20080008 20090001 139902 2709825 132021 20020022 c 1094022 1500fff9 108702 2c9b022
  //   12c00001 8000c50 4020 1084027 84400 3508ffff 82021 20020022 c 2010ffff 20110000 ae300000 22100001
  //   22310004 ae300000 22100001 22310004 ae300000 22100001 22310004 ae300000 22100001 22310004 ae300000
  //   22100001 22310004 ae300000 22100001 22310004 ae300000 22100001 22310004 ae300000 22100001 22310004
  //   ae300000 22100001 22310004 ae300000 22100001 22310004 ae300000 22100001 22310004 ae300000 22100001
  //   22310004 ae300000 22100001 22310004 ae300000 22100001 22310004 ae300000 22100001 22310004 ae300000
  //   22100001 22310004 22100001 8020 2011003c 8e130000 8e340000 274402a 11000002 ae330000 ae140000
  //   2231fffc 1611fff8 102020 20020022 c 22100004 2011003c 1611fff2 20020032 c 8000c00 2002000a c
  //   20100000 22100001 102020 20020022 c 22100002 102020 20020022 c 22100003 102020 20020022 c 22100004
  //   102020 20020022 c 22100005 102020 20020022 c 22100006 102020 20020022 c 22100007 102020 20020022 c
  //   22100008 102020 20020022 20020022 c 3e00008
  //   指令字
  //   rt
  //   rd
  //   总复位信号应将除ROM以外所有存储组件全部清零
  //   Beq
  //   JMP
  //   JR
  //   Bne
  //   OP
  //   JAL
  //   Func
  //   Syscall
  //   MemToReg
  //   MemWrite
  //   AluOP
  //   AluSrcB
  //   RegWrite
  //   RegDst
  //   SW
  //   lw
  //   addi
  //   ANDI
  //   slti
  //   addiu
  //   ORI
  //   beq =  bne!=
endmodule

// 单周期硬布线控制器
module \硬布线控制器  (
  input  [5:0] OP,
  input  [5:0] Func,
  output [3:0] ALU_OP,
  output MemToReg,
  output MemWrite,
  output ALU_SRC,
  output RegWrite,
  output SysCALL,
  output SignedExt,
  output RegDst,
  output Beq,
  output Bne,
  output JR,
  output JMP,
  output JAL
);

  \运算控制器  \u_运算控制器_1  (
    .OP0(OP[0]), .OP1(OP[1]), .OP2(OP[2]), .OP3(OP[3]), .OP4(OP[4]), .OP5(OP[5]), .F0(Func[0]), .F1(Func[1]),
    .F2(Func[2]), .F3(Func[3]), .F4(Func[4]), .F5(Func[5]), .S0(ALU_OP[0]), .S1(ALU_OP[1]), .S2(ALU_OP[2]),
    .S3(ALU_OP[3]));
  \控制信号生成  \u_控制信号生成_1  (
    .OP0(OP[0]), .OP1(OP[1]), .OP2(OP[2]), .OP3(OP[3]), .OP4(OP[4]), .OP5(OP[5]), .F0(Func[0]), .F1(Func[1]),
    .F2(Func[2]), .F3(Func[3]), .F4(Func[4]), .F5(Func[5]), .MemToReg(MemToReg), .MemWrite(MemWrite),
    .ALU_SRC(ALU_SRC), .RegWrite(RegWrite), .SysCALL(SysCALL), .SignedExt(SignedExt), .RegDst(RegDst),
    .BEQ(Beq), .BNE(Bne), .JR(JR), .JMP(JMP), .JAL(JAL));

  // Other names for the same wires on the sheet: OP_CODE[5:0] = OP

  // Notes on the sheet:
  //   运算器控制器，根据指令生成运算器功能选择信号
  //   控制信号生成，产生数据通路需要的其他控制信号
endmodule

// 运算器控制器
module \运算控制器  (
  input  OP0,
  input  OP1,
  input  OP2,
  input  OP3,
  input  OP4,
  input  OP5,
  input  F0,
  input  F1,
  input  F2,
  input  F3,
  input  F4,
  input  F5,
  output S0,
  output S1,
  output S2,
  output S3
);

  wire and_1_out, and_2_out, and_3_out, and_4_out, and_5_out, and_6_out, and_7_out, and_8_out, and_9_out,
       and_10_out, and_11_out, and_12_out, and_13_out, and_14_out, and_15_out, and_16_out, and_17_out,
       and_18_out, and_19_out, and_20_out, and_21_out, and_22_out, and_23_out, and_24_out, and_25_out,
       and_26_out, and_27_out, and_28_out, and_29_out, and_30_out, and_31_out, and_32_out, and_33_out,
       and_34_out, and_35_out, and_36_out, and_37_out, and_38_out, not_1_out, not_2_out, not_3_out,
       not_4_out, not_5_out, not_6_out, not_7_out, not_8_out, not_9_out, not_10_out, not_11_out, not_12_out,
       not_13_out, not_14_out, not_15_out, not_16_out, not_17_out, not_18_out, not_19_out, not_20_out,
       not_21_out, not_22_out, not_23_out, not_24_out, not_25_out, not_26_out, not_27_out, not_28_out,
       not_29_out, not_30_out, not_31_out, not_32_out, not_33_out, not_34_out, not_35_out, not_36_out,
       not_37_out, not_38_out, not_39_out, not_40_out, not_41_out, not_42_out, not_43_out, not_44_out,
       not_45_out, not_46_out, not_47_out, not_48_out, not_49_out, not_50_out, not_51_out, not_52_out,
       not_53_out, not_54_out, not_55_out, not_56_out, not_57_out, not_58_out, not_59_out, not_60_out,
       not_61_out, not_62_out, not_63_out, not_64_out, not_65_out, not_66_out, not_67_out, not_68_out,
       not_69_out, not_70_out, not_71_out, not_72_out, not_73_out, not_74_out, not_75_out, not_76_out,
       not_77_out, not_78_out, not_79_out, not_80_out, not_81_out, not_82_out, not_83_out, not_84_out,
       not_85_out, not_86_out, not_87_out, not_88_out, not_89_out, not_90_out, not_91_out, not_92_out,
       not_93_out, not_94_out, not_95_out, not_96_out, not_97_out, not_98_out, not_99_out, not_100_out,
       not_101_out, not_102_out, not_103_out, not_104_out, not_105_out, not_106_out, not_107_out,
       not_108_out, not_109_out, not_110_out, not_111_out, not_112_out, not_113_out, not_114_out,
       not_115_out, not_116_out, not_117_out, not_118_out, not_119_out, not_120_out, not_121_out,
       not_122_out, not_123_out, not_124_out, not_125_out, not_126_out, not_127_out, not_128_out,
       not_129_out, not_130_out, not_131_out, not_132_out, not_133_out, not_134_out, not_135_out,
       not_136_out, not_137_out, not_138_out, not_139_out, not_140_out, not_141_out, not_142_out,
       not_143_out, not_144_out, not_145_out, not_146_out, not_147_out, not_148_out, not_149_out,
       not_150_out, not_151_out, not_152_out, not_153_out, not_154_out, not_155_out, not_156_out,
       not_157_out, not_158_out, not_159_out, not_160_out, not_161_out, not_162_out, not_163_out,
       not_164_out, not_165_out, not_166_out, not_167_out, not_168_out, not_169_out, not_170_out,
       not_171_out, not_172_out, not_173_out, not_174_out, not_175_out, not_176_out, not_177_out,
       not_178_out, not_179_out, not_180_out, not_181_out, not_182_out, not_183_out, not_184_out,
       not_185_out, not_186_out, not_187_out, not_188_out, not_189_out, not_190_out, not_191_out,
       not_192_out, not_193_out, not_194_out, not_195_out, not_196_out, not_197_out, not_198_out,
       not_199_out, not_200_out, not_201_out, not_202_out, not_203_out, not_204_out, not_205_out,
       not_206_out, not_207_out, not_208_out, not_209_out, not_210_out, not_211_out, not_212_out,
       not_213_out, not_214_out, not_215_out, not_216_out, not_217_out, not_218_out, not_219_out,
       not_220_out, not_221_out, not_222_out, not_223_out, not_224_out, not_225_out, not_226_out,
       not_227_out, not_228_out, not_229_out, not_230_out, not_231_out, not_232_out, not_233_out,
       not_234_out, not_235_out, not_236_out, not_237_out, not_238_out, not_239_out, not_240_out,
       not_241_out, not_242_out, not_243_out, not_244_out, not_245_out, not_246_out, not_247_out,
       not_248_out, not_249_out, not_250_out;

  not not_1 (not_1_out, OP5);
  not not_2 (not_2_out, OP4);
  not not_3 (not_3_out, OP3);
  not not_4 (not_4_out, OP2);
  not not_5 (not_5_out, OP1);
  not not_6 (not_6_out, OP0);
  not not_7 (not_7_out, F5);
  not not_8 (not_8_out, F4);
  not not_9 (not_9_out, F3);
  not not_10 (not_10_out, F2);
  not not_11 (not_11_out, OP5);
  not not_12 (not_12_out, OP4);
  not not_13 (not_13_out, OP3);
  not not_14 (not_14_out, OP2);
  not not_15 (not_15_out, OP1);
  not not_16 (not_16_out, OP0);
  not not_17 (not_17_out, F4);
  not not_18 (not_18_out, F3);
  not not_19 (not_19_out, F2);
  not not_20 (not_20_out, F1);
  not not_21 (not_21_out, F0);
  not not_22 (not_22_out, OP5);
  not not_23 (not_23_out, OP4);
  not not_24 (not_24_out, OP3);
  not not_25 (not_25_out, OP2);
  not not_26 (not_26_out, OP1);
  not not_27 (not_27_out, OP0);
  not not_28 (not_28_out, F4);
  not not_29 (not_29_out, F3);
  not not_30 (not_30_out, F2);
  not not_31 (not_31_out, F1);
  not not_32 (not_32_out, OP5);
  not not_33 (not_33_out, OP4);
  not not_34 (not_34_out, OP3);
  not not_35 (not_35_out, OP2);
  not not_36 (not_36_out, OP1);
  not not_37 (not_37_out, OP0);
  not not_38 (not_38_out, F4);
  not not_39 (not_39_out, F3);
  not not_40 (not_40_out, F1);
  not not_41 (not_41_out, F0);
  not not_42 (not_42_out, OP5);
  not not_43 (not_43_out, OP4);
  not not_44 (not_44_out, OP3);
  not not_45 (not_45_out, OP2);
  not not_46 (not_46_out, OP1);
  not not_47 (not_47_out, OP0);
  not not_48 (not_48_out, F4);
  not not_49 (not_49_out, F2);
  not not_50 (not_50_out, F0);
  not not_51 (not_51_out, OP5);
  not not_52 (not_52_out, OP4);
  not not_53 (not_53_out, OP2);
  not not_54 (not_54_out, OP1);
  not not_55 (not_55_out, OP0);
  not not_56 (not_56_out, OP5);
  not not_57 (not_57_out, OP4);
  not not_58 (not_58_out, OP1);
  not not_59 (not_59_out, OP0);
  not not_60 (not_60_out, OP5);
  not not_61 (not_61_out, OP4);
  not not_62 (not_62_out, OP2);
  not not_63 (not_63_out, OP1);
  not not_64 (not_64_out, OP5);
  not not_65 (not_65_out, OP4);
  not not_66 (not_66_out, OP2);
  not not_67 (not_67_out, OP0);
  not not_68 (not_68_out, OP4);
  not not_69 (not_69_out, OP3);
  not not_70 (not_70_out, OP2);
  not not_71 (not_71_out, OP4);
  not not_72 (not_72_out, OP2);
  not not_73 (not_73_out, OP5);
  not not_74 (not_74_out, OP4);
  not not_75 (not_75_out, OP0);
  not not_76 (not_76_out, OP4);
  not not_77 (not_77_out, OP3);
  not not_78 (not_78_out, OP1);
  not not_79 (not_79_out, OP0);
  not not_80 (not_80_out, OP5);
  not not_81 (not_81_out, OP4);
  not not_82 (not_82_out, OP3);
  not not_83 (not_83_out, OP2);
  not not_84 (not_84_out, OP1);
  not not_85 (not_85_out, OP0);
  not not_86 (not_86_out, F5);
  not not_87 (not_87_out, F4);
  not not_88 (not_88_out, F3);
  not not_89 (not_89_out, F2);
  not not_90 (not_90_out, F0);
  not not_91 (not_91_out, OP5);
  not not_92 (not_92_out, OP4);
  not not_93 (not_93_out, OP3);
  not not_94 (not_94_out, OP2);
  not not_95 (not_95_out, OP1);
  not not_96 (not_96_out, OP0);
  not not_97 (not_97_out, F4);
  not not_98 (not_98_out, F3);
  not not_99 (not_99_out, F2);
  not not_100 (not_100_out, F0);
  not not_101 (not_101_out, OP5);
  not not_102 (not_102_out, OP4);
  not not_103 (not_103_out, OP3);
  not not_104 (not_104_out, OP2);
  not not_105 (not_105_out, OP1);
  not not_106 (not_106_out, OP0);
  not not_107 (not_107_out, F4);
  not not_108 (not_108_out, F3);
  not not_109 (not_109_out, F1);
  not not_110 (not_110_out, F0);
  not not_111 (not_111_out, OP5);
  not not_112 (not_112_out, OP4);
  not not_113 (not_113_out, OP3);
  not not_114 (not_114_out, OP2);
  not not_115 (not_115_out, OP1);
  not not_116 (not_116_out, OP0);
  not not_117 (not_117_out, F4);
  not not_118 (not_118_out, F3);
  not not_119 (not_119_out, OP5);
  not not_120 (not_120_out, OP4);
  not not_121 (not_121_out, OP3);
  not not_122 (not_122_out, OP2);
  not not_123 (not_123_out, OP1);
  not not_124 (not_124_out, OP0);
  not not_125 (not_125_out, F4);
  not not_126 (not_126_out, F2);
  not not_127 (not_127_out, F0);
  not not_128 (not_128_out, OP5);
  not not_129 (not_129_out, OP4);
  not not_130 (not_130_out, OP1);
  not not_131 (not_131_out, OP0);
  not not_132 (not_132_out, OP5);
  not not_133 (not_133_out, OP4);
  not not_134 (not_134_out, OP2);
  not not_135 (not_135_out, OP0);
  not not_136 (not_136_out, OP5);
  not not_137 (not_137_out, OP4);
  not not_138 (not_138_out, OP3);
  not not_139 (not_139_out, OP2);
  not not_140 (not_140_out, OP1);
  not not_141 (not_141_out, OP0);
  not not_142 (not_142_out, F4);
  not not_143 (not_143_out, F3);
  not not_144 (not_144_out, F2);
  not not_145 (not_145_out, F1);
  not not_146 (not_146_out, F0);
  not not_147 (not_147_out, OP5);
  not not_148 (not_148_out, OP4);
  not not_149 (not_149_out, OP3);
  not not_150 (not_150_out, OP2);
  not not_151 (not_151_out, OP1);
  not not_152 (not_152_out, OP0);
  not not_153 (not_153_out, F4);
  not not_154 (not_154_out, F3);
  not not_155 (not_155_out, F2);
  not not_156 (not_156_out, F1);
  not not_157 (not_157_out, OP5);
  not not_158 (not_158_out, OP4);
  not not_159 (not_159_out, OP3);
  not not_160 (not_160_out, OP2);
  not not_161 (not_161_out, OP1);
  not not_162 (not_162_out, OP0);
  not not_163 (not_163_out, F4);
  not not_164 (not_164_out, F3);
  not not_165 (not_165_out, F2);
  not not_166 (not_166_out, F0);
  not not_167 (not_167_out, OP5);
  not not_168 (not_168_out, OP4);
  not not_169 (not_169_out, OP3);
  not not_170 (not_170_out, OP2);
  not not_171 (not_171_out, OP1);
  not not_172 (not_172_out, OP0);
  not not_173 (not_173_out, F4);
  not not_174 (not_174_out, F3);
  not not_175 (not_175_out, F1);
  not not_176 (not_176_out, F0);
  not not_177 (not_177_out, OP5);
  not not_178 (not_178_out, OP4);
  not not_179 (not_179_out, OP3);
  not not_180 (not_180_out, OP2);
  not not_181 (not_181_out, OP1);
  not not_182 (not_182_out, OP0);
  not not_183 (not_183_out, F4);
  not not_184 (not_184_out, F2);
  not not_185 (not_185_out, OP5);
  not not_186 (not_186_out, OP4);
  not not_187 (not_187_out, OP2);
  not not_188 (not_188_out, OP1);
  not not_189 (not_189_out, OP0);
  not not_190 (not_190_out, OP5);
  not not_191 (not_191_out, OP4);
  not not_192 (not_192_out, OP1);
  not not_193 (not_193_out, OP0);
  not not_194 (not_194_out, OP5);
  not not_195 (not_195_out, OP4);
  not not_196 (not_196_out, OP2);
  not not_197 (not_197_out, OP1);
  not not_198 (not_198_out, OP4);
  not not_199 (not_199_out, OP3);
  not not_200 (not_200_out, OP2);
  not not_201 (not_201_out, OP4);
  not not_202 (not_202_out, OP2);
  not not_203 (not_203_out, OP4);
  not not_204 (not_204_out, OP3);
  not not_205 (not_205_out, OP1);
  not not_206 (not_206_out, OP0);
  not not_207 (not_207_out, OP5);
  not not_208 (not_208_out, OP4);
  not not_209 (not_209_out, OP3);
  not not_210 (not_210_out, OP2);
  not not_211 (not_211_out, OP1);
  not not_212 (not_212_out, OP0);
  not not_213 (not_213_out, F4);
  not not_214 (not_214_out, F3);
  not not_215 (not_215_out, F1);
  not not_216 (not_216_out, OP5);
  not not_217 (not_217_out, OP4);
  not not_218 (not_218_out, OP3);
  not not_219 (not_219_out, OP2);
  not not_220 (not_220_out, OP1);
  not not_221 (not_221_out, OP0);
  not not_222 (not_222_out, F4);
  not not_223 (not_223_out, F3);
  not not_224 (not_224_out, OP5);
  not not_225 (not_225_out, OP4);
  not not_226 (not_226_out, OP3);
  not not_227 (not_227_out, OP2);
  not not_228 (not_228_out, OP1);
  not not_229 (not_229_out, OP0);
  not not_230 (not_230_out, F4);
  not not_231 (not_231_out, F2);
  not not_232 (not_232_out, F0);
  not not_233 (not_233_out, OP5);
  not not_234 (not_234_out, OP4);
  not not_235 (not_235_out, OP3);
  not not_236 (not_236_out, OP2);
  not not_237 (not_237_out, OP1);
  not not_238 (not_238_out, OP0);
  not not_239 (not_239_out, F4);
  not not_240 (not_240_out, F2);
  not not_241 (not_241_out, OP5);
  not not_242 (not_242_out, OP4);
  not not_243 (not_243_out, OP2);
  not not_244 (not_244_out, OP0);
  not not_245 (not_245_out, OP5);
  not not_246 (not_246_out, OP4);
  not not_247 (not_247_out, OP1);
  not not_248 (not_248_out, OP5);
  not not_249 (not_249_out, OP4);
  not not_250 (not_250_out, OP0);
  and and_1 (and_1_out, not_1_out, not_2_out, not_3_out, not_4_out, not_5_out, not_6_out, not_7_out, not_8_out, not_9_out, not_10_out, F1, F0);
  and and_2 (and_2_out, not_11_out, not_12_out, not_13_out, not_14_out, not_15_out, not_16_out, F5, not_17_out, not_18_out, not_19_out, not_20_out, not_21_out);
  and and_3 (and_3_out, not_22_out, not_23_out, not_24_out, not_25_out, not_26_out, not_27_out, F5, not_28_out, not_29_out, not_30_out, not_31_out, F0);
  and and_4 (and_4_out, not_32_out, not_33_out, not_34_out, not_35_out, not_36_out, not_37_out, F5, not_38_out, not_39_out, F2, not_40_out, not_41_out);
  and and_5 (and_5_out, not_42_out, not_43_out, not_44_out, not_45_out, not_46_out, not_47_out, F5, not_48_out, F3, not_49_out, F1, not_50_out);
  and and_6 (and_6_out, not_51_out, not_52_out, OP3, not_53_out, not_54_out, not_55_out);
  and and_7 (and_7_out, not_56_out, not_57_out, OP3, OP2, not_58_out, not_59_out);
  and and_8 (and_8_out, not_60_out, not_61_out, OP3, not_62_out, not_63_out, OP0);
  and and_9 (and_9_out, not_64_out, not_65_out, OP3, not_66_out, OP1, not_67_out);
  and and_10 (and_10_out, OP5, not_68_out, not_69_out, not_70_out, OP1, OP0);
  and and_11 (and_11_out, OP5, not_71_out, OP3, not_72_out, OP1, OP0);
  and and_12 (and_12_out, not_73_out, not_74_out, OP3, OP2, OP1, not_75_out);
  and and_13 (and_13_out, OP5, not_76_out, not_77_out, OP2, not_78_out, not_79_out);
  and and_14 (and_14_out, not_80_out, not_81_out, not_82_out, not_83_out, not_84_out, not_85_out, not_86_out, not_87_out, not_88_out, not_89_out, F1, not_90_out);
  and and_15 (and_15_out, not_91_out, not_92_out, not_93_out, not_94_out, not_95_out, not_96_out, F5, not_97_out, not_98_out, not_99_out, F1, not_100_out);
  and and_16 (and_16_out, not_101_out, not_102_out, not_103_out, not_104_out, not_105_out, not_106_out, F5, not_107_out, not_108_out, F2, not_109_out, not_110_out);
  and and_17 (and_17_out, not_111_out, not_112_out, not_113_out, not_114_out, not_115_out, not_116_out, F5, not_117_out, not_118_out, F2, F1, F0);
  and and_18 (and_18_out, not_119_out, not_120_out, not_121_out, not_122_out, not_123_out, not_124_out, F5, not_125_out, F3, not_126_out, F1, not_127_out);
  and and_19 (and_19_out, not_128_out, not_129_out, OP3, OP2, not_130_out, not_131_out);
  and and_20 (and_20_out, not_132_out, not_133_out, OP3, not_134_out, OP1, not_135_out);
  and and_21 (and_21_out, not_136_out, not_137_out, not_138_out, not_139_out, not_140_out, not_141_out, F5, not_142_out, not_143_out, not_144_out, not_145_out, not_146_out);
  and and_22 (and_22_out, not_147_out, not_148_out, not_149_out, not_150_out, not_151_out, not_152_out, F5, not_153_out, not_154_out, not_155_out, not_156_out, F0);
  and and_23 (and_23_out, not_157_out, not_158_out, not_159_out, not_160_out, not_161_out, not_162_out, F5, not_163_out, not_164_out, not_165_out, F1, not_166_out);
  and and_24 (and_24_out, not_167_out, not_168_out, not_169_out, not_170_out, not_171_out, not_172_out, F5, not_173_out, not_174_out, F2, not_175_out, not_176_out);
  and and_25 (and_25_out, not_177_out, not_178_out, not_179_out, not_180_out, not_181_out, not_182_out, F5, not_183_out, F3, not_184_out, F1, F0);
  and and_26 (and_26_out, not_185_out, not_186_out, OP3, not_187_out, not_188_out, not_189_out);
  and and_27 (and_27_out, not_190_out, not_191_out, OP3, OP2, not_192_out, not_193_out);
  and and_28 (and_28_out, not_194_out, not_195_out, OP3, not_196_out, not_197_out, OP0);
  and and_29 (and_29_out, OP5, not_198_out, not_199_out, not_200_out, OP1, OP0);
  and and_30 (and_30_out, OP5, not_201_out, OP3, not_202_out, OP1, OP0);
  and and_31 (and_31_out, OP5, not_203_out, not_204_out, OP2, not_205_out, not_206_out);
  and and_32 (and_32_out, not_207_out, not_208_out, not_209_out, not_210_out, not_211_out, not_212_out, F5, not_213_out, not_214_out, F2, not_215_out, F0);
  and and_33 (and_33_out, not_216_out, not_217_out, not_218_out, not_219_out, not_220_out, not_221_out, F5, not_222_out, not_223_out, F2, F1, F0);
  and and_34 (and_34_out, not_224_out, not_225_out, not_226_out, not_227_out, not_228_out, not_229_out, F5, not_230_out, F3, not_231_out, F1, not_232_out);
  and and_35 (and_35_out, not_233_out, not_234_out, not_235_out, not_236_out, not_237_out, not_238_out, F5, not_239_out, F3, not_240_out, F1, F0);
  and and_36 (and_36_out, not_241_out, not_242_out, OP3, not_243_out, OP1, not_244_out);
  and and_37 (and_37_out, not_245_out, not_246_out, OP3, OP2, not_247_out, OP0);
  and and_38 (and_38_out, not_248_out, not_249_out, OP3, OP2, OP1, not_250_out);
  or or_1 (S1, and_14_out, and_15_out, and_16_out, and_17_out, and_18_out, and_19_out, and_20_out);
  or or_2 (S2, and_21_out, and_22_out, and_23_out, and_24_out, and_25_out, and_26_out, and_27_out, and_28_out, and_29_out, and_30_out, and_31_out);
  or or_3 (S3, and_32_out, and_33_out, and_34_out, and_35_out, and_36_out, and_37_out, and_38_out);
  or or_4 (S0, and_1_out, and_2_out, and_3_out, and_4_out, and_5_out, and_6_out, and_7_out, and_8_out, and_9_out, and_10_out, and_11_out, and_12_out, and_13_out);
endmodule

// 控制信号生成
module \控制信号生成  (
  input  OP0,
  input  OP1,
  input  OP2,
  input  OP3,
  input  OP4,
  input  OP5,
  input  F0,
  input  F1,
  input  F2,
  input  F3,
  input  F4,
  input  F5,
  output MemToReg,
  output MemWrite,
  output ALU_SRC,
  output RegWrite,
  output SysCALL,
  output SignedExt,
  output RegDst,
  output BEQ,
  output BNE,
  output JR,
  output JMP,
  output JAL
);

  wire and_1_out, and_2_out, and_4_out, and_5_out, and_6_out, and_7_out, and_8_out, and_9_out, and_10_out,
       and_11_out, and_12_out, and_13_out, and_14_out, and_15_out, and_16_out, and_17_out, and_18_out,
       and_19_out, and_20_out, and_21_out, and_22_out, and_23_out, and_24_out, and_25_out, and_26_out,
       and_27_out, and_28_out, and_29_out, and_30_out, and_31_out, and_32_out, and_33_out, and_35_out,
       and_36_out, and_37_out, and_38_out, and_39_out, and_40_out, and_41_out, and_42_out, and_43_out,
       and_44_out, and_45_out, and_46_out, and_47_out, and_48_out, and_49_out, and_50_out, and_51_out,
       and_52_out, and_53_out, and_54_out, and_58_out, and_59_out, and_60_out, not_1_out, not_2_out,
       not_3_out, not_4_out, not_5_out, not_6_out, not_7_out, not_8_out, not_9_out, not_10_out, not_11_out,
       not_12_out, not_13_out, not_14_out, not_15_out, not_16_out, not_17_out, not_18_out, not_19_out,
       not_20_out, not_21_out, not_22_out, not_23_out, not_24_out, not_25_out, not_26_out, not_27_out,
       not_28_out, not_29_out, not_30_out, not_31_out, not_32_out, not_33_out, not_34_out, not_35_out,
       not_36_out, not_37_out, not_38_out, not_39_out, not_40_out, not_41_out, not_42_out, not_43_out,
       not_44_out, not_45_out, not_46_out, not_47_out, not_48_out, not_49_out, not_50_out, not_51_out,
       not_52_out, not_53_out, not_54_out, not_55_out, not_56_out, not_57_out, not_58_out, not_59_out,
       not_60_out, not_61_out, not_62_out, not_63_out, not_64_out, not_65_out, not_66_out, not_67_out,
       not_68_out, not_69_out, not_70_out, not_71_out, not_72_out, not_73_out, not_74_out, not_75_out,
       not_76_out, not_77_out, not_78_out, not_79_out, not_80_out, not_81_out, not_82_out, not_83_out,
       not_84_out, not_85_out, not_86_out, not_87_out, not_88_out, not_89_out, not_90_out, not_91_out,
       not_92_out, not_93_out, not_94_out, not_95_out, not_96_out, not_97_out, not_98_out, not_99_out,
       not_100_out, not_101_out, not_102_out, not_103_out, not_104_out, not_105_out, not_106_out,
       not_107_out, not_108_out, not_109_out, not_110_out, not_111_out, not_112_out, not_113_out,
       not_114_out, not_115_out, not_116_out, not_117_out, not_118_out, not_119_out, not_120_out,
       not_121_out, not_122_out, not_123_out, not_124_out, not_125_out, not_126_out, not_127_out,
       not_128_out, not_129_out, not_130_out, not_131_out, not_132_out, not_133_out, not_134_out,
       not_135_out, not_136_out, not_137_out, not_138_out, not_139_out, not_140_out, not_141_out,
       not_142_out, not_143_out, not_144_out, not_145_out, not_146_out, not_147_out, not_148_out,
       not_149_out, not_150_out, not_151_out, not_152_out, not_153_out, not_154_out, not_155_out,
       not_156_out, not_157_out, not_158_out, not_159_out, not_160_out, not_161_out, not_162_out,
       not_163_out, not_164_out, not_165_out, not_166_out, not_167_out, not_168_out, not_169_out,
       not_170_out, not_171_out, not_172_out, not_173_out, not_174_out, not_175_out, not_176_out,
       not_177_out, not_178_out, not_179_out, not_180_out, not_181_out, not_182_out, not_183_out,
       not_184_out, not_185_out, not_186_out, not_187_out, not_188_out, not_189_out, not_190_out,
       not_191_out, not_192_out, not_193_out, not_194_out, not_195_out, not_196_out, not_197_out,
       not_198_out, not_199_out, not_200_out, not_201_out, not_202_out, not_203_out, not_204_out,
       not_205_out, not_206_out, not_207_out, not_208_out, not_209_out, not_210_out, not_211_out,
       not_212_out, not_213_out, not_214_out, not_215_out, not_216_out, not_217_out, not_218_out,
       not_219_out, not_220_out, not_221_out, not_222_out, not_223_out, not_224_out, not_225_out,
       not_226_out, not_227_out, not_228_out, not_229_out, not_230_out, not_231_out, not_232_out,
       not_233_out, not_234_out, not_235_out, not_236_out, not_237_out, not_238_out, not_239_out,
       not_240_out, not_241_out, not_242_out, not_243_out, not_244_out, not_245_out, not_246_out,
       not_247_out, not_248_out, not_249_out, not_250_out, not_251_out, not_252_out, not_253_out,
       not_254_out, not_255_out, not_256_out, not_257_out, not_258_out, not_259_out, not_260_out,
       not_261_out, not_262_out, not_263_out, not_264_out, not_265_out, not_266_out, not_267_out,
       not_268_out, not_269_out, not_270_out, not_271_out, not_272_out, not_273_out, not_274_out,
       not_275_out, not_276_out, not_277_out, not_278_out, not_279_out, not_280_out, not_281_out,
       not_282_out, not_283_out, not_284_out, not_285_out, not_286_out, not_287_out, not_288_out,
       not_289_out, not_290_out, not_291_out, not_292_out, not_293_out, not_294_out, not_295_out,
       not_296_out, not_297_out, not_298_out, not_299_out, not_300_out, not_301_out, not_302_out,
       not_303_out, not_304_out, not_305_out, not_306_out, not_307_out, not_308_out, not_309_out,
       not_310_out, not_311_out, not_312_out, not_313_out, not_314_out, not_315_out, not_316_out,
       not_317_out, not_318_out, not_319_out, not_320_out, not_321_out, not_322_out, not_323_out,
       not_324_out, not_325_out, not_326_out, not_327_out, not_328_out, not_329_out, not_330_out,
       not_331_out, not_332_out, not_333_out, not_334_out, not_335_out, not_336_out, not_337_out,
       not_338_out, not_339_out, not_340_out, not_341_out, not_342_out, not_343_out, not_344_out,
       not_345_out, not_346_out, not_347_out, not_348_out, not_349_out, not_350_out, not_351_out,
       not_352_out, not_353_out, not_354_out, not_355_out, not_356_out, not_357_out, not_358_out,
       not_359_out, not_360_out, not_361_out, not_362_out, not_363_out, not_364_out, not_365_out,
       not_366_out, not_367_out, not_368_out, not_369_out, not_370_out, not_371_out, not_372_out,
       not_373_out, not_374_out, not_375_out, not_376_out, not_377_out, not_378_out, not_379_out,
       not_380_out, not_381_out, not_382_out, not_383_out, not_384_out, not_385_out, not_386_out,
       not_387_out, not_388_out, not_389_out, not_390_out, not_391_out, not_392_out, not_393_out,
       not_394_out, not_395_out, not_396_out, not_397_out, not_398_out;

  not not_1 (not_1_out, OP4);
  not not_2 (not_2_out, OP3);
  not not_3 (not_3_out, OP2);
  not not_4 (not_4_out, OP4);
  not not_5 (not_5_out, OP3);
  not not_6 (not_6_out, OP1);
  not not_7 (not_7_out, OP0);
  not not_8 (not_8_out, OP4);
  not not_9 (not_9_out, OP2);
  not not_10 (not_10_out, OP5);
  not not_11 (not_11_out, OP4);
  not not_12 (not_12_out, OP2);
  not not_13 (not_13_out, OP1);
  not not_14 (not_14_out, OP0);
  not not_15 (not_15_out, OP5);
  not not_16 (not_16_out, OP4);
  not not_17 (not_17_out, OP1);
  not not_18 (not_18_out, OP0);
  not not_19 (not_19_out, OP5);
  not not_20 (not_20_out, OP4);
  not not_21 (not_21_out, OP2);
  not not_22 (not_22_out, OP1);
  not not_23 (not_23_out, OP5);
  not not_24 (not_24_out, OP4);
  not not_25 (not_25_out, OP2);
  not not_26 (not_26_out, OP0);
  not not_27 (not_27_out, OP5);
  not not_28 (not_28_out, OP4);
  not not_29 (not_29_out, OP1);
  not not_30 (not_30_out, OP4);
  not not_31 (not_31_out, OP3);
  not not_32 (not_32_out, OP2);
  not not_33 (not_33_out, OP4);
  not not_34 (not_34_out, OP2);
  not not_35 (not_35_out, OP5);
  not not_36 (not_36_out, OP4);
  not not_37 (not_37_out, OP0);
  not not_38 (not_38_out, OP4);
  not not_39 (not_39_out, OP3);
  not not_40 (not_40_out, OP1);
  not not_41 (not_41_out, OP0);
  not not_42 (not_42_out, OP5);
  not not_43 (not_43_out, OP4);
  not not_44 (not_44_out, OP3);
  not not_45 (not_45_out, OP2);
  not not_46 (not_46_out, OP1);
  not not_47 (not_47_out, OP0);
  not not_48 (not_48_out, F5);
  not not_49 (not_49_out, F4);
  not not_50 (not_50_out, F3);
  not not_51 (not_51_out, F2);
  not not_52 (not_52_out, F1);
  not not_53 (not_53_out, F0);
  not not_54 (not_54_out, OP5);
  not not_55 (not_55_out, OP4);
  not not_56 (not_56_out, OP3);
  not not_57 (not_57_out, OP2);
  not not_58 (not_58_out, OP1);
  not not_59 (not_59_out, OP0);
  not not_60 (not_60_out, F5);
  not not_61 (not_61_out, F4);
  not not_62 (not_62_out, F3);
  not not_63 (not_63_out, F2);
  not not_64 (not_64_out, OP5);
  not not_65 (not_65_out, OP4);
  not not_66 (not_66_out, OP3);
  not not_67 (not_67_out, OP2);
  not not_68 (not_68_out, OP1);
  not not_69 (not_69_out, OP0);
  not not_70 (not_70_out, F5);
  not not_71 (not_71_out, F4);
  not not_72 (not_72_out, F3);
  not not_73 (not_73_out, F2);
  not not_74 (not_74_out, F0);
  not not_75 (not_75_out, OP5);
  not not_76 (not_76_out, OP4);
  not not_77 (not_77_out, OP3);
  not not_78 (not_78_out, OP2);
  not not_79 (not_79_out, OP1);
  not not_80 (not_80_out, OP0);
  not not_81 (not_81_out, F4);
  not not_82 (not_82_out, F3);
  not not_83 (not_83_out, F2);
  not not_84 (not_84_out, F1);
  not not_85 (not_85_out, F0);
  not not_86 (not_86_out, OP5);
  not not_87 (not_87_out, OP4);
  not not_88 (not_88_out, OP3);
  not not_89 (not_89_out, OP2);
  not not_90 (not_90_out, OP1);
  not not_91 (not_91_out, OP0);
  not not_92 (not_92_out, F4);
  not not_93 (not_93_out, F3);
  not not_94 (not_94_out, F2);
  not not_95 (not_95_out, F1);
  not not_96 (not_96_out, OP5);
  not not_97 (not_97_out, OP4);
  not not_98 (not_98_out, OP3);
  not not_99 (not_99_out, OP2);
  not not_100 (not_100_out, OP1);
  not not_101 (not_101_out, OP0);
  not not_102 (not_102_out, F4);
  not not_103 (not_103_out, F3);
  not not_104 (not_104_out, F2);
  not not_105 (not_105_out, F0);
  not not_106 (not_106_out, OP5);
  not not_107 (not_107_out, OP4);
  not not_108 (not_108_out, OP3);
  not not_109 (not_109_out, OP2);
  not not_110 (not_110_out, OP1);
  not not_111 (not_111_out, OP0);
  not not_112 (not_112_out, F4);
  not not_113 (not_113_out, F3);
  not not_114 (not_114_out, F1);
  not not_115 (not_115_out, F0);
  not not_116 (not_116_out, OP5);
  not not_117 (not_117_out, OP4);
  not not_118 (not_118_out, OP3);
  not not_119 (not_119_out, OP2);
  not not_120 (not_120_out, OP1);
  not not_121 (not_121_out, OP0);
  not not_122 (not_122_out, F4);
  not not_123 (not_123_out, F3);
  not not_124 (not_124_out, F1);
  not not_125 (not_125_out, OP5);
  not not_126 (not_126_out, OP4);
  not not_127 (not_127_out, OP3);
  not not_128 (not_128_out, OP2);
  not not_129 (not_129_out, OP1);
  not not_130 (not_130_out, OP0);
  not not_131 (not_131_out, F4);
  not not_132 (not_132_out, F3);
  not not_133 (not_133_out, OP5);
  not not_134 (not_134_out, OP4);
  not not_135 (not_135_out, OP3);
  not not_136 (not_136_out, OP2);
  not not_137 (not_137_out, OP1);
  not not_138 (not_138_out, OP0);
  not not_139 (not_139_out, F4);
  not not_140 (not_140_out, F2);
  not not_141 (not_141_out, F0);
  not not_142 (not_142_out, OP5);
  not not_143 (not_143_out, OP4);
  not not_144 (not_144_out, OP3);
  not not_145 (not_145_out, OP2);
  not not_146 (not_146_out, OP1);
  not not_147 (not_147_out, OP0);
  not not_148 (not_148_out, F4);
  not not_149 (not_149_out, F2);
  not not_150 (not_150_out, OP5);
  not not_151 (not_151_out, OP4);
  not not_152 (not_152_out, OP2);
  not not_153 (not_153_out, OP1);
  not not_154 (not_154_out, OP0);
  not not_155 (not_155_out, OP5);
  not not_156 (not_156_out, OP4);
  not not_157 (not_157_out, OP1);
  not not_158 (not_158_out, OP0);
  not not_159 (not_159_out, OP5);
  not not_160 (not_160_out, OP4);
  not not_161 (not_161_out, OP2);
  not not_162 (not_162_out, OP1);
  not not_163 (not_163_out, OP5);
  not not_164 (not_164_out, OP4);
  not not_165 (not_165_out, OP2);
  not not_166 (not_166_out, OP0);
  not not_167 (not_167_out, OP5);
  not not_168 (not_168_out, OP4);
  not not_169 (not_169_out, OP1);
  not not_170 (not_170_out, OP4);
  not not_171 (not_171_out, OP3);
  not not_172 (not_172_out, OP2);
  not not_173 (not_173_out, OP5);
  not not_174 (not_174_out, OP4);
  not not_175 (not_175_out, OP3);
  not not_176 (not_176_out, OP2);
  not not_177 (not_177_out, OP5);
  not not_178 (not_178_out, OP4);
  not not_179 (not_179_out, OP3);
  not not_180 (not_180_out, OP2);
  not not_181 (not_181_out, OP1);
  not not_182 (not_182_out, OP0);
  not not_183 (not_183_out, F5);
  not not_184 (not_184_out, F4);
  not not_185 (not_185_out, F3);
  not not_186 (not_186_out, F1);
  not not_187 (not_187_out, F0);
  not not_188 (not_188_out, OP5);
  not not_189 (not_189_out, OP4);
  not not_190 (not_190_out, OP0);
  not not_191 (not_191_out, OP4);
  not not_192 (not_192_out, OP3);
  not not_193 (not_193_out, OP1);
  not not_194 (not_194_out, OP0);
  not not_195 (not_195_out, OP5);
  not not_196 (not_196_out, OP4);
  not not_197 (not_197_out, OP3);
  not not_198 (not_198_out, OP2);
  not not_199 (not_199_out, OP1);
  not not_200 (not_200_out, OP0);
  not not_201 (not_201_out, F5);
  not not_202 (not_202_out, F4);
  not not_203 (not_203_out, F1);
  not not_204 (not_204_out, F0);
  not not_205 (not_205_out, OP5);
  not not_206 (not_206_out, OP4);
  not not_207 (not_207_out, OP2);
  not not_208 (not_208_out, OP1);
  not not_209 (not_209_out, OP0);
  not not_210 (not_210_out, OP5);
  not not_211 (not_211_out, OP4);
  not not_212 (not_212_out, OP2);
  not not_213 (not_213_out, OP1);
  not not_214 (not_214_out, OP5);
  not not_215 (not_215_out, OP4);
  not not_216 (not_216_out, OP2);
  not not_217 (not_217_out, OP0);
  not not_218 (not_218_out, OP4);
  not not_219 (not_219_out, OP3);
  not not_220 (not_220_out, OP2);
  not not_221 (not_221_out, OP4);
  not not_222 (not_222_out, OP2);
  not not_223 (not_223_out, OP4);
  not not_224 (not_224_out, OP3);
  not not_225 (not_225_out, OP1);
  not not_226 (not_226_out, OP0);
  not not_227 (not_227_out, OP5);
  not not_228 (not_228_out, OP4);
  not not_229 (not_229_out, OP3);
  not not_230 (not_230_out, OP1);
  not not_231 (not_231_out, OP0);
  not not_232 (not_232_out, OP5);
  not not_233 (not_233_out, OP4);
  not not_234 (not_234_out, OP3);
  not not_235 (not_235_out, OP1);
  not not_236 (not_236_out, OP5);
  not not_237 (not_237_out, OP4);
  not not_238 (not_238_out, OP3);
  not not_239 (not_239_out, OP2);
  not not_240 (not_240_out, OP1);
  not not_241 (not_241_out, OP0);
  not not_242 (not_242_out, F5);
  not not_243 (not_243_out, F4);
  not not_244 (not_244_out, F3);
  not not_245 (not_245_out, F2);
  not not_246 (not_246_out, F1);
  not not_247 (not_247_out, F0);
  not not_248 (not_248_out, OP5);
  not not_249 (not_249_out, OP4);
  not not_250 (not_250_out, OP3);
  not not_251 (not_251_out, OP2);
  not not_252 (not_252_out, OP1);
  not not_253 (not_253_out, OP0);
  not not_254 (not_254_out, F5);
  not not_255 (not_255_out, F4);
  not not_256 (not_256_out, F3);
  not not_257 (not_257_out, F2);
  not not_258 (not_258_out, OP5);
  not not_259 (not_259_out, OP4);
  not not_260 (not_260_out, OP3);
  not not_261 (not_261_out, OP2);
  not not_262 (not_262_out, OP1);
  not not_263 (not_263_out, OP0);
  not not_264 (not_264_out, F5);
  not not_265 (not_265_out, F4);
  not not_266 (not_266_out, F3);
  not not_267 (not_267_out, F2);
  not not_268 (not_268_out, F0);
  not not_269 (not_269_out, OP5);
  not not_270 (not_270_out, OP4);
  not not_271 (not_271_out, OP3);
  not not_272 (not_272_out, OP2);
  not not_273 (not_273_out, OP1);
  not not_274 (not_274_out, OP0);
  not not_275 (not_275_out, F4);
  not not_276 (not_276_out, F3);
  not not_277 (not_277_out, F2);
  not not_278 (not_278_out, F1);
  not not_279 (not_279_out, F0);
  not not_280 (not_280_out, OP5);
  not not_281 (not_281_out, OP4);
  not not_282 (not_282_out, OP3);
  not not_283 (not_283_out, OP2);
  not not_284 (not_284_out, OP1);
  not not_285 (not_285_out, OP0);
  not not_286 (not_286_out, F4);
  not not_287 (not_287_out, F3);
  not not_288 (not_288_out, F2);
  not not_289 (not_289_out, F1);
  not not_290 (not_290_out, OP5);
  not not_291 (not_291_out, OP4);
  not not_292 (not_292_out, OP3);
  not not_293 (not_293_out, OP2);
  not not_294 (not_294_out, OP1);
  not not_295 (not_295_out, OP0);
  not not_296 (not_296_out, F4);
  not not_297 (not_297_out, F3);
  not not_298 (not_298_out, F2);
  not not_299 (not_299_out, F0);
  not not_300 (not_300_out, OP5);
  not not_301 (not_301_out, OP4);
  not not_302 (not_302_out, OP3);
  not not_303 (not_303_out, OP2);
  not not_304 (not_304_out, OP1);
  not not_305 (not_305_out, OP0);
  not not_306 (not_306_out, F4);
  not not_307 (not_307_out, F3);
  not not_308 (not_308_out, F1);
  not not_309 (not_309_out, F0);
  not not_310 (not_310_out, OP5);
  not not_311 (not_311_out, OP4);
  not not_312 (not_312_out, OP3);
  not not_313 (not_313_out, OP2);
  not not_314 (not_314_out, OP1);
  not not_315 (not_315_out, OP0);
  not not_316 (not_316_out, F4);
  not not_317 (not_317_out, F3);
  not not_318 (not_318_out, F1);
  not not_319 (not_319_out, OP5);
  not not_320 (not_320_out, OP4);
  not not_321 (not_321_out, OP3);
  not not_322 (not_322_out, OP2);
  not not_323 (not_323_out, OP1);
  not not_324 (not_324_out, OP0);
  not not_325 (not_325_out, F4);
  not not_326 (not_326_out, F3);
  not not_327 (not_327_out, OP5);
  not not_328 (not_328_out, OP4);
  not not_329 (not_329_out, OP3);
  not not_330 (not_330_out, OP2);
  not not_331 (not_331_out, OP1);
  not not_332 (not_332_out, OP0);
  not not_333 (not_333_out, F4);
  not not_334 (not_334_out, F2);
  not not_335 (not_335_out, F0);
  not not_336 (not_336_out, OP5);
  not not_337 (not_337_out, OP4);
  not not_338 (not_338_out, OP3);
  not not_339 (not_339_out, OP2);
  not not_340 (not_340_out, OP1);
  not not_341 (not_341_out, OP0);
  not not_342 (not_342_out, F4);
  not not_343 (not_343_out, F2);
  not not_344 (not_344_out, OP5);
  not not_345 (not_345_out, OP4);
  not not_346 (not_346_out, OP3);
  not not_347 (not_347_out, OP2);
  not not_348 (not_348_out, OP1);
  not not_349 (not_349_out, OP0);
  not not_350 (not_350_out, F5);
  not not_351 (not_351_out, F4);
  not not_352 (not_352_out, F3);
  not not_353 (not_353_out, F1);
  not not_354 (not_354_out, F0);
  not not_355 (not_355_out, OP5);
  not not_356 (not_356_out, OP4);
  not not_357 (not_357_out, OP3);
  not not_358 (not_358_out, OP1);
  not not_359 (not_359_out, OP0);
  not not_360 (not_360_out, OP5);
  not not_361 (not_361_out, OP4);
  not not_362 (not_362_out, OP3);
  not not_363 (not_363_out, OP1);
  not not_364 (not_364_out, OP5);
  not not_365 (not_365_out, OP4);
  not not_366 (not_366_out, OP3);
  not not_367 (not_367_out, OP2);
  not not_368 (not_368_out, OP1);
  not not_369 (not_369_out, OP0);
  not not_370 (not_370_out, F5);
  not not_371 (not_371_out, F4);
  not not_372 (not_372_out, F2);
  not not_373 (not_373_out, F1);
  not not_374 (not_374_out, F0);
  not not_375 (not_375_out, OP5);
  not not_376 (not_376_out, OP4);
  not not_377 (not_377_out, OP3);
  not not_378 (not_378_out, OP2);
  not not_379 (not_379_out, OP1);
  not not_380 (not_380_out, OP0);
  not not_381 (not_381_out, F5);
  not not_382 (not_382_out, F4);
  not not_383 (not_383_out, F2);
  not not_384 (not_384_out, F1);
  not not_385 (not_385_out, F0);
  not not_386 (not_386_out, OP5);
  not not_387 (not_387_out, OP4);
  not not_388 (not_388_out, OP3);
  not not_389 (not_389_out, OP2);
  not not_390 (not_390_out, OP0);
  not not_391 (not_391_out, OP5);
  not not_392 (not_392_out, OP4);
  not not_393 (not_393_out, OP3);
  not not_394 (not_394_out, OP2);
  not not_395 (not_395_out, OP5);
  not not_396 (not_396_out, OP4);
  not not_397 (not_397_out, OP3);
  not not_398 (not_398_out, OP2);
  and and_1 (and_1_out, OP5, not_1_out, not_2_out, not_3_out, OP1, OP0);
  and and_2 (and_2_out, OP5, not_4_out, not_5_out, OP2, not_6_out, not_7_out);
  and and_3 (MemWrite, OP5, not_8_out, OP3, not_9_out, OP1, OP0);
  and and_4 (and_4_out, not_10_out, not_11_out, OP3, not_12_out, not_13_out, not_14_out);
  and and_5 (and_5_out, not_15_out, not_16_out, OP3, OP2, not_17_out, not_18_out);
  and and_6 (and_6_out, not_19_out, not_20_out, OP3, not_21_out, not_22_out, OP0);
  and and_7 (and_7_out, not_23_out, not_24_out, OP3, not_25_out, OP1, not_26_out);
  and and_8 (and_8_out, not_27_out, not_28_out, OP3, OP2, not_29_out, OP0);
  and and_9 (and_9_out, OP5, not_30_out, not_31_out, not_32_out, OP1, OP0);
  and and_10 (and_10_out, OP5, not_33_out, OP3, not_34_out, OP1, OP0);
  and and_11 (and_11_out, not_35_out, not_36_out, OP3, OP2, OP1, not_37_out);
  and and_12 (and_12_out, OP5, not_38_out, not_39_out, OP2, not_40_out, not_41_out);
  and and_13 (and_13_out, not_42_out, not_43_out, not_44_out, not_45_out, not_46_out, not_47_out, not_48_out, not_49_out, not_50_out, not_51_out, not_52_out, not_53_out);
  and and_14 (and_14_out, not_54_out, not_55_out, not_56_out, not_57_out, not_58_out, not_59_out, not_60_out, not_61_out, not_62_out, not_63_out, F1, F0);
  and and_15 (and_15_out, not_64_out, not_65_out, not_66_out, not_67_out, not_68_out, not_69_out, not_70_out, not_71_out, not_72_out, not_73_out, F1, not_74_out);
  and and_16 (and_16_out, not_75_out, not_76_out, not_77_out, not_78_out, not_79_out, not_80_out, F5, not_81_out, not_82_out, not_83_out, not_84_out, not_85_out);
  and and_17 (and_17_out, not_86_out, not_87_out, not_88_out, not_89_out, not_90_out, not_91_out, F5, not_92_out, not_93_out, not_94_out, not_95_out, F0);
  and and_18 (and_18_out, not_96_out, not_97_out, not_98_out, not_99_out, not_100_out, not_101_out, F5, not_102_out, not_103_out, not_104_out, F1, not_105_out);
  and and_19 (and_19_out, not_106_out, not_107_out, not_108_out, not_109_out, not_110_out, not_111_out, F5, not_112_out, not_113_out, F2, not_114_out, not_115_out);
  and and_20 (and_20_out, not_116_out, not_117_out, not_118_out, not_119_out, not_120_out, not_121_out, F5, not_122_out, not_123_out, F2, not_124_out, F0);
  and and_21 (and_21_out, not_125_out, not_126_out, not_127_out, not_128_out, not_129_out, not_130_out, F5, not_131_out, not_132_out, F2, F1, F0);
  and and_22 (and_22_out, not_133_out, not_134_out, not_135_out, not_136_out, not_137_out, not_138_out, F5, not_139_out, F3, not_140_out, F1, not_141_out);
  and and_23 (and_23_out, not_142_out, not_143_out, not_144_out, not_145_out, not_146_out, not_147_out, F5, not_148_out, F3, not_149_out, F1, F0);
  and and_24 (and_24_out, not_150_out, not_151_out, OP3, not_152_out, not_153_out, not_154_out);
  and and_25 (and_25_out, not_155_out, not_156_out, OP3, OP2, not_157_out, not_158_out);
  and and_26 (and_26_out, not_159_out, not_160_out, OP3, not_161_out, not_162_out, OP0);
  and and_27 (and_27_out, not_163_out, not_164_out, OP3, not_165_out, OP1, not_166_out);
  and and_28 (and_28_out, not_167_out, not_168_out, OP3, OP2, not_169_out, OP0);
  and and_29 (and_29_out, OP5, not_170_out, not_171_out, not_172_out, OP1, OP0);
  and and_30 (and_30_out, not_173_out, not_174_out, not_175_out, not_176_out, OP1, OP0);
  and and_31 (and_31_out, not_177_out, not_178_out, not_179_out, not_180_out, not_181_out, not_182_out, not_183_out, not_184_out, not_185_out, F2, not_186_out, not_187_out);
  and and_32 (and_32_out, not_188_out, not_189_out, OP3, OP2, OP1, not_190_out);
  and and_33 (and_33_out, OP5, not_191_out, not_192_out, OP2, not_193_out, not_194_out);
  and and_34 (SysCALL, not_195_out, not_196_out, not_197_out, not_198_out, not_199_out, not_200_out, not_201_out, not_202_out, F3, F2, not_203_out, not_204_out);
  and and_35 (and_35_out, not_205_out, not_206_out, OP3, not_207_out, not_208_out, not_209_out);
  and and_36 (and_36_out, not_210_out, not_211_out, OP3, not_212_out, not_213_out, OP0);
  and and_37 (and_37_out, not_214_out, not_215_out, OP3, not_216_out, OP1, not_217_out);
  and and_38 (and_38_out, OP5, not_218_out, not_219_out, not_220_out, OP1, OP0);
  and and_39 (and_39_out, OP5, not_221_out, OP3, not_222_out, OP1, OP0);
  and and_40 (and_40_out, OP5, not_223_out, not_224_out, OP2, not_225_out, not_226_out);
  and and_41 (and_41_out, not_227_out, not_228_out, not_229_out, OP2, not_230_out, not_231_out);
  and and_42 (and_42_out, not_232_out, not_233_out, not_234_out, OP2, not_235_out, OP0);
  and and_43 (and_43_out, not_236_out, not_237_out, not_238_out, not_239_out, not_240_out, not_241_out, not_242_out, not_243_out, not_244_out, not_245_out, not_246_out, not_247_out);
  and and_44 (and_44_out, not_248_out, not_249_out, not_250_out, not_251_out, not_252_out, not_253_out, not_254_out, not_255_out, not_256_out, not_257_out, F1, F0);
  and and_45 (and_45_out, not_258_out, not_259_out, not_260_out, not_261_out, not_262_out, not_263_out, not_264_out, not_265_out, not_266_out, not_267_out, F1, not_268_out);
  and and_46 (and_46_out, not_269_out, not_270_out, not_271_out, not_272_out, not_273_out, not_274_out, F5, not_275_out, not_276_out, not_277_out, not_278_out, not_279_out);
  and and_47 (and_47_out, not_280_out, not_281_out, not_282_out, not_283_out, not_284_out, not_285_out, F5, not_286_out, not_287_out, not_288_out, not_289_out, F0);
  and and_48 (and_48_out, not_290_out, not_291_out, not_292_out, not_293_out, not_294_out, not_295_out, F5, not_296_out, not_297_out, not_298_out, F1, not_299_out);
  and and_49 (and_49_out, not_300_out, not_301_out, not_302_out, not_303_out, not_304_out, not_305_out, F5, not_306_out, not_307_out, F2, not_308_out, not_309_out);
  and and_50 (and_50_out, not_310_out, not_311_out, not_312_out, not_313_out, not_314_out, not_315_out, F5, not_316_out, not_317_out, F2, not_318_out, F0);
  and and_51 (and_51_out, not_319_out, not_320_out, not_321_out, not_322_out, not_323_out, not_324_out, F5, not_325_out, not_326_out, F2, F1, F0);
  and and_52 (and_52_out, not_327_out, not_328_out, not_329_out, not_330_out, not_331_out, not_332_out, F5, not_333_out, F3, not_334_out, F1, not_335_out);
  and and_53 (and_53_out, not_336_out, not_337_out, not_338_out, not_339_out, not_340_out, not_341_out, F5, not_342_out, F3, not_343_out, F1, F0);
  and and_54 (and_54_out, not_344_out, not_345_out, not_346_out, not_347_out, not_348_out, not_349_out, not_350_out, not_351_out, not_352_out, F2, not_353_out, not_354_out);
  and and_55 (BEQ, not_355_out, not_356_out, not_357_out, OP2, not_358_out, not_359_out);
  and and_56 (BNE, not_360_out, not_361_out, not_362_out, OP2, not_363_out, OP0);
  and and_57 (JR, not_364_out, not_365_out, not_366_out, not_367_out, not_368_out, not_369_out, not_370_out, not_371_out, F3, not_372_out, not_373_out, not_374_out);
  and and_58 (and_58_out, not_375_out, not_376_out, not_377_out, not_378_out, not_379_out, not_380_out, not_381_out, not_382_out, F3, not_383_out, not_384_out, not_385_out);
  and and_59 (and_59_out, not_386_out, not_387_out, not_388_out, not_389_out, OP1, not_390_out);
  and and_60 (and_60_out, not_391_out, not_392_out, not_393_out, not_394_out, OP1, OP0);
  and and_61 (JAL, not_395_out, not_396_out, not_397_out, not_398_out, OP1, OP0);
  or or_1 (MemToReg, and_1_out, and_2_out);
  or or_2 (ALU_SRC, and_4_out, and_5_out, and_6_out, and_7_out, and_8_out, and_9_out, and_10_out, and_11_out, and_12_out);
  or or_3 (SignedExt, and_35_out, and_36_out, and_37_out, and_38_out, and_39_out, and_40_out, and_41_out, and_42_out);
  or or_4 (JMP, and_58_out, and_59_out, and_60_out);
  or or_5 (RegWrite, and_13_out, and_14_out, and_15_out, and_16_out, and_17_out, and_18_out, and_19_out, and_20_out, and_21_out, and_22_out, and_23_out, and_24_out, and_25_out, and_26_out, and_27_out, and_28_out, and_29_out, and_30_out, and_31_out, and_32_out, and_33_out);
  or or_6 (RegDst, and_43_out, and_44_out, and_45_out, and_46_out, and_47_out, and_48_out, and_49_out, and_50_out, and_51_out, and_52_out, and_53_out, and_54_out);
endmodule

// ALU
module MIPS_ALU (
  input  [4:0] shamt,
  input  [31:0] X,
  input  [31:0] Y,
  input  [3:0] AluOP,
  output Equal,
  output [31:0] Result,
  output [31:0] Result_2
);

  wire [0:0] comparator_1_lt, comparator_2_lt;
  wire [31:0] adder_1_out, AND_out, divider_1_out, divider_1_rem, multiplier_1_cout, multiplier_1_out,
       NOR_out, OR_out, shifter_1_out, shifter_2_out, shifter_3_out, subtractor_1_out, XOR_out;

  assign AND_out = X & Y;  // AND_Gate AND, 32 bits wide
  assign OR_out = X | Y;  // OR_Gate OR, 32 bits wide
  Shifter #(.width(32)) shifter_1 (.in(Y), .\dist (shamt), .out(shifter_1_out));
  Shifter #(.width(32), .shift("ar")) shifter_2 (.in(Y), .\dist (shamt), .out(shifter_2_out));
  Shifter #(.width(32), .shift("lr")) shifter_3 (.in(Y), .\dist (shamt), .out(shifter_3_out));
  Multiplier #(.width(32)) multiplier_1 (.a(X), .b(Y), .out(multiplier_1_out), .cout(multiplier_1_cout));  // open: cin
  Divider #(.width(32)) divider_1 (.a(X), .b(Y), .out(divider_1_out), .rem(divider_1_rem));  // open: upper
  Adder #(.width(32)) adder_1 (.a(X), .b(Y), .out(adder_1_out));  // open: cin, cout
  Subtractor #(.width(32)) subtractor_1 (.a(X), .b(Y), .out(subtractor_1_out));  // open: bin, bout
  assign XOR_out = X ^ Y;  // XOR_Gate XOR, 32 bits wide
  assign NOR_out = ~(X | Y);  // NOR_Gate NOR, 32 bits wide
  Comparator #(.width(32)) comparator_1 (.a(X), .b(Y), .eq(Equal), .lt(comparator_1_lt[0]));  // open: gt
  Comparator #(.width(32), .mode("unsigned")) comparator_2 (.a(X), .b(Y), .lt(comparator_2_lt[0]));  // open: gt, eq
  Multiplexer #(.select(4), .width(32), .enable("false")) multiplexer_1 (
    .in0(shifter_1_out), .in1(shifter_2_out), .in2(shifter_3_out), .in3(multiplier_1_out),
    .in4(divider_1_out), .in5(adder_1_out), .in6(subtractor_1_out), .in7(AND_out), .in8(OR_out),
    .in9(XOR_out), .in10(NOR_out), .in11({{31{1'b0}}, comparator_1_lt[0]}),
    .in12({{31{1'b0}}, comparator_2_lt[0]}), .in13({32{1'b0}}), .in14({32{1'b0}}), .in15({32{1'b0}}),
    .out(Result), .sel(AluOP));
  Multiplexer #(.select(4), .width(32), .enable("false")) multiplexer_2 (
    .in0({32{1'b0}}), .in1({32{1'b0}}), .in2({32{1'b0}}), .in3(multiplier_1_cout), .in4(divider_1_rem),
    .in5({32{1'b0}}), .in6({32{1'b0}}), .in7({32{1'b0}}), .in8({32{1'b0}}), .in9({32{1'b0}}),
    .in10({32{1'b0}}), .in11({32{1'b0}}), .in12({32{1'b0}}), .in13({32{1'b0}}), .in14({32{1'b0}}),
    .in15({32{1'b0}}), .out(Result_2), .sel(AluOP));

  // Other names for the same wires on the sheet: Result2[31:0] = Result_2; S[3:0] = AluOP

  // Notes on the sheet:
  //   不要改变此引脚区域内容，也不要改变ALU封装形式
  //   输入引脚
  //   逻辑左移
  //   算数右移
  //   逻辑右移
  //   x*y
  //   x/y
  //   x+y
  //   x-y
  //   x=y
  //   x<y
  //    signed cmp
  //   输出引脚
endmodule

module MIPS_Regifile (
  input  [31:0] Din,
  input  Clk,
  input  WE,
  input  [4:0] R1_num,
  input  [4:0] W_num,
  input  [4:0] R2_num,
  output [31:0] R1,
  output [31:0] R2
);

  // RegisterFile registerfile_1: pin names not known; wires that end beside it: Din, Clk, WE, W_num, R1_num, R2_num, R1, R2
endmodule

module \理想流水线  (
);

  wire ALU_src_EX, ALU_src_ID, and_3_out, and_4_out, and_5_out, Beq_EX, Beq_ID, Bne_EX, Bne_ID, branch_EX,
       CLK, comparator_1_eq, condbranch_EX, display_ID, ex_mem_1_enable_out, ex_mem_1_jal_out,
       ex_mem_1_memtoreg_out, ex_mem_1_regdst_out, ex_mem_1_regwrite_out, Go, id_ex_1_enable_out,
       if_id_1_enable_out, IR1, IR2, IR3, JAL_EX, JAL_ID, JAL_WB, JMP_EX, JMP_ID, JR_EX, JR_ID, MemToReg_EX,
       MemToReg_ID, MemToReg_WB, MemWrite_EX, MemWrite_ID, MemWrite_MEM, mips_alu_1_equal, not_1_out,
       not_3_out, not_4_out, not_5_out, or_1_out, or_2_out, or_3_out, pause_ID, pcable, pcable_out,
       RegDst_EX, RegDst_ID, RegDst_WB, RegWrite_EX, RegWrite_ID, RegWrite_WB, RST, SignedExt_ID, syscall_ID,
       W1, W2, W3;
  wire [3:0] ALU_op_EX, ALU_op_ID;
  wire [4:0] ex_mem_1_rd_out, ex_mem_1_rt_out, id_ex_1_shamt_out, multiplexer_4_out, multiplexer_6_out,
       multiplexer_7_out, multiplexer_8_out, Rd_EX, Rd_WB, Rt_EX, Rt_WB;
  wire [15:0] \LoadUse次数 , \总周期数 , \插入气泡数 , \无条件分支数 , \条件分支成功数 ;
  wire [27:0] adder_2_out;
  wire [31:0] adder_1_out, ALU_result_WB, ALUresult_MEM, beqbneaddr_EX, bit_extender_1_out,
       bit_extender_2_out, ex_mem_1_rout, EX_PC, ID_PC, IF_PC, Imm_EX, IR_EX, IR_ID, IR_MEM, IR_WB,
       JAL_WB_Addr, LedData, MEM_PC, MemData_WB, mips_alu_1_result, multiplexer_1_out, multiplexer_2_out,
       multiplexer_3_out, multiplexer_5_out, multiplexer_9_out, multiplexer_10_out, multiplexer_11_out,
       PC_WB, R1_EX, R1_ID, R2_EX, R2_ID, ram_1_data, rom_1_data, shifter_1_out;
  wire [31:2] J_JAL_addr_EX;

  Button \u_总复位  (.out(RST));
  Button _1 (.out(IR1));
  Button _2 (.out(IR2));
  Button _3 (.out(IR3));
  Button \u_继续运行  (.out(Go));
  LED led_1 (.in(W1));
  LED led_2 (.in(W2));
  LED led_3 (.in(W3));
  Multiplexer #(.width(32), .enable("false")) multiplexer_1 (
    .in0(adder_1_out), .in1(beqbneaddr_EX), .out(multiplexer_1_out), .sel(condbranch_EX));
  Multiplexer #(.width(32), .enable("false")) multiplexer_2 (
    .in0({J_JAL_addr_EX, 2'b00}), .in1(R1_EX), .out(multiplexer_2_out), .sel(JR_EX));
  Hex_Digit_Display hex_digit_display_1 (.value(LedData[31:28]));  // open: dp
  Hex_Digit_Display hex_digit_display_2 (.value(LedData[27:24]));  // open: dp
  Multiplexer #(.width(32), .enable("false")) multiplexer_3 (
    .in0(multiplexer_1_out), .in1(multiplexer_2_out), .out(multiplexer_3_out), .sel(JMP_EX));
  Hex_Digit_Display hex_digit_display_3 (.value(LedData[23:20]));  // open: dp
  Hex_Digit_Display hex_digit_display_4 (.value(LedData[19:16]));  // open: dp
  Register #(.width(32)) PC (.D(multiplexer_3_out), .en(pcable), .Q(IF_PC), .clk(CLK), .clr(RST));
  Hex_Digit_Display hex_digit_display_5 (.value(LedData[15:12]));  // open: dp
  Hex_Digit_Display hex_digit_display_6 (.value(LedData[11:8]));  // open: dp
  Comparator #(.width(32)) comparator_1 (.a(R1_ID), .b(32'h22), .eq(comparator_1_eq));  // open: gt, lt
  Hex_Digit_Display hex_digit_display_7 (.value(LedData[7:4]));  // open: dp
  Hex_Digit_Display hex_digit_display_8 (.value(LedData[3:0]));  // open: dp
  Clock clock_1 (.out(CLK));
  not not_1 (not_1_out, comparator_1_eq);
  and and_1 (display_ID, comparator_1_eq, syscall_ID);
  and and_2 (pause_ID, syscall_ID, not_1_out);
  // Probe on \总周期数 
  // Probe on \无条件分支数 
  // Probe on \条件分支成功数 
  // Probe on \插入气泡数 
  // Probe on \LoadUse次数 
  // Probe on IF_PC[11:0]
  ROM #(.addrWidth(10), .dataWidth(32)) rom_1 (.addr(IF_PC[11:2]), .data(rom_1_data));  // open: sel
  // Probe on EX_PC[11:0]
  // Probe on ID_PC[11:0]
  // Probe on IR_ID
  Register #(.width(32)) register_1 (.D(R2_ID), .en(display_ID), .Q(LedData), .clk(CLK), .clr(RST));
  // Probe on MEM_PC[11:0]
  IF_ID if_id_1 (
    .IRin(rom_1_data), .PCin(IF_PC), .IRout(IR_ID), .PCout(ID_PC), .clk(CLK), .enable(pcable),
    .clear_tong(or_1_out), .enable_out(if_id_1_enable_out));  // open: clear_yi, Miss_in, Miss_out, predict_branch_in, predict_branch_out
  or or_1 (or_1_out, RST, branch_EX);
  // Probe on PC_WB[11:0]
  assign bit_extender_1_out = {{16{1'b0}}, IR_ID[15:0]};  // Bit_Extender bit_extender_1
  assign bit_extender_2_out = {{16{IR_ID[15]}}, IR_ID[15:0]};  // Bit_Extender bit_extender_2
  Multiplexer #(.width(5), .enable("false")) multiplexer_4 (
    .in0(Rt_WB), .in1(Rd_WB), .out(multiplexer_4_out), .sel(RegDst_WB));
  Multiplexer #(.width(32), .enable("false")) multiplexer_5 (
    .in0(bit_extender_1_out), .in1(bit_extender_2_out), .out(multiplexer_5_out), .sel(SignedExt_ID));
  Adder #(.width(32)) adder_1 (.a(IF_PC), .b(32'h4), .out(adder_1_out));  // open: cin, cout
  not not_2 (pcable, and_3_out);
  and and_3 (and_3_out, not_3_out, pause_ID);
  not not_3 (not_3_out, Go);
  \硬布线控制器  \u_硬布线控制器_1  (
    .Func(IR_ID[5:0]), .OP(IR_ID[31:26]), .ALU_OP(ALU_op_ID), .MemToReg(MemToReg_ID), .MemWrite(MemWrite_ID),
    .ALU_SRC(ALU_src_ID), .RegWrite(RegWrite_ID), .SysCALL(syscall_ID), .SignedExt(SignedExt_ID),
    .RegDst(RegDst_ID), .JR(JR_ID), .JMP(JMP_ID), .Beq(Beq_ID), .JAL(JAL_ID), .Bne(Bne_ID));
  Multiplexer #(.width(5), .enable("false")) multiplexer_6 (
    .in0(IR_ID[25:21]), .in1(5'b00010), .out(multiplexer_6_out), .sel(syscall_ID));
  Multiplexer #(.width(5), .enable("false")) multiplexer_7 (
    .in0(IR_ID[20:16]), .in1(5'b00100), .out(multiplexer_7_out), .sel(syscall_ID));
  Multiplexer #(.width(5), .enable("false")) multiplexer_8 (
    .in0(multiplexer_4_out), .in1({5{1'b1}}), .out(multiplexer_8_out), .sel(JAL_WB));
  Multiplexer #(.width(32), .enable("false")) multiplexer_9 (
    .in0(multiplexer_10_out), .in1(JAL_WB_Addr), .out(multiplexer_9_out), .sel(JAL_WB));
  Multiplexer #(.width(32), .enable("false")) multiplexer_10 (
    .in0(ALU_result_WB), .in1(MemData_WB), .out(multiplexer_10_out), .sel(MemToReg_WB));
  MIPS_Regifile mips_regifile_1 (
    .Din(multiplexer_9_out), .Clk(CLK), .R1(R1_ID), .R2(R2_ID), .WE(RegWrite_WB), .W_num(multiplexer_8_out),
    .R1_num(multiplexer_6_out), .R2_num(multiplexer_7_out));
  or or_2 (or_2_out, pcable, pcable_out);
  Counter #(.width(16), .max('hffff)) counter_1 (
    .count(or_2_out), .Q(\总周期数 ), .clk(CLK), .clr(RST));  // open: load, D, carry
  ID_EX id_ex_1 (
    .RegDst_in(RegDst_ID), .JAL_in(JAL_ID), .RegWrite_in(RegWrite_ID), .MemToReg_in(MemToReg_ID),
    .MemWrite_in(MemWrite_ID), .ALU_OP_in(ALU_op_ID), .ALU_src_in(ALU_src_ID), .Bne_in(Bne_ID),
    .Beq_in(Beq_ID), .IRin(IR_ID), .PCin(ID_PC), .R1in(R1_ID), .R2in(R2_ID), .IMMin(multiplexer_5_out),
    .RegDst_out(RegDst_EX), .JAL_out(JAL_EX), .RegWrite_out(RegWrite_EX), .MemToReg_out(MemToReg_EX),
    .MemWrite_out(MemWrite_EX), .ALU_OP_out(ALU_op_EX), .ALU_src_out(ALU_src_EX), .Bne_out(Bne_EX),
    .Beq_out(Beq_EX), .out_55(IR_EX), .PCout(EX_PC), .R1out(R1_EX), .R2out(R2_EX), .IMMout(Imm_EX),
    .enable(if_id_1_enable_out), .clk(CLK), .clear_tong(or_3_out), .shamt_in(IR_ID[10:6]),
    .shamt_out(id_ex_1_shamt_out), .enable_out(id_ex_1_enable_out), .Rd_in(IR_ID[15:11]),
    .Rt_in(IR_ID[20:16]), .Rt_out(Rt_EX), .Rd_out(Rd_EX), .JMP_in(JMP_ID), .JR_in(JR_ID), .JMP_out(JMP_EX),
    .JR_out(JR_EX), .J_JAL_imm_in(IR_ID[25:0]), .J_JAL_imm_out(J_JAL_addr_EX[27:2]));  // open: syscall_in, syscall_out, shamtsrc_in, bltz_in, byteorword_in, shamtsrc_out, bltz_out, byteorword_out, forwardB_in, forwardA_in, forwardB_out, forwardA_out, clear_yibu, Miss_in, Miss_out, predict_branch_in, predict_branch_out
  or or_3 (or_3_out, RST, branch_EX);
  Multiplexer #(.width(32), .enable("false")) multiplexer_11 (
    .in0(R2_EX), .in1(Imm_EX), .out(multiplexer_11_out), .sel(ALU_src_EX));
  or or_4 (condbranch_EX, and_5_out, and_4_out);
  and and_4 (and_4_out, not_4_out, Bne_EX);
  and and_5 (and_5_out, Beq_EX, mips_alu_1_equal);
  not not_4 (not_4_out, mips_alu_1_equal);
  MIPS_ALU mips_alu_1 (
    .X(R1_EX), .Y(multiplexer_11_out), .AluOP(ALU_op_EX), .Equal(mips_alu_1_equal),
    .Result(mips_alu_1_result), .shamt(id_ex_1_shamt_out));  // open: Result_2
  Adder #(.width(32)) adder_2 (.a(EX_PC), .b(32'h4), .out({J_JAL_addr_EX[31:28], adder_2_out}));  // open: cin, cout
  Shifter #(.width(32)) shifter_1 (.in(Imm_EX), .\dist (5'b00010), .out(shifter_1_out));
  Counter #(.width(16), .max('hffff)) counter_2 (
    .count(condbranch_EX), .Q(\条件分支成功数 ), .clk(CLK), .clr(RST));  // open: load, D, carry
  or or_5 (branch_EX, JMP_EX, condbranch_EX);
  Adder #(.width(32)) adder_3 (
    .a({J_JAL_addr_EX[31:28], adder_2_out}), .b(shifter_1_out), .out(beqbneaddr_EX));  // open: cin, cout
  Counter #(.width(16), .max('hffff)) counter_3 (
    .count(JMP_EX), .Q(\无条件分支数 ), .clk(CLK), .clr(RST));  // open: load, D, carry
  EX_MEM ex_mem_1 (
    .RegDst_in(RegDst_EX), .JAL_in(JAL_EX), .RegWrite_in(RegWrite_EX), .MemToReg_in(MemToReg_EX),
    .MemWrite_in(MemWrite_EX), .IRin(IR_EX), .PCin(EX_PC), .Rin(R2_EX), .ALUresult_in(mips_alu_1_result),
    .RegDst_out(ex_mem_1_regdst_out), .JAL_out(ex_mem_1_jal_out), .RegWrite_out(ex_mem_1_regwrite_out),
    .MemToReg_out(ex_mem_1_memtoreg_out), .MemWrite_out(MemWrite_MEM), .IRout(IR_MEM), .PCout(MEM_PC),
    .Rout(ex_mem_1_rout), .ALUresult_out(ALUresult_MEM), .enable(id_ex_1_enable_out), .clk(CLK), .clear(RST),
    .enable_out(ex_mem_1_enable_out), .Rt_in(Rt_EX), .Rd_in(Rd_EX), .Rd_out(ex_mem_1_rd_out),
    .Rt_out(ex_mem_1_rt_out));  // open: syscal_in, syscall_out, byteorword_out, byteorword_in
  not not_5 (not_5_out, MemWrite_MEM);
  RAM #(.addrWidth(10), .dataWidth(32), .bus("separate")) ram_1 (
    .addr(ALUresult_MEM[11:2]), .din(ex_mem_1_rout), .data(ram_1_data), .str(MemWrite_MEM), .clk(CLK),
    .ld(not_5_out), .clr(RST));  // open: sel
  MEM_WB MEM_WB (
    .RegDst_in(ex_mem_1_regdst_out), .JAL_in(ex_mem_1_jal_out), .RegWrite_in(ex_mem_1_regwrite_out),
    .MemToReg_in(ex_mem_1_memtoreg_out), .IRin(IR_MEM), .PCin(MEM_PC), .ALUresult_in(ALUresult_MEM),
    .MemData_in(ram_1_data), .RegDst_out(RegDst_WB), .JAL_out(JAL_WB), .RegWrite_out(RegWrite_WB),
    .MemToReg_out(MemToReg_WB), .IRout(IR_WB), .PCout(PC_WB), .ALUresult_out(ALU_result_WB),
    .MemData_out(MemData_WB), .enable(ex_mem_1_enable_out), .clk(CLK), .clear(RST), .enable_out(pcable_out),
    .Rt_out(Rt_WB), .Rd_out(Rd_WB), .Rt_in(ex_mem_1_rt_out), .Rd_in(ex_mem_1_rd_out));  // open: syscall_in, syscall_out, byteorword_in, byteorword_out
  Adder #(.width(32)) adder_4 (.a(PC_WB), .b(32'h4), .out(JAL_WB_Addr));  // open: cin, cout

  // Other names for the same wires on the sheet: J_JAL_imm_EX[25:0] = J_JAL_addr_EX[27:2];
  //   J_JAL_imm_ID[25:0] = IR_ID[25:0]; Rd_ID[4:0] = IR_ID[15:11]; Rt_ID[4:0] = IR_ID[20:16]; PC_EX[31:0] = EX_PC;
  //   PC_ID[31:0] = ID_PC; PC_MEM[31:0] = MEM_PC; WB_PC[31:0] = PC_WB

  // Notes on the sheet:
  //   中断源
  //   中断等待指示
  //   数码管输出
  //   指令存储器
  //   contents of rom_1 (hex, n*v repeats v):
  //   20110001 8000c05 20110001 20120002 20130003 8000c09 20110001 20120002 20130003 8000c0d 20110001
  //   20120002 20130003 8000c11 20110001 20120002 20130003 c000cbb 20100001 20110001 118fc0 112020
  //   20020022 c 118882 12200001 8000c15 112020 20020022 c 20110001 118880 112020 20020022 c 12200001
  //   8000c1f 20110001 118fc0 112020 20020022 c 1188c3 112020 20020022 c 118903 112020 20020022 c 118903
  //   112020 20020022 c 118903 112020 20020022 c 118903 112020 20020022 c 118903 112020 20020022 c 118903
  //   112020 20020022 c 118903 112020 20020022 c 20100001 109fc0 139fc3 8021 2012000c 24160003 26100001
  //   3210000f 20080008 20090001 139900 2709825 132020 20020022 c 1094022 1500fff9 22100001 2018000f
  //   2188024 108700 20080008 20090001 139902 2709825 132021 20020022 c 1094022 1500fff9 108702 2c9b022
  //   12c00001 8000c50 4020 1084027 84400 3508ffff 82021 20020022 c 2010ffff 20110000 ae300000 22100001
  //   22310004 ae300000 22100001 22310004 ae300000 22100001 22310004 ae300000 22100001 22310004 ae300000
  //   22100001 22310004 ae300000 22100001 22310004 ae300000 22100001 22310004 ae300000 22100001 22310004
  //   ae300000 22100001 22310004 ae300000 22100001 22310004 ae300000 22100001 22310004 ae300000 22100001
  //   22310004 ae300000 22100001 22310004 ae300000 22100001 22310004 ae300000 22100001 22310004 ae300000
  //   22100001 22310004 22100001 8020 2011003c 8e130000 8e340000 274402a 11000002 ae330000 ae140000
  //   2231fffc 1611fff8 102020 20020022 c 22100004 2011003c 1611fff2 20020032 c 8000c00 2002000a c
  //   20100000 22100001 102020 20020022 c 22100002 102020 20020022 c 22100003 102020 20020022 c 22100004
  //   102020 20020022 c 22100005 102020 20020022 c 22100006 102020 20020022 c 22100007 102020 20020022 c
  //   22100008 102020 20020022 20020022 c 3e00008
  //   流水调试日志用
  //   OP
  //   func
  //   rs
  //   rt
  //   rd
  //   数据寄存器
endmodule

// 源寄存器使用情况
module \源寄存器使用情况  (
  input  OP0,
  input  OP1,
  input  OP2,
  input  OP3,
  input  OP4,
  input  OP5,
  input  F0,
  input  F1,
  input  F2,
  input  F3,
  input  F4,
  input  F5,
  output R1_Used,
  output R2_Used
);

  wire and_1_out, and_2_out, and_3_out, and_4_out, and_5_out, and_6_out, and_7_out, and_8_out, and_9_out,
       and_10_out, and_11_out, and_12_out, and_13_out, and_14_out, and_15_out, and_16_out, and_17_out,
       and_18_out, and_19_out, and_20_out, and_21_out, and_22_out, and_23_out, and_24_out, and_25_out,
       and_26_out, and_27_out, and_28_out, and_29_out, and_30_out, and_31_out, and_32_out, and_33_out,
       and_34_out, and_35_out, and_36_out, and_37_out, and_38_out, and_39_out, and_40_out, not_1_out,
       not_2_out, not_3_out, not_4_out, not_5_out, not_6_out, not_7_out, not_8_out, not_9_out, not_10_out,
       not_11_out, not_12_out, not_13_out, not_14_out, not_15_out, not_16_out, not_17_out, not_18_out,
       not_19_out, not_20_out, not_21_out, not_22_out, not_23_out, not_24_out, not_25_out, not_26_out,
       not_27_out, not_28_out, not_29_out, not_30_out, not_31_out, not_32_out, not_33_out, not_34_out,
       not_35_out, not_36_out, not_37_out, not_38_out, not_39_out, not_40_out, not_41_out, not_42_out,
       not_43_out, not_44_out, not_45_out, not_46_out, not_47_out, not_48_out, not_49_out, not_50_out,
       not_51_out, not_52_out, not_53_out, not_54_out, not_55_out, not_56_out, not_57_out, not_58_out,
       not_59_out, not_60_out, not_61_out, not_62_out, not_63_out, not_64_out, not_65_out, not_66_out,
       not_67_out, not_68_out, not_69_out, not_70_out, not_71_out, not_72_out, not_73_out, not_74_out,
       not_75_out, not_76_out, not_77_out, not_78_out, not_79_out, not_80_out, not_81_out, not_82_out,
       not_83_out, not_84_out, not_85_out, not_86_out, not_87_out, not_88_out, not_89_out, not_90_out,
       not_91_out, not_92_out, not_93_out, not_94_out, not_95_out, not_96_out, not_97_out, not_98_out,
       not_99_out, not_100_out, not_101_out, not_102_out, not_103_out, not_104_out, not_105_out, not_106_out,
       not_107_out, not_108_out, not_109_out, not_110_out, not_111_out, not_112_out, not_113_out,
       not_114_out, not_115_out, not_116_out, not_117_out, not_118_out, not_119_out, not_120_out,
       not_121_out, not_122_out, not_123_out, not_124_out, not_125_out, not_126_out, not_127_out,
       not_128_out, not_129_out, not_130_out, not_131_out, not_132_out, not_133_out, not_134_out,
       not_135_out, not_136_out, not_137_out, not_138_out, not_139_out, not_140_out, not_141_out,
       not_142_out, not_143_out, not_144_out, not_145_out, not_146_out, not_147_out, not_148_out,
       not_149_out, not_150_out, not_151_out, not_152_out, not_153_out, not_154_out, not_155_out,
       not_156_out, not_157_out, not_158_out, not_159_out, not_160_out, not_161_out, not_162_out,
       not_163_out, not_164_out, not_165_out, not_166_out, not_167_out, not_168_out, not_169_out,
       not_170_out, not_171_out, not_172_out, not_173_out, not_174_out, not_175_out, not_176_out,
       not_177_out, not_178_out, not_179_out, not_180_out, not_181_out, not_182_out, not_183_out,
       not_184_out, not_185_out, not_186_out, not_187_out, not_188_out, not_189_out, not_190_out,
       not_191_out, not_192_out, not_193_out, not_194_out, not_195_out, not_196_out, not_197_out,
       not_198_out, not_199_out, not_200_out, not_201_out, not_202_out, not_203_out, not_204_out,
       not_205_out, not_206_out, not_207_out, not_208_out, not_209_out, not_210_out, not_211_out,
       not_212_out, not_213_out, not_214_out, not_215_out, not_216_out, not_217_out, not_218_out,
       not_219_out, not_220_out, not_221_out, not_222_out, not_223_out, not_224_out, not_225_out,
       not_226_out, not_227_out, not_228_out, not_229_out, not_230_out, not_231_out, not_232_out,
       not_233_out, not_234_out, not_235_out, not_236_out, not_237_out, not_238_out, not_239_out,
       not_240_out, not_241_out, not_242_out, not_243_out, not_244_out, not_245_out, not_246_out,
       not_247_out, not_248_out, not_249_out, not_250_out, not_251_out, not_252_out, not_253_out,
       not_254_out, not_255_out, not_256_out, not_257_out, not_258_out, not_259_out, not_260_out,
       not_261_out, not_262_out, not_263_out, not_264_out, not_265_out, not_266_out, not_267_out,
       not_268_out, not_269_out, not_270_out, not_271_out, not_272_out, not_273_out, not_274_out,
       not_275_out, not_276_out, not_277_out, not_278_out, not_279_out, not_280_out, not_281_out,
       not_282_out, not_283_out, not_284_out, not_285_out, not_286_out, not_287_out, not_288_out,
       not_289_out, not_290_out, not_291_out, not_292_out, not_293_out, not_294_out, not_295_out,
       not_296_out, not_297_out;

  not not_1 (not_1_out, OP5);
  not not_2 (not_2_out, OP4);
  not not_3 (not_3_out, OP3);
  not not_4 (not_4_out, OP2);
  not not_5 (not_5_out, OP1);
  not not_6 (not_6_out, OP0);
  not not_7 (not_7_out, F4);
  not not_8 (not_8_out, F3);
  not not_9 (not_9_out, F2);
  not not_10 (not_10_out, F1);
  not not_11 (not_11_out, F0);
  not not_12 (not_12_out, OP5);
  not not_13 (not_13_out, OP4);
  not not_14 (not_14_out, OP3);
  not not_15 (not_15_out, OP2);
  not not_16 (not_16_out, OP1);
  not not_17 (not_17_out, OP0);
  not not_18 (not_18_out, F4);
  not not_19 (not_19_out, F3);
  not not_20 (not_20_out, F2);
  not not_21 (not_21_out, F1);
  not not_22 (not_22_out, OP5);
  not not_23 (not_23_out, OP4);
  not not_24 (not_24_out, OP3);
  not not_25 (not_25_out, OP2);
  not not_26 (not_26_out, OP1);
  not not_27 (not_27_out, OP0);
  not not_28 (not_28_out, F4);
  not not_29 (not_29_out, F3);
  not not_30 (not_30_out, F2);
  not not_31 (not_31_out, F0);
  not not_32 (not_32_out, OP5);
  not not_33 (not_33_out, OP4);
  not not_34 (not_34_out, OP3);
  not not_35 (not_35_out, OP2);
  not not_36 (not_36_out, OP1);
  not not_37 (not_37_out, OP0);
  not not_38 (not_38_out, F4);
  not not_39 (not_39_out, F3);
  not not_40 (not_40_out, F1);
  not not_41 (not_41_out, F0);
  not not_42 (not_42_out, OP5);
  not not_43 (not_43_out, OP4);
  not not_44 (not_44_out, OP3);
  not not_45 (not_45_out, OP2);
  not not_46 (not_46_out, OP1);
  not not_47 (not_47_out, OP0);
  not not_48 (not_48_out, F4);
  not not_49 (not_49_out, F3);
  not not_50 (not_50_out, F1);
  not not_51 (not_51_out, OP5);
  not not_52 (not_52_out, OP4);
  not not_53 (not_53_out, OP3);
  not not_54 (not_54_out, OP2);
  not not_55 (not_55_out, OP1);
  not not_56 (not_56_out, OP0);
  not not_57 (not_57_out, F4);
  not not_58 (not_58_out, F3);
  not not_59 (not_59_out, OP5);
  not not_60 (not_60_out, OP4);
  not not_61 (not_61_out, OP3);
  not not_62 (not_62_out, OP2);
  not not_63 (not_63_out, OP1);
  not not_64 (not_64_out, OP0);
  not not_65 (not_65_out, F4);
  not not_66 (not_66_out, F2);
  not not_67 (not_67_out, F0);
  not not_68 (not_68_out, OP5);
  not not_69 (not_69_out, OP4);
  not not_70 (not_70_out, OP3);
  not not_71 (not_71_out, OP2);
  not not_72 (not_72_out, OP1);
  not not_73 (not_73_out, OP0);
  not not_74 (not_74_out, F4);
  not not_75 (not_75_out, F2);
  not not_76 (not_76_out, OP5);
  not not_77 (not_77_out, OP4);
  not not_78 (not_78_out, OP3);
  not not_79 (not_79_out, OP2);
  not not_80 (not_80_out, OP1);
  not not_81 (not_81_out, OP0);
  not not_82 (not_82_out, F5);
  not not_83 (not_83_out, F4);
  not not_84 (not_84_out, F2);
  not not_85 (not_85_out, F1);
  not not_86 (not_86_out, F0);
  not not_87 (not_87_out, OP5);
  not not_88 (not_88_out, OP4);
  not not_89 (not_89_out, OP3);
  not not_90 (not_90_out, OP2);
  not not_91 (not_91_out, OP1);
  not not_92 (not_92_out, OP0);
  not not_93 (not_93_out, F5);
  not not_94 (not_94_out, F4);
  not not_95 (not_95_out, F1);
  not not_96 (not_96_out, F0);
  not not_97 (not_97_out, OP5);
  not not_98 (not_98_out, OP4);
  not not_99 (not_99_out, OP3);
  not not_100 (not_100_out, OP1);
  not not_101 (not_101_out, OP0);
  not not_102 (not_102_out, OP5);
  not not_103 (not_103_out, OP4);
  not not_104 (not_104_out, OP3);
  not not_105 (not_105_out, OP1);
  not not_106 (not_106_out, OP5);
  not not_107 (not_107_out, OP4);
  not not_108 (not_108_out, OP2);
  not not_109 (not_109_out, OP1);
  not not_110 (not_110_out, OP0);
  not not_111 (not_111_out, OP5);
  not not_112 (not_112_out, OP4);
  not not_113 (not_113_out, OP1);
  not not_114 (not_114_out, OP0);
  not not_115 (not_115_out, OP5);
  not not_116 (not_116_out, OP4);
  not not_117 (not_117_out, OP1);
  not not_118 (not_118_out, OP0);
  not not_119 (not_119_out, OP5);
  not not_120 (not_120_out, OP4);
  not not_121 (not_121_out, OP2);
  not not_122 (not_122_out, OP1);
  not not_123 (not_123_out, OP5);
  not not_124 (not_124_out, OP4);
  not not_125 (not_125_out, OP2);
  not not_126 (not_126_out, OP0);
  not not_127 (not_127_out, OP5);
  not not_128 (not_128_out, OP4);
  not not_129 (not_129_out, OP1);
  not not_130 (not_130_out, OP4);
  not not_131 (not_131_out, OP3);
  not not_132 (not_132_out, OP2);
  not not_133 (not_133_out, OP4);
  not not_134 (not_134_out, OP2);
  not not_135 (not_135_out, OP5);
  not not_136 (not_136_out, OP4);
  not not_137 (not_137_out, OP3);
  not not_138 (not_138_out, OP2);
  not not_139 (not_139_out, OP1);
  not not_140 (not_140_out, OP0);
  not not_141 (not_141_out, F5);
  not not_142 (not_142_out, F4);
  not not_143 (not_143_out, F3);
  not not_144 (not_144_out, F1);
  not not_145 (not_145_out, F0);
  not not_146 (not_146_out, OP5);
  not not_147 (not_147_out, OP4);
  not not_148 (not_148_out, OP0);
  not not_149 (not_149_out, OP4);
  not not_150 (not_150_out, OP3);
  not not_151 (not_151_out, OP1);
  not not_152 (not_152_out, OP0);
  not not_153 (not_153_out, OP5);
  not not_154 (not_154_out, OP4);
  not not_155 (not_155_out, OP3);
  not not_156 (not_156_out, OP2);
  not not_157 (not_157_out, OP1);
  not not_158 (not_158_out, OP5);
  not not_159 (not_159_out, OP4);
  not not_160 (not_160_out, OP3);
  not not_161 (not_161_out, OP2);
  not not_162 (not_162_out, OP1);
  not not_163 (not_163_out, OP0);
  not not_164 (not_164_out, F5);
  not not_165 (not_165_out, F4);
  not not_166 (not_166_out, F3);
  not not_167 (not_167_out, F2);
  not not_168 (not_168_out, F1);
  not not_169 (not_169_out, F0);
  not not_170 (not_170_out, OP5);
  not not_171 (not_171_out, OP4);
  not not_172 (not_172_out, OP3);
  not not_173 (not_173_out, OP2);
  not not_174 (not_174_out, OP1);
  not not_175 (not_175_out, OP0);
  not not_176 (not_176_out, F5);
  not not_177 (not_177_out, F4);
  not not_178 (not_178_out, F3);
  not not_179 (not_179_out, F2);
  not not_180 (not_180_out, OP5);
  not not_181 (not_181_out, OP4);
  not not_182 (not_182_out, OP3);
  not not_183 (not_183_out, OP2);
  not not_184 (not_184_out, OP1);
  not not_185 (not_185_out, OP0);
  not not_186 (not_186_out, F5);
  not not_187 (not_187_out, F4);
  not not_188 (not_188_out, F3);
  not not_189 (not_189_out, F2);
  not not_190 (not_190_out, F0);
  not not_191 (not_191_out, OP5);
  not not_192 (not_192_out, OP4);
  not not_193 (not_193_out, OP3);
  not not_194 (not_194_out, OP2);
  not not_195 (not_195_out, OP1);
  not not_196 (not_196_out, OP0);
  not not_197 (not_197_out, F4);
  not not_198 (not_198_out, F3);
  not not_199 (not_199_out, F2);
  not not_200 (not_200_out, F1);
  not not_201 (not_201_out, F0);
  not not_202 (not_202_out, OP5);
  not not_203 (not_203_out, OP4);
  not not_204 (not_204_out, OP3);
  not not_205 (not_205_out, OP2);
  not not_206 (not_206_out, OP1);
  not not_207 (not_207_out, OP0);
  not not_208 (not_208_out, F4);
  not not_209 (not_209_out, F3);
  not not_210 (not_210_out, F2);
  not not_211 (not_211_out, F1);
  not not_212 (not_212_out, OP5);
  not not_213 (not_213_out, OP4);
  not not_214 (not_214_out, OP3);
  not not_215 (not_215_out, OP2);
  not not_216 (not_216_out, OP1);
  not not_217 (not_217_out, OP0);
  not not_218 (not_218_out, F4);
  not not_219 (not_219_out, F3);
  not not_220 (not_220_out, F2);
  not not_221 (not_221_out, F0);
  not not_222 (not_222_out, OP5);
  not not_223 (not_223_out, OP4);
  not not_224 (not_224_out, OP3);
  not not_225 (not_225_out, OP2);
  not not_226 (not_226_out, OP1);
  not not_227 (not_227_out, OP0);
  not not_228 (not_228_out, F4);
  not not_229 (not_229_out, F3);
  not not_230 (not_230_out, F1);
  not not_231 (not_231_out, F0);
  not not_232 (not_232_out, OP5);
  not not_233 (not_233_out, OP4);
  not not_234 (not_234_out, OP3);
  not not_235 (not_235_out, OP2);
  not not_236 (not_236_out, OP1);
  not not_237 (not_237_out, OP0);
  not not_238 (not_238_out, F4);
  not not_239 (not_239_out, F3);
  not not_240 (not_240_out, F1);
  not not_241 (not_241_out, OP5);
  not not_242 (not_242_out, OP4);
  not not_243 (not_243_out, OP3);
  not not_244 (not_244_out, OP2);
  not not_245 (not_245_out, OP1);
  not not_246 (not_246_out, OP0);
  not not_247 (not_247_out, F4);
  not not_248 (not_248_out, F3);
  not not_249 (not_249_out, OP5);
  not not_250 (not_250_out, OP4);
  not not_251 (not_251_out, OP3);
  not not_252 (not_252_out, OP2);
  not not_253 (not_253_out, OP1);
  not not_254 (not_254_out, OP0);
  not not_255 (not_255_out, F4);
  not not_256 (not_256_out, F2);
  not not_257 (not_257_out, F0);
  not not_258 (not_258_out, OP5);
  not not_259 (not_259_out, OP4);
  not not_260 (not_260_out, OP3);
  not not_261 (not_261_out, OP2);
  not not_262 (not_262_out, OP1);
  not not_263 (not_263_out, OP0);
  not not_264 (not_264_out, F4);
  not not_265 (not_265_out, F2);
  not not_266 (not_266_out, OP5);
  not not_267 (not_267_out, OP4);
  not not_268 (not_268_out, OP3);
  not not_269 (not_269_out, OP2);
  not not_270 (not_270_out, OP1);
  not not_271 (not_271_out, OP0);
  not not_272 (not_272_out, F5);
  not not_273 (not_273_out, F4);
  not not_274 (not_274_out, F1);
  not not_275 (not_275_out, F0);
  not not_276 (not_276_out, OP5);
  not not_277 (not_277_out, OP4);
  not not_278 (not_278_out, OP3);
  not not_279 (not_279_out, OP1);
  not not_280 (not_280_out, OP0);
  not not_281 (not_281_out, OP5);
  not not_282 (not_282_out, OP4);
  not not_283 (not_283_out, OP3);
  not not_284 (not_284_out, OP1);
  not not_285 (not_285_out, OP4);
  not not_286 (not_286_out, OP2);
  not not_287 (not_287_out, OP5);
  not not_288 (not_288_out, OP4);
  not not_289 (not_289_out, OP3);
  not not_290 (not_290_out, OP2);
  not not_291 (not_291_out, OP1);
  not not_292 (not_292_out, OP0);
  not not_293 (not_293_out, F5);
  not not_294 (not_294_out, F4);
  not not_295 (not_295_out, F3);
  not not_296 (not_296_out, F1);
  not not_297 (not_297_out, F0);
  and and_1 (and_1_out, not_1_out, not_2_out, not_3_out, not_4_out, not_5_out, not_6_out, F5, not_7_out, not_8_out, not_9_out, not_10_out, not_11_out);
  and and_2 (and_2_out, not_12_out, not_13_out, not_14_out, not_15_out, not_16_out, not_17_out, F5, not_18_out, not_19_out, not_20_out, not_21_out, F0);
  and and_3 (and_3_out, not_22_out, not_23_out, not_24_out, not_25_out, not_26_out, not_27_out, F5, not_28_out, not_29_out, not_30_out, F1, not_31_out);
  and and_4 (and_4_out, not_32_out, not_33_out, not_34_out, not_35_out, not_36_out, not_37_out, F5, not_38_out, not_39_out, F2, not_40_out, not_41_out);
  and and_5 (and_5_out, not_42_out, not_43_out, not_44_out, not_45_out, not_46_out, not_47_out, F5, not_48_out, not_49_out, F2, not_50_out, F0);
  and and_6 (and_6_out, not_51_out, not_52_out, not_53_out, not_54_out, not_55_out, not_56_out, F5, not_57_out, not_58_out, F2, F1, F0);
  and and_7 (and_7_out, not_59_out, not_60_out, not_61_out, not_62_out, not_63_out, not_64_out, F5, not_65_out, F3, not_66_out, F1, not_67_out);
  and and_8 (and_8_out, not_68_out, not_69_out, not_70_out, not_71_out, not_72_out, not_73_out, F5, not_74_out, F3, not_75_out, F1, F0);
  and and_9 (and_9_out, not_76_out, not_77_out, not_78_out, not_79_out, not_80_out, not_81_out, not_82_out, not_83_out, F3, not_84_out, not_85_out, not_86_out);
  and and_10 (and_10_out, not_87_out, not_88_out, not_89_out, not_90_out, not_91_out, not_92_out, not_93_out, not_94_out, F3, F2, not_95_out, not_96_out);
  and and_11 (and_11_out, not_97_out, not_98_out, not_99_out, OP2, not_100_out, not_101_out);
  and and_12 (and_12_out, not_102_out, not_103_out, not_104_out, OP2, not_105_out, OP0);
  and and_13 (and_13_out, not_106_out, not_107_out, OP3, not_108_out, not_109_out, not_110_out);
  and and_14 (and_14_out, not_111_out, not_112_out, OP3, OP2, not_113_out, not_114_out);
  and and_15 (and_15_out, not_115_out, not_116_out, OP3, OP2, not_117_out, not_118_out);
  and and_16 (and_16_out, not_119_out, not_120_out, OP3, not_121_out, not_122_out, OP0);
  and and_17 (and_17_out, not_123_out, not_124_out, OP3, not_125_out, OP1, not_126_out);
  and and_18 (and_18_out, not_127_out, not_128_out, OP3, OP2, not_129_out, OP0);
  and and_19 (and_19_out, OP5, not_130_out, not_131_out, not_132_out, OP1, OP0);
  and and_20 (and_20_out, OP5, not_133_out, OP3, not_134_out, OP1, OP0);
  and and_21 (and_21_out, not_135_out, not_136_out, not_137_out, not_138_out, not_139_out, not_140_out, not_141_out, not_142_out, not_143_out, F2, not_144_out, not_145_out);
  and and_22 (and_22_out, not_146_out, not_147_out, OP3, OP2, OP1, not_148_out);
  and and_23 (and_23_out, OP5, not_149_out, not_150_out, OP2, not_151_out, not_152_out);
  and and_24 (and_24_out, not_153_out, not_154_out, not_155_out, not_156_out, not_157_out, OP0);
  and and_25 (and_25_out, not_158_out, not_159_out, not_160_out, not_161_out, not_162_out, not_163_out, not_164_out, not_165_out, not_166_out, not_167_out, not_168_out, not_169_out);
  and and_26 (and_26_out, not_170_out, not_171_out, not_172_out, not_173_out, not_174_out, not_175_out, not_176_out, not_177_out, not_178_out, not_179_out, F1, F0);
  and and_27 (and_27_out, not_180_out, not_181_out, not_182_out, not_183_out, not_184_out, not_185_out, not_186_out, not_187_out, not_188_out, not_189_out, F1, not_190_out);
  and and_28 (and_28_out, not_191_out, not_192_out, not_193_out, not_194_out, not_195_out, not_196_out, F5, not_197_out, not_198_out, not_199_out, not_200_out, not_201_out);
  and and_29 (and_29_out, not_202_out, not_203_out, not_204_out, not_205_out, not_206_out, not_207_out, F5, not_208_out, not_209_out, not_210_out, not_211_out, F0);
  and and_30 (and_30_out, not_212_out, not_213_out, not_214_out, not_215_out, not_216_out, not_217_out, F5, not_218_out, not_219_out, not_220_out, F1, not_221_out);
  and and_31 (and_31_out, not_222_out, not_223_out, not_224_out, not_225_out, not_226_out, not_227_out, F5, not_228_out, not_229_out, F2, not_230_out, not_231_out);
  and and_32 (and_32_out, not_232_out, not_233_out, not_234_out, not_235_out, not_236_out, not_237_out, F5, not_238_out, not_239_out, F2, not_240_out, F0);
  and and_33 (and_33_out, not_241_out, not_242_out, not_243_out, not_244_out, not_245_out, not_246_out, F5, not_247_out, not_248_out, F2, F1, F0);
  and and_34 (and_34_out, not_249_out, not_250_out, not_251_out, not_252_out, not_253_out, not_254_out, F5, not_255_out, F3, not_256_out, F1, not_257_out);
  and and_35 (and_35_out, not_258_out, not_259_out, not_260_out, not_261_out, not_262_out, not_263_out, F5, not_264_out, F3, not_265_out, F1, F0);
  and and_36 (and_36_out, not_266_out, not_267_out, not_268_out, not_269_out, not_270_out, not_271_out, not_272_out, not_273_out, F3, F2, not_274_out, not_275_out);
  and and_37 (and_37_out, not_276_out, not_277_out, not_278_out, OP2, not_279_out, not_280_out);
  and and_38 (and_38_out, not_281_out, not_282_out, not_283_out, OP2, not_284_out, OP0);
  and and_39 (and_39_out, OP5, not_285_out, OP3, not_286_out, OP1, OP0);
  and and_40 (and_40_out, not_287_out, not_288_out, not_289_out, not_290_out, not_291_out, not_292_out, not_293_out, not_294_out, not_295_out, F2, not_296_out, not_297_out);
  or or_1 (R1_Used, and_1_out, and_2_out, and_3_out, and_4_out, and_5_out, and_6_out, and_7_out, and_8_out, and_9_out, and_10_out, and_11_out, and_12_out, and_13_out, and_14_out, and_15_out, and_16_out, and_17_out, and_18_out, and_19_out, and_20_out, and_21_out, and_22_out, and_23_out, and_24_out);
  or or_2 (R2_Used, and_25_out, and_26_out, and_27_out, and_28_out, and_29_out, and_30_out, and_31_out, and_32_out, and_33_out, and_34_out, and_35_out, and_36_out, and_37_out, and_38_out, and_39_out, and_40_out);
endmodule

// 数据相关检测
module \数据相关检测  (
  input  [5:0] OP,
  input  [4:0] EX_WriteReg_num,
  input  EX_RegWrite,
  input  [4:0] MEM_WriteReg_num,
  input  MEM_RegWrite,
  input  [5:0] Func,
  input  [4:0] ID_R1_num,
  input  [4:0] ID_R2_num,
  output \数据相关 
);

  wire and_1_out, and_2_out, and_3_out, and_4_out, and_5_out, and_6_out, and_7_out, and_8_out,
       comparator_1_eq, comparator_2_eq, comparator_3_eq, comparator_4_eq, comparator_5_eq, comparator_6_eq,
       not_1_out, not_2_out, or_1_out, or_2_out, \源寄存器使用情况_1_r1_used , \源寄存器使用情况_1_r2_used ;

  \源寄存器使用情况  \u_源寄存器使用情况_1  (
    .OP0(OP[0]), .OP1(OP[1]), .OP2(OP[2]), .OP3(OP[3]), .OP4(OP[4]), .OP5(OP[5]), .F0(Func[0]), .F1(Func[1]),
    .F2(Func[2]), .F3(Func[3]), .F4(Func[4]), .F5(Func[5]), .R1_Used(\源寄存器使用情况_1_r1_used ),
    .R2_Used(\源寄存器使用情况_1_r2_used ));
  Comparator #(.width(5)) comparator_1 (.a(ID_R1_num), .b({5{1'b0}}), .eq(comparator_1_eq));  // open: gt, lt
  Comparator #(.width(5)) comparator_2 (.a(ID_R1_num), .b(MEM_WriteReg_num), .eq(comparator_2_eq));  // open: gt, lt
  Comparator #(.width(5)) comparator_3 (.a(ID_R1_num), .b(EX_WriteReg_num), .eq(comparator_3_eq));  // open: gt, lt
  Comparator #(.width(5)) comparator_4 (.a(ID_R2_num), .b(MEM_WriteReg_num), .eq(comparator_4_eq));  // open: gt, lt
  Comparator #(.width(5)) comparator_5 (.a(ID_R2_num), .b(EX_WriteReg_num), .eq(comparator_5_eq));  // open: gt, lt
  and and_1 (and_1_out, comparator_5_eq, EX_RegWrite);
  not not_1 (not_1_out, comparator_6_eq);
  Comparator #(.width(5)) comparator_6 (.a(ID_R2_num), .b({5{1'b0}}), .eq(comparator_6_eq));  // open: gt, lt
  not not_2 (not_2_out, comparator_1_eq);
  and and_2 (and_2_out, MEM_RegWrite, comparator_2_eq);
  and and_3 (and_3_out, comparator_3_eq, EX_RegWrite);
  and and_4 (and_4_out, comparator_4_eq, MEM_RegWrite);
  or or_1 (or_1_out, and_2_out, and_3_out);
  or or_2 (or_2_out, and_4_out, and_1_out);
  and and_5 (and_5_out, or_1_out, \源寄存器使用情况_1_r1_used );
  and and_6 (and_6_out, \源寄存器使用情况_1_r2_used , or_2_out);
  and and_7 (and_7_out, not_2_out, and_5_out);
  and and_8 (and_8_out, and_6_out, not_1_out);
  or or_3 (\数据相关 , and_7_out, and_8_out);

  // Other names for the same wires on the sheet: OP_CODE[5:0] = OP
endmodule

module IF_ID (
  input  predict_branch_in,
  input  Miss_in,
  input  [31:0] IRin,
  input  [31:0] PCin,
  input  clear_tong,
  input  enable,
  input  clk,
  input  clear_yi,
  output predict_branch_out,
  output Miss_out,
  output [31:0] IRout,
  output [31:0] PCout,
  output enable_out
);

  wire multiplexer_1_out, multiplexer_2_out;
  wire [31:0] multiplexer_3_out, multiplexer_4_out;

  Multiplexer #(.enable("false")) multiplexer_1 (
    .in0(predict_branch_in), .in1(1'b0), .out(multiplexer_1_out), .sel(clear_tong));
  Multiplexer #(.enable("false")) multiplexer_2 (.in0(Miss_in), .in1(1'b0), .out(multiplexer_2_out), .sel(clear_tong));
  Multiplexer #(.width(32), .enable("false")) multiplexer_3 (
    .in0(IRin), .in1({32{1'b0}}), .out(multiplexer_3_out), .sel(clear_tong));
  Multiplexer #(.width(32), .enable("false")) multiplexer_4 (
    .in0(PCin), .in1({32{1'b0}}), .out(multiplexer_4_out), .sel(clear_tong));
  Register #(.width(1)) predict_branch (
    .D(multiplexer_1_out), .en(enable), .Q(predict_branch_out), .clk(clk), .clr(clear_yi));
  Register #(.width(1)) valid (.D(multiplexer_2_out), .en(enable), .Q(Miss_out), .clk(clk), .clr(clear_yi));
  Register #(.width(32)) IR (.D(multiplexer_3_out), .en(enable), .Q(IRout), .clk(clk), .clr(clear_yi));
  Register #(.width(32)) PC (.D(multiplexer_4_out), .en(enable), .Q(PCout), .clk(clk), .clr(clear_yi));
  Register #(.width(1)) u_enable (.D(enable), .Q(enable_out), .clk(clk), .clr(clear_yi));  // open: en
endmodule
// ID/EX
module ID_EX (
  input  predict_branch_in,
  input  Miss_in,
  input  [1:0] forwardA_in,
  input  [1:0] forwardB_in,
  input  byteorword_in,
  input  bltz_in,
  input  shamtsrc_in,
  input  syscall_in,
  input  [25:0] J_JAL_imm_in,
  input  JMP_in,
  input  JR_in,
  input  [4:0] Rt_in,
  input  [4:0] Rd_in,
  input  RegDst_in,
  input  JAL_in,
  input  RegWrite_in,
  input  MemToReg_in,
  input  MemWrite_in,
  input  [3:0] ALU_OP_in,
  input  ALU_src_in,
  input  Bne_in,
  input  Beq_in,
  input  [31:0] IRin,
  input  [31:0] PCin,
  input  [31:0] R1in,
  input  [31:0] R2in,
  input  [31:0] IMMin,
  input  [4:0] shamt_in,
  input  clear_tong,
  input  enable,
  input  clk,
  input  clear_yibu,
  output predict_branch_out,
  output Miss_out,
  output [1:0] forwardA_out,
  output [1:0] forwardB_out,
  output byteorword_out,
  output bltz_out,
  output shamtsrc_out,
  output syscall_out,
  output [25:0] J_JAL_imm_out,
  output JMP_out,
  output JR_out,
  output [4:0] Rt_out,
  output [4:0] Rd_out,
  output RegDst_out,
  output JAL_out,
  output RegWrite_out,
  output MemToReg_out,
  output MemWrite_out,
  output [3:0] ALU_OP_out,
  output ALU_src_out,
  output Bne_out,
  output Beq_out,
  output [31:0] out_55,
  output [31:0] PCout,
  output [31:0] R1out,
  output [31:0] R2out,
  output [31:0] IMMout,
  output [4:0] shamt_out,
  output enable_out
);

  wire multiplexer_1_out, multiplexer_2_out, multiplexer_5_out, multiplexer_6_out, multiplexer_7_out,
       multiplexer_8_out, multiplexer_10_out, multiplexer_11_out, multiplexer_14_out, multiplexer_15_out,
       multiplexer_16_out, multiplexer_17_out, multiplexer_18_out, multiplexer_20_out, multiplexer_21_out,
       multiplexer_22_out;
  wire [1:0] multiplexer_3_out, multiplexer_4_out;
  wire [3:0] multiplexer_19_out;
  wire [4:0] multiplexer_12_out, multiplexer_13_out, multiplexer_28_out;
  wire [25:0] multiplexer_9_out;
  wire [31:0] multiplexer_23_out, multiplexer_24_out, multiplexer_25_out, multiplexer_26_out,
       multiplexer_27_out;

  Multiplexer #(.enable("false")) multiplexer_1 (
    .in0(predict_branch_in), .in1(1'b0), .out(multiplexer_1_out), .sel(clear_tong));
  Multiplexer #(.enable("false")) multiplexer_2 (.in0(Miss_in), .in1(1'b0), .out(multiplexer_2_out), .sel(clear_tong));
  Multiplexer #(.width(2), .enable("false")) multiplexer_3 (
    .in0(forwardA_in), .in1(2'b00), .out(multiplexer_3_out), .sel(clear_tong));
  Multiplexer #(.width(2), .enable("false")) multiplexer_4 (
    .in0(forwardB_in), .in1(2'b00), .out(multiplexer_4_out), .sel(clear_tong));
  Multiplexer #(.enable("false")) multiplexer_5 (
    .in0(byteorword_in), .in1(1'b0), .out(multiplexer_5_out), .sel(clear_tong));
  Multiplexer #(.enable("false")) multiplexer_6 (.in0(bltz_in), .in1(1'b0), .out(multiplexer_6_out), .sel(clear_tong));
  Multiplexer #(.enable("false")) multiplexer_7 (
    .in0(shamtsrc_in), .in1(1'b0), .out(multiplexer_7_out), .sel(clear_tong));
  Multiplexer #(.enable("false")) multiplexer_8 (
    .in0(syscall_in), .in1(1'b0), .out(multiplexer_8_out), .sel(clear_tong));
  Multiplexer #(.width(26), .enable("false")) multiplexer_9 (
    .in0(J_JAL_imm_in), .in1({26{1'b0}}), .out(multiplexer_9_out), .sel(clear_tong));
  Multiplexer #(.enable("false")) multiplexer_10 (.in0(JMP_in), .in1(1'b0), .out(multiplexer_10_out), .sel(clear_tong));
  Multiplexer #(.enable("false")) multiplexer_11 (.in0(JR_in), .in1(1'b0), .out(multiplexer_11_out), .sel(clear_tong));
  Multiplexer #(.width(5), .enable("false")) multiplexer_12 (
    .in0(Rt_in), .in1({5{1'b0}}), .out(multiplexer_12_out), .sel(clear_tong));
  Multiplexer #(.width(5), .enable("false")) multiplexer_13 (
    .in0(Rd_in), .in1({5{1'b0}}), .out(multiplexer_13_out), .sel(clear_tong));
  Multiplexer #(.enable("false")) multiplexer_14 (
    .in0(RegDst_in), .in1(1'b0), .out(multiplexer_14_out), .sel(clear_tong));
  Multiplexer #(.enable("false")) multiplexer_15 (.in0(JAL_in), .in1(1'b0), .out(multiplexer_15_out), .sel(clear_tong));
  Multiplexer #(.enable("false")) multiplexer_16 (
    .in0(RegWrite_in), .in1(1'b0), .out(multiplexer_16_out), .sel(clear_tong));
  Multiplexer #(.enable("false")) multiplexer_17 (
    .in0(MemToReg_in), .in1(1'b0), .out(multiplexer_17_out), .sel(clear_tong));
  Multiplexer #(.enable("false")) multiplexer_18 (
    .in0(MemWrite_in), .in1(1'b0), .out(multiplexer_18_out), .sel(clear_tong));
  Multiplexer #(.width(4), .enable("false")) multiplexer_19 (
    .in0(ALU_OP_in), .in1(4'b0000), .out(multiplexer_19_out), .sel(clear_tong));
  Multiplexer #(.enable("false")) multiplexer_20 (
    .in0(ALU_src_in), .in1(1'b0), .out(multiplexer_20_out), .sel(clear_tong));
  Multiplexer #(.enable("false")) multiplexer_21 (.in0(Bne_in), .in1(1'b0), .out(multiplexer_21_out), .sel(clear_tong));
  Multiplexer #(.enable("false")) multiplexer_22 (.in0(Beq_in), .in1(1'b0), .out(multiplexer_22_out), .sel(clear_tong));
  Multiplexer #(.width(32), .enable("false")) multiplexer_23 (
    .in0(IRin), .in1({32{1'b0}}), .out(multiplexer_23_out), .sel(clear_tong));
  Multiplexer #(.width(32), .enable("false")) multiplexer_24 (
    .in0(PCin), .in1({32{1'b0}}), .out(multiplexer_24_out), .sel(clear_tong));
  Multiplexer #(.width(32), .enable("false")) multiplexer_25 (
    .in0(R1in), .in1({32{1'b0}}), .out(multiplexer_25_out), .sel(clear_tong));
  Multiplexer #(.width(32), .enable("false")) multiplexer_26 (
    .in0(R2in), .in1({32{1'b0}}), .out(multiplexer_26_out), .sel(clear_tong));
  Multiplexer #(.width(32), .enable("false")) multiplexer_27 (
    .in0(IMMin), .in1({32{1'b0}}), .out(multiplexer_27_out), .sel(clear_tong));
  Multiplexer #(.width(5), .enable("false")) multiplexer_28 (
    .in0(shamt_in), .in1({5{1'b0}}), .out(multiplexer_28_out), .sel(clear_tong));
  Register #(.width(1)) predict_branch (
    .D(multiplexer_1_out), .en(enable), .Q(predict_branch_out), .clk(clk), .clr(clear_yibu));
  Register #(.width(1)) miss (.D(multiplexer_2_out), .en(enable), .Q(Miss_out), .clk(clk), .clr(clear_yibu));
  Register #(.width(2)) register_1 (.D(multiplexer_3_out), .en(enable), .Q(forwardA_out), .clk(clk), .clr(clear_yibu));
  Register #(.width(2)) register_2 (.D(multiplexer_4_out), .en(enable), .Q(forwardB_out), .clk(clk), .clr(clear_yibu));
  Register #(.width(1)) byteorword (
    .D(multiplexer_5_out), .en(enable), .Q(byteorword_out), .clk(clk), .clr(clear_yibu));
  Register #(.width(1)) bltz (.D(multiplexer_6_out), .en(enable), .Q(bltz_out), .clk(clk), .clr(clear_yibu));
  Register #(.width(1)) shamtsrc (.D(multiplexer_7_out), .en(enable), .Q(shamtsrc_out), .clk(clk), .clr(clear_yibu));
  Register #(.width(1)) syscall (.D(multiplexer_8_out), .en(enable), .Q(syscall_out), .clk(clk), .clr(clear_yibu));
  Register #(.width(26)) J_JAL_imm (.D(multiplexer_9_out), .en(enable), .Q(J_JAL_imm_out), .clk(clk), .clr(clear_yibu));
  Register #(.width(1)) JMP (.D(multiplexer_10_out), .en(enable), .Q(JMP_out), .clk(clk), .clr(clear_yibu));
  Register #(.width(1)) JR (.D(multiplexer_11_out), .en(enable), .Q(JR_out), .clk(clk), .clr(clear_yibu));
  Register #(.width(5)) Rt (.D(multiplexer_12_out), .en(enable), .Q(Rt_out), .clk(clk), .clr(clear_yibu));
  Register #(.width(5)) Rd (.D(multiplexer_13_out), .en(enable), .Q(Rd_out), .clk(clk), .clr(clear_yibu));
  Register #(.width(1)) RegDst (.D(multiplexer_14_out), .en(enable), .Q(RegDst_out), .clk(clk), .clr(clear_yibu));
  Register #(.width(1)) JAL (.D(multiplexer_15_out), .en(enable), .Q(JAL_out), .clk(clk), .clr(clear_yibu));
  Register #(.width(1)) RegWrite (.D(multiplexer_16_out), .en(enable), .Q(RegWrite_out), .clk(clk), .clr(clear_yibu));
  Register #(.width(1)) MemToReg (.D(multiplexer_17_out), .en(enable), .Q(MemToReg_out), .clk(clk), .clr(clear_yibu));
  Register #(.width(1)) MemWrite (.D(multiplexer_18_out), .en(enable), .Q(MemWrite_out), .clk(clk), .clr(clear_yibu));
  Register #(.width(4)) ALU_OP (.D(multiplexer_19_out), .en(enable), .Q(ALU_OP_out), .clk(clk), .clr(clear_yibu));
  Register #(.width(1)) ALU_src (.D(multiplexer_20_out), .en(enable), .Q(ALU_src_out), .clk(clk), .clr(clear_yibu));
  Register #(.width(1)) Bne (.D(multiplexer_21_out), .en(enable), .Q(Bne_out), .clk(clk), .clr(clear_yibu));
  Register #(.width(1)) Beq (.D(multiplexer_22_out), .en(enable), .Q(Beq_out), .clk(clk), .clr(clear_yibu));
  Register #(.width(32)) IR (.D(multiplexer_23_out), .en(enable), .Q(out_55), .clk(clk), .clr(clear_yibu));
  Register #(.width(32)) PC (.D(multiplexer_24_out), .en(enable), .Q(PCout), .clk(clk), .clr(clear_yibu));
  Register #(.width(32)) R1 (.D(multiplexer_25_out), .en(enable), .Q(R1out), .clk(clk), .clr(clear_yibu));
  Register #(.width(32)) R2 (.D(multiplexer_26_out), .en(enable), .Q(R2out), .clk(clk), .clr(clear_yibu));
  Register #(.width(32)) imm (.D(multiplexer_27_out), .en(enable), .Q(IMMout), .clk(clk), .clr(clear_yibu));
  Register #(.width(5)) register_3 (.D(multiplexer_28_out), .en(enable), .Q(shamt_out), .clk(clk), .clr(clear_yibu));
  Register #(.width(1)) register_4 (.D(enable), .Q(enable_out), .clk(clk), .clr(clear_yibu));  // open: en

  // Notes on the sheet:
  //   WB
  //   EX
  //   WB
  //   MEM
  //   EX
endmodule

// EX/MEM
module EX_MEM (
  input  byteorword_in,
  input  syscal_in,
  input  [4:0] Rd_in,
  input  [4:0] Rt_in,
  input  RegDst_in,
  input  JAL_in,
  input  RegWrite_in,
  input  MemToReg_in,
  input  MemWrite_in,
  input  [31:0] IRin,
  input  [31:0] PCin,
  input  [31:0] Rin,
  input  [31:0] ALUresult_in,
  input  enable,
  input  clk,
  input  clear,
  output byteorword_out,
  output syscall_out,
  output [4:0] Rd_out,
  output [4:0] Rt_out,
  output RegDst_out,
  output JAL_out,
  output RegWrite_out,
  output MemToReg_out,
  output MemWrite_out,
  output [31:0] IRout,
  output [31:0] PCout,
  output [31:0] Rout,
  output [31:0] ALUresult_out,
  output enable_out
);

  Register #(.width(1)) byteorword (.D(byteorword_in), .en(enable), .Q(byteorword_out), .clk(clk), .clr(clear));
  Register #(.width(1)) syacall (.D(syscal_in), .en(enable), .Q(syscall_out), .clk(clk), .clr(clear));
  Register #(.width(5)) Rd (.D(Rd_in), .en(enable), .Q(Rd_out), .clk(clk), .clr(clear));
  Register #(.width(5)) Rt (.D(Rt_in), .en(enable), .Q(Rt_out), .clk(clk), .clr(clear));
  Register #(.width(1)) RegDst (.D(RegDst_in), .en(enable), .Q(RegDst_out), .clk(clk), .clr(clear));
  Register #(.width(1)) JAL (.D(JAL_in), .en(enable), .Q(JAL_out), .clk(clk), .clr(clear));
  Register #(.width(1)) RegWrite (.D(RegWrite_in), .en(enable), .Q(RegWrite_out), .clk(clk), .clr(clear));
  Register #(.width(1)) MemToReg (.D(MemToReg_in), .en(enable), .Q(MemToReg_out), .clk(clk), .clr(clear));
  Register #(.width(1)) MemWrite (.D(MemWrite_in), .en(enable), .Q(MemWrite_out), .clk(clk), .clr(clear));
  Register #(.width(1)) register_1 (.D(enable), .Q(enable_out), .clk(clk), .clr(clear));  // open: en
  Register #(.width(32)) IR (.D(IRin), .en(enable), .Q(IRout), .clk(clk), .clr(clear));
  Register #(.width(32)) PC (.D(PCin), .en(enable), .Q(PCout), .clk(clk), .clr(clear));
  Register #(.width(32)) R2 (.D(Rin), .en(enable), .Q(Rout), .clk(clk), .clr(clear));
  Register #(.width(32)) ALUresult (.D(ALUresult_in), .en(enable), .Q(ALUresult_out), .clk(clk), .clr(clear));

  // Notes on the sheet:
  //   WB
  //   MEM
endmodule

// MEM/WB
module MEM_WB (
  input  byteorword_in,
  input  syscall_in,
  input  [4:0] Rd_in,
  input  [4:0] Rt_in,
  input  RegDst_in,
  input  JAL_in,
  input  RegWrite_in,
  input  MemToReg_in,
  input  [31:0] IRin,
  input  [31:0] PCin,
  input  [31:0] ALUresult_in,
  input  [31:0] MemData_in,
  input  enable,
  input  clear,
  input  clk,
  output byteorword_out,
  output syscall_out,
  output [4:0] Rd_out,
  output [4:0] Rt_out,
  output RegDst_out,
  output JAL_out,
  output RegWrite_out,
  output MemToReg_out,
  output [31:0] IRout,
  output [31:0] PCout,
  output [31:0] ALUresult_out,
  output [31:0] MemData_out,
  output enable_out
);

  Register #(.width(1)) byteorword (.D(byteorword_in), .en(enable), .Q(byteorword_out), .clk(clk), .clr(clear));
  Register #(.width(1)) register_1 (.D(syscall_in), .en(enable), .Q(syscall_out), .clk(clk), .clr(clear));
  Register #(.width(5)) Rd (.D(Rd_in), .en(enable), .Q(Rd_out), .clk(clk), .clr(clear));
  Register #(.width(5)) Rt (.D(Rt_in), .en(enable), .Q(Rt_out), .clk(clk), .clr(clear));
  Register #(.width(1)) RegDst (.D(RegDst_in), .en(enable), .Q(RegDst_out), .clk(clk), .clr(clear));
  Register #(.width(1)) JAL (.D(JAL_in), .en(enable), .Q(JAL_out), .clk(clk), .clr(clear));
  Register #(.width(1)) RegWrite (.D(RegWrite_in), .en(enable), .Q(RegWrite_out), .clk(clk), .clr(clear));
  Register #(.width(1)) MemToReg (.D(MemToReg_in), .en(enable), .Q(MemToReg_out), .clk(clk), .clr(clear));
  Register #(.width(1)) register_2 (.D(enable), .Q(enable_out), .clk(clk), .clr(clear));  // open: en
  Register #(.width(32)) IR (.D(IRin), .en(enable), .Q(IRout), .clk(clk), .clr(clear));
  Register #(.width(32)) PC (.D(PCin), .en(enable), .Q(PCout), .clk(clk), .clr(clear));
  Register #(.width(32)) ALUresult (.D(ALUresult_in), .en(enable), .Q(ALUresult_out), .clk(clk), .clr(clear));
  Register #(.width(32)) MemData (.D(MemData_in), .en(enable), .Q(MemData_out), .clk(clk), .clr(clear));

  // Notes on the sheet:
  //   WB
endmodule

module \分支相关流水线  (
);

  wire CLK, Go, IR1, IR2, IR3, RST, W1, W2, W3;
  wire [11:0] EX_PC, ID_PC, IF_PC, MEM_PC, WB_PC;
  wire [15:0] \LoadUse次数 , \总周期数 , \插入气泡数 , \无条件分支数 , \条件分支成功数 ;
  wire [31:0] LedData;

  Button \u_总复位  (.out(RST));
  Button _1 (.out(IR1));
  Button _2 (.out(IR2));
  Button _3 (.out(IR3));
  Button \u_继续运行  (.out(Go));
  LED led_1 (.in(W1));
  LED led_2 (.in(W2));
  LED led_3 (.in(W3));
  Hex_Digit_Display hex_digit_display_1 (.value(LedData[31:28]));  // open: dp
  Hex_Digit_Display hex_digit_display_2 (.value(LedData[27:24]));  // open: dp
  Hex_Digit_Display hex_digit_display_3 (.value(LedData[23:20]));  // open: dp
  Hex_Digit_Display hex_digit_display_4 (.value(LedData[19:16]));  // open: dp
  Hex_Digit_Display hex_digit_display_5 (.value(LedData[15:12]));  // open: dp
  Hex_Digit_Display hex_digit_display_6 (.value(LedData[7:4]));  // open: dp
  Hex_Digit_Display hex_digit_display_7 (.value(LedData[11:8]));  // open: dp
  Clock clock_1 (.out(CLK));
  Hex_Digit_Display hex_digit_display_8 (.value(LedData[3:0]));  // open: dp
  // Probe on \总周期数 
  // Probe on \无条件分支数 
  // Probe on \条件分支成功数 
  // Probe on \插入气泡数 
  // Probe on \LoadUse次数 
  // Probe on IF_PC
  // Probe on ID_PC
  // Probe on MEM_PC
  // Probe on EX_PC
  // Probe on WB_PC

  // Notes on the sheet:
  //   中断源
  //   中断等待指示
  //   数码管输出
  //   流水调试日志用
endmodule

module \气泡流水线  (
);

  wire ALU_src_EX, ALU_src_ID, and_1_out, and_4_out, and_5_out, and_6_out, and_7_out, and_8_out, Beq_EX,
       Beq_ID, bltz_EX, bltz_ID, Bne_EX, Bne_ID, branch_EX, byteorword_EX, byteorword_ID, byteorword_MEM,
       byteorword_WB, CLK, comparator_1_eq, comparator_2_lt, condbranch_EX, data_related, display_ID,
       ex_mem_1_enable_out, ex_mem_1_memtoreg_out, ex_mem_1_syscall_out, Go, id_ex_1_enable_out, IR1, IR2,
       IR3, JAL_EX, JAL_ID, JAL_MEM, JAL_WB, JMP_EX, JMP_ID, JR_EX, JR_ID, MemToReg_EX, MemToReg_ID,
       MemToReg_WB, MemWrite_EX, MemWrite_ID, MemWrite_MEM, mips_alu_1_equal, not_1_out, not_2_out,
       not_3_out, not_4_out, not_6_out, not_7_out, not_8_out, or_1_out, or_2_out, pause_ID, pcable,
       pcable_out, RegDst_EX, RegDst_ID, RegDst_MEM, RegDst_WB, RegWrite_EX, RegWrite_ID, RegWrite_MEM,
       RegWrite_WB, RST, shamtsrc_EX, shamtsrc_ID, SignedExt_ID, syscall_EX, syscall_ID, syscall_WB, W1, W2,
       W3;
  wire [3:0] ALU_op_EX, ALU_op_ID;
  wire [4:0] id_ex_1_shamt_out, multiplexer_4_out, multiplexer_5_out, multiplexer_6_out, multiplexer_7_out,
       multiplexer_11_out, multiplexer_12_out, multiplexer_16_out, R1__ID, R2__ID, Rd_EX, Rd_MEM, Rd_WB,
       Rt_EX, Rt_MEM, Rt_WB;
  wire [5:0] Func_ID;
  wire [15:0] \LoadUse次数 , \总周期数 , \插入气泡数 , \无条件分支数 , \条件分支成功数 ;
  wire [27:0] adder_2_out;
  wire [31:0] adder_1_out, ALU_result_WB, ALUresult_MEM, and_9_out, beqbneaddr_EX, bit_extender_1_out,
       bit_extender_2_out, ex_mem_1_rout, EX_PC, ID_PC, IF_PC, Imm_EX, IR_EX, IR_MEM, IR_WB, JAL_WB_Addr,
       LedData, MEM_PC, MEM_WB_memdata_out, MemData_WB, mips_alu_1_result, multiplexer_1_out,
       multiplexer_2_out, multiplexer_3_out, multiplexer_8_out, multiplexer_13_out, multiplexer_14_out,
       multiplexer_15_out, PC_WB, R1_EX, R1_ID, R2_EX, R2_ID, ram_1_data, rom_1_data, shifter_1_out,
       shifter_2_out;
  wire [31:2] J_JAL_addr_EX;
  wire [31:6] IR_ID;

  Button \u_总复位  (.out(RST));
  Button _1 (.out(IR1));
  Button _2 (.out(IR2));
  Button _3 (.out(IR3));
  Button \u_继续运行  (.out(Go));
  LED led_1 (.in(W1));
  LED led_2 (.in(W2));
  LED led_3 (.in(W3));
  Hex_Digit_Display hex_digit_display_1 (.value(LedData[31:28]));  // open: dp
  Hex_Digit_Display hex_digit_display_2 (.value(LedData[27:24]));  // open: dp
  Hex_Digit_Display hex_digit_display_3 (.value(LedData[23:20]));  // open: dp
  Hex_Digit_Display hex_digit_display_4 (.value(LedData[19:16]));  // open: dp
  Hex_Digit_Display hex_digit_display_5 (.value(LedData[11:8]));  // open: dp
  Hex_Digit_Display hex_digit_display_6 (.value(LedData[15:12]));  // open: dp
  Hex_Digit_Display hex_digit_display_7 (.value(LedData[3:0]));  // open: dp
  Hex_Digit_Display hex_digit_display_8 (.value(LedData[7:4]));  // open: dp
  Clock clock_1 (.out(CLK));
  Multiplexer #(.width(32), .enable("false")) multiplexer_1 (
    .in0(adder_1_out), .in1(beqbneaddr_EX), .out(multiplexer_1_out), .sel(condbranch_EX));
  Multiplexer #(.width(32), .enable("false")) multiplexer_2 (
    .in0({J_JAL_addr_EX, 2'b00}), .in1(R1_EX), .out(multiplexer_2_out), .sel(JR_EX));
  Multiplexer #(.width(32), .enable("false")) multiplexer_3 (
    .in0(multiplexer_1_out), .in1(multiplexer_2_out), .out(multiplexer_3_out), .sel(JMP_EX));
  Register #(.width(32)) PC (.D(multiplexer_3_out), .en(and_1_out), .Q(IF_PC), .clk(CLK), .clr(RST));
  and and_1 (and_1_out, not_1_out, pcable);
  not not_1 (not_1_out, data_related);
  // Probe on \总周期数 
  // Probe on \无条件分支数 
  // Probe on \条件分支成功数 
  // Probe on \插入气泡数 
  // Probe on \LoadUse次数 
  Multiplexer #(.width(5), .enable("false")) multiplexer_4 (
    .in0(Rt_EX), .in1(Rd_EX), .out(multiplexer_4_out), .sel(RegDst_EX));
  Comparator #(.width(32)) comparator_1 (.a(R1_ID), .b(32'h22), .eq(comparator_1_eq));  // open: gt, lt
  // Probe on IF_PC[11:0]
  Multiplexer #(.width(5), .enable("false")) multiplexer_5 (
    .in0(Rt_MEM), .in1(Rd_MEM), .out(multiplexer_5_out), .sel(RegDst_MEM));
  not not_2 (not_2_out, comparator_1_eq);
  // Probe on ID_PC[11:0]
  // Probe on EX_PC[11:0]
  Multiplexer #(.width(5), .enable("false")) multiplexer_6 (
    .in0(multiplexer_4_out), .in1({5{1'b1}}), .out(multiplexer_6_out), .sel(JAL_EX));
  Multiplexer #(.width(5), .enable("false")) multiplexer_7 (
    .in0(multiplexer_5_out), .in1({5{1'b1}}), .out(multiplexer_7_out), .sel(JAL_MEM));
  and and_2 (display_ID, comparator_1_eq, syscall_ID);
  and and_3 (pause_ID, syscall_ID, not_2_out);
  // Probe on MEM_PC[11:0]
  // Probe on PC_WB[11:0]
  \数据相关检测  \u_数据相关检测_1  (
    .OP(IR_ID[31:26]), .EX_WriteReg_num(multiplexer_6_out), .EX_RegWrite(RegWrite_EX),
    .MEM_WriteReg_num(multiplexer_7_out), .MEM_RegWrite(RegWrite_MEM), .\数据相关 (data_related), .Func(Func_ID),
    .ID_R1_num(R1__ID), .ID_R2_num(R2__ID));
  ROM #(.addrWidth(10), .dataWidth(32)) rom_1 (.addr(IF_PC[11:2]), .data(rom_1_data));  // open: sel
  // Probe on {IR_ID, Func_ID}
  and and_4 (and_4_out, not_3_out, pcable);
  not not_3 (not_3_out, data_related);
  IF_ID if_id_1 (
    .IRin(rom_1_data), .PCin(IF_PC), .IRout({IR_ID, Func_ID}), .PCout(ID_PC), .clk(CLK), .enable(and_4_out),
    .clear_tong(branch_EX), .clear_yi(RST));  // open: enable_out, Miss_in, Miss_out, predict_branch_in, predict_branch_out
  Register #(.width(32)) register_1 (.D(R2_ID), .en(display_ID), .Q(LedData), .clk(CLK), .clr(RST));
  assign bit_extender_1_out = {{16{1'b0}}, {IR_ID[15:6], Func_ID}};  // Bit_Extender bit_extender_1
  assign bit_extender_2_out = {{16{IR_ID[15]}}, {IR_ID[15:6], Func_ID}};  // Bit_Extender bit_extender_2
  Multiplexer #(.width(32), .enable("false")) multiplexer_8 (
    .in0(bit_extender_1_out), .in1(bit_extender_2_out), .out(multiplexer_8_out), .sel(SignedExt_ID));
  Adder #(.width(32)) adder_1 (.a(IF_PC), .b(32'h4), .out(adder_1_out));  // open: cin, cout
  Multiplexer #(.width(5), .enable("false")) multiplexer_9 (
    .in0(IR_ID[25:21]), .in1(5'b00010), .out(R1__ID), .sel(syscall_ID));
  Multiplexer #(.width(5), .enable("false")) multiplexer_10 (
    .in0(IR_ID[20:16]), .in1(5'b00100), .out(R2__ID), .sel(syscall_ID));
  Multiplexer #(.width(5), .enable("false")) multiplexer_11 (
    .in0(Rt_WB), .in1(Rd_WB), .out(multiplexer_11_out), .sel(RegDst_WB));
  not not_4 (not_4_out, Go);
  // newcontrol 扩展指令译码: pin names not known; wires that end beside it: IR_ID[26], IR_ID[27], IR_ID[28], IR_ID[29], IR_ID[30], IR_ID[31], Func_ID[0], Func_ID[1], Func_ID[2], Func_ID[3], Func_ID[4], Func_ID[5], shamtsrc_ID, byteorword_ID, bltz_ID
  \硬布线控制器  \u_硬布线控制器_1  (
    .Func(Func_ID), .OP(IR_ID[31:26]), .ALU_OP(ALU_op_ID), .MemToReg(MemToReg_ID), .MemWrite(MemWrite_ID),
    .ALU_SRC(ALU_src_ID), .RegWrite(RegWrite_ID), .SysCALL(syscall_ID), .SignedExt(SignedExt_ID),
    .RegDst(RegDst_ID), .JR(JR_ID), .JMP(JMP_ID), .Beq(Beq_ID), .JAL(JAL_ID), .Bne(Bne_ID));
  Multiplexer #(.width(5), .enable("false")) multiplexer_12 (
    .in0(multiplexer_11_out), .in1({5{1'b1}}), .out(multiplexer_12_out), .sel(JAL_WB));
  Multiplexer #(.width(32), .enable("false")) multiplexer_13 (
    .in0(multiplexer_14_out), .in1(JAL_WB_Addr), .out(multiplexer_13_out), .sel(JAL_WB));
  Multiplexer #(.width(32), .enable("false")) multiplexer_14 (
    .in0(ALU_result_WB), .in1(MemData_WB), .out(multiplexer_14_out), .sel(MemToReg_WB));
  not not_5 (pcable, and_5_out);
  and and_5 (and_5_out, not_4_out, pause_ID);
  not not_6 (not_6_out, syscall_WB);
  Counter #(.width(16), .max('hffff)) counter_1 (
    .count(data_related), .Q(\插入气泡数 ), .clk(CLK), .clr(RST));  // open: load, D, carry
  MIPS_Regifile mips_regifile_1 (
    .Din(multiplexer_13_out), .Clk(CLK), .R1(R1_ID), .R2(R2_ID), .WE(RegWrite_WB),
    .W_num(multiplexer_12_out), .R1_num(R1__ID), .R2_num(R2__ID));
  or or_1 (or_1_out, pcable, not_6_out);
  Counter #(.width(16), .max('hffff)) counter_2 (
    .count(or_1_out), .Q(\总周期数 ), .clk(CLK), .clr(RST));  // open: load, D, carry
  ID_EX id_ex_1 (
    .RegDst_in(RegDst_ID), .JAL_in(JAL_ID), .RegWrite_in(RegWrite_ID), .MemToReg_in(MemToReg_ID),
    .MemWrite_in(MemWrite_ID), .ALU_OP_in(ALU_op_ID), .ALU_src_in(ALU_src_ID), .Bne_in(Bne_ID),
    .Beq_in(Beq_ID), .IRin({IR_ID, Func_ID}), .PCin(ID_PC), .R1in(R1_ID), .R2in(R2_ID),
    .IMMin(multiplexer_8_out), .RegDst_out(RegDst_EX), .JAL_out(JAL_EX), .RegWrite_out(RegWrite_EX),
    .MemToReg_out(MemToReg_EX), .MemWrite_out(MemWrite_EX), .ALU_OP_out(ALU_op_EX), .ALU_src_out(ALU_src_EX),
    .Bne_out(Bne_EX), .Beq_out(Beq_EX), .out_55(IR_EX), .PCout(EX_PC), .R1out(R1_EX), .R2out(R2_EX),
    .IMMout(Imm_EX), .enable(1'b1), .clk(CLK), .clear_tong(or_2_out), .shamt_in(IR_ID[10:6]),
    .shamt_out(id_ex_1_shamt_out), .enable_out(id_ex_1_enable_out), .Rd_in(IR_ID[15:11]),
    .Rt_in(IR_ID[20:16]), .Rt_out(Rt_EX), .Rd_out(Rd_EX), .JMP_in(JMP_ID), .JR_in(JR_ID), .JMP_out(JMP_EX),
    .JR_out(JR_EX), .J_JAL_imm_in({IR_ID[25:6], Func_ID}), .J_JAL_imm_out(J_JAL_addr_EX[27:2]),
    .syscall_in(syscall_ID), .syscall_out(syscall_EX), .shamtsrc_in(shamtsrc_ID), .bltz_in(bltz_ID),
    .byteorword_in(byteorword_ID), .shamtsrc_out(shamtsrc_EX), .bltz_out(bltz_EX),
    .byteorword_out(byteorword_EX));  // open: forwardB_in, forwardA_in, forwardB_out, forwardA_out, clear_yibu, Miss_in, Miss_out, predict_branch_in, predict_branch_out
  or or_2 (or_2_out, RST, data_related, branch_EX);
  Adder #(.width(32)) adder_2 (.a(EX_PC), .b(32'h4), .out({J_JAL_addr_EX[31:28], adder_2_out}));  // open: cin, cout
  Shifter #(.width(32)) shifter_1 (.in(Imm_EX), .\dist (5'b00010), .out(shifter_1_out));
  Multiplexer #(.width(32), .enable("false")) multiplexer_15 (
    .in0(R2_EX), .in1(Imm_EX), .out(multiplexer_15_out), .sel(ALU_src_EX));
  Multiplexer #(.width(5), .enable("false")) multiplexer_16 (
    .in0(id_ex_1_shamt_out), .in1(R1_EX[4:0]), .out(multiplexer_16_out), .sel(shamtsrc_EX));
  or or_3 (branch_EX, JMP_EX, condbranch_EX);
  Counter #(.width(16), .max('hffff)) counter_3 (
    .count(JMP_EX), .Q(\无条件分支数 ), .clk(CLK), .clr(RST));  // open: load, D, carry
  or or_4 (condbranch_EX, and_6_out, and_7_out, and_8_out);
  and and_6 (and_6_out, Beq_EX, mips_alu_1_equal);
  and and_7 (and_7_out, not_7_out, Bne_EX);
  not not_7 (not_7_out, mips_alu_1_equal);
  MIPS_ALU mips_alu_1 (
    .X(R1_EX), .Y(multiplexer_15_out), .AluOP(ALU_op_EX), .Equal(mips_alu_1_equal),
    .Result(mips_alu_1_result), .shamt(multiplexer_16_out));  // open: Result_2
  Adder #(.width(32)) adder_3 (
    .a({J_JAL_addr_EX[31:28], adder_2_out}), .b(shifter_1_out), .out(beqbneaddr_EX));  // open: cin, cout
  Counter #(.width(16), .max('hffff)) counter_4 (
    .count(condbranch_EX), .Q(\条件分支成功数 ), .clk(CLK), .clr(RST));  // open: load, D, carry
  and and_8 (and_8_out, bltz_EX, comparator_2_lt);
  Comparator #(.width(32)) comparator_2 (.a(R1_EX), .b({32{1'b0}}), .lt(comparator_2_lt));  // open: gt, eq
  EX_MEM ex_mem_1 (
    .RegDst_in(RegDst_EX), .JAL_in(JAL_EX), .RegWrite_in(RegWrite_EX), .MemToReg_in(MemToReg_EX),
    .MemWrite_in(MemWrite_EX), .IRin(IR_EX), .PCin(EX_PC), .Rin(R2_EX), .ALUresult_in(mips_alu_1_result),
    .RegDst_out(RegDst_MEM), .JAL_out(JAL_MEM), .RegWrite_out(RegWrite_MEM),
    .MemToReg_out(ex_mem_1_memtoreg_out), .MemWrite_out(MemWrite_MEM), .IRout(IR_MEM), .PCout(MEM_PC),
    .Rout(ex_mem_1_rout), .ALUresult_out(ALUresult_MEM), .enable(id_ex_1_enable_out), .clk(CLK), .clear(RST),
    .enable_out(ex_mem_1_enable_out), .Rt_in(Rt_EX), .Rd_in(Rd_EX), .Rd_out(Rd_MEM), .Rt_out(Rt_MEM),
    .syscal_in(syscall_EX), .syscall_out(ex_mem_1_syscall_out), .byteorword_out(byteorword_MEM),
    .byteorword_in(byteorword_EX));
  not not_8 (not_8_out, MemWrite_MEM);
  RAM #(.addrWidth(10), .dataWidth(32), .bus("separate")) ram_1 (
    .addr(ALUresult_MEM[11:2]), .din(ex_mem_1_rout), .data(ram_1_data), .str(MemWrite_MEM), .clk(CLK),
    .ld(not_8_out), .clr(RST));  // open: sel
  MEM_WB MEM_WB (
    .RegDst_in(RegDst_MEM), .JAL_in(JAL_MEM), .RegWrite_in(RegWrite_MEM),
    .MemToReg_in(ex_mem_1_memtoreg_out), .IRin(IR_MEM), .PCin(MEM_PC), .ALUresult_in(ALUresult_MEM),
    .MemData_in(ram_1_data), .RegDst_out(RegDst_WB), .JAL_out(JAL_WB), .RegWrite_out(RegWrite_WB),
    .MemToReg_out(MemToReg_WB), .IRout(IR_WB), .PCout(PC_WB), .ALUresult_out(ALU_result_WB),
    .MemData_out(MEM_WB_memdata_out), .enable(ex_mem_1_enable_out), .clk(CLK), .clear(RST),
    .enable_out(pcable_out), .Rt_out(Rt_WB), .Rd_out(Rd_WB), .Rt_in(Rt_MEM), .Rd_in(Rd_MEM),
    .syscall_in(ex_mem_1_syscall_out), .syscall_out(syscall_WB), .byteorword_in(byteorword_MEM),
    .byteorword_out(byteorword_WB));
  Adder #(.width(32)) adder_4 (.a(PC_WB), .b(32'h4), .out(JAL_WB_Addr));  // open: cin, cout
  Shifter #(.width(32), .shift("lr")) shifter_2 (
    .in(MEM_WB_memdata_out), .\dist ({ALU_result_WB[1:0], 3'b000}), .out(shifter_2_out));
  assign and_9_out = shifter_2_out & 32'hff;  // AND_Gate and_9, 32 bits wide
  Multiplexer #(.width(32), .enable("false")) multiplexer_17 (
    .in0(MEM_WB_memdata_out), .in1(and_9_out), .out(MemData_WB), .sel(byteorword_WB));

  // Other names for the same wires on the sheet: IR_ID[5:0] = Func_ID; J_JAL_imm_ID[25:0] = {IR_ID[25:6], Func_ID};
  //   Rd_ID[4:0] = IR_ID[15:11]; OP_ID[5:0] = IR_ID[31:26]; J_JAL_imm_EX[25:0] = J_JAL_addr_EX[27:2];
  //   Rt_ID[4:0] = IR_ID[20:16]; PC_EX[31:0] = EX_PC; PC_ID[31:0] = ID_PC; PC_MEM[31:0] = MEM_PC; WB_PC[31:0] = PC_WB

  // Notes on the sheet:
  //   中断源
  //   中断等待指示
  //   数码管输出
  //   流水调试日志用
  //   指令存储器
  //   contents of rom_1 (hex, n*v repeats v):
  //   20110001 8000c05 20110001 20120002 20130003 8000c09 20110001 20120002 20130003 8000c0d 20110001
  //   20120002 20130003 8000c11 20110001 20120002 20130003 c000cbb 20100001 20110001 118fc0 112020
  //   20020022 c 118882 12200001 8000c15 112020 20020022 c 20110001 118880 112020 20020022 c 12200001
  //   8000c1f 20110001 118fc0 112020 20020022 c 1188c3 112020 20020022 c 118903 112020 20020022 c 118903
  //   112020 20020022 c 118903 112020 20020022 c 118903 112020 20020022 c 118903 112020 20020022 c 118903
  //   112020 20020022 c 118903 112020 20020022 c 20100001 109fc0 139fc3 8021 2012000c 24160003 26100001
  //   3210000f 20080008 20090001 139900 2709825 132020 20020022 c 1094022 1500fff9 22100001 2018000f
  //   2188024 108700 20080008 20090001 139902 2709825 132021 20020022 c 1094022 1500fff9 108702 2c9b022
  //   12c00001 8000c50 4020 1084027 84400 3508ffff 82021 20020022 c 2010ffff 20110000 ae300000 22100001
  //   22310004 ae300000 22100001 22310004 ae300000 22100001 22310004 ae300000 22100001 22310004 ae300000
  //   22100001 22310004 ae300000 22100001 22310004 ae300000 22100001 22310004 ae300000 22100001 22310004
  //   ae300000 22100001 22310004 ae300000 22100001 22310004 ae300000 22100001 22310004 ae300000 22100001
  //   22310004 ae300000 22100001 22310004 ae300000 22100001 22310004 ae300000 22100001 22310004 ae300000
  //   22100001 22310004 22100001 8020 2011003c 8e130000 8e340000 274402a 11000002 ae330000 ae140000
  //   2231fffc 1611fff8 102020 20020022 c 22100004 2011003c 1611fff2 20020032 c 8000c00 2002000a c
  //   20100000 22100001 102020 20020022 c 22100002 102020 20020022 c 22100003 102020 20020022 c 22100004
  //   102020 20020022 c 22100005 102020 20020022 c 22100006 102020 20020022 c 22100007 102020 20020022 c
  //   22100008 102020 20020022 20020022 c 3e00008
  //   OP
  //   func
  //   rs
  //   rt
  //   rd
  //   数据寄存器
endmodule

module \重定向流水线  (
);

  wire ALU_src_EX, ALU_src_ID, and_1_out, and_4_out, and_5_out, and_6_out, and_7_out, and_8_out, Beq_EX,
       Beq_ID, bltz_EX, bltz_ID, Bne_EX, Bne_ID, branch_EX, byteorword_EX, byteorword_ID, byteorword_MEM,
       byteorword_WB, CLK, comparator_1_eq, comparator_2_lt, condbranch_EX, data_related, display_EX,
       ex_mem_1_enable_out, ex_mem_1_syscall_out, Go, id_ex_1_enable_out, IR1, IR2, IR3, JAL_EX, JAL_ID,
       JAL_MEM, JAL_WB, JMP_EX, JMP_ID, JR_EX, JR_ID, loaduse_ID, MemToReg_EX, MemToReg_ID, MemToReg_MEM,
       MemToReg_WB, MemWrite_EX, MemWrite_ID, MemWrite_MEM, mips_alu_1_equal, not_1_out, not_2_out,
       not_3_out, not_4_out, not_6_out, not_7_out, not_8_out, or_1_out, or_2_out, pause_EX, pcable,
       pcable_out, RegDst_EX, RegDst_ID, RegDst_MEM, RegDst_WB, RegWrite_EX, RegWrite_ID, RegWrite_MEM,
       RegWrite_WB, RST, shamtsrc_EX, shamtsrc_ID, SignedExt_ID, syscall_EX, syscall_ID, syscall_WB, W1, W2,
       W3;
  wire [1:0] forwardA_EX, forwardA_ID, forwardB_EX, forwardB_ID;
  wire [3:0] ALU_op_EX, ALU_op_ID;
  wire [4:0] id_ex_1_shamt_out, multiplexer_4_out, multiplexer_5_out, multiplexer_6_out, multiplexer_7_out,
       multiplexer_11_out, multiplexer_12_out, multiplexer_18_out, R1__ID, R2__ID, Rd_EX, Rd_MEM, Rd_WB,
       Rt_EX, Rt_MEM, Rt_WB;
  wire [5:0] Func_ID;
  wire [15:0] \LoadUse次数 , \总周期数 , \插入气泡数 , \无条件分支数 , \条件分支成功数 ;
  wire [27:0] adder_2_out;
  wire [31:0] adder_1_out, ALU_result_WB, ALUresult_MEM, and_9_out, beqbneaddr_EX, bit_extender_1_out,
       bit_extender_2_out, ex_mem_1_rout, EX_PC, ID_PC, IF_PC, Imm_EX, IR_EX, IR_MEM, IR_WB, JAL_WB_Addr,
       LedData, MEM_PC, MEM_WB_memdata_out, MemData_WB, mips_alu_1_result, multiplexer_1_out,
       multiplexer_2_out, multiplexer_3_out, multiplexer_8_out, multiplexer_13_out, multiplexer_14_out,
       multiplexer_17_out, PC_WB, R1_EX, R1_first_use, R1_ID, R2_EX, R2_first_use, R2_ID, ram_1_data,
       rom_1_data, shifter_1_out, shifter_2_out;
  wire [31:2] J_JAL_addr_EX;
  wire [31:6] IR_ID;

  Button \u_总复位  (.out(RST));
  Button _1 (.out(IR1));
  Button _2 (.out(IR2));
  Button _3 (.out(IR3));
  Button \u_继续运行  (.out(Go));
  LED led_1 (.in(W1));
  LED led_2 (.in(W2));
  LED led_3 (.in(W3));
  Hex_Digit_Display hex_digit_display_1 (.value(LedData[31:28]));  // open: dp
  Hex_Digit_Display hex_digit_display_2 (.value(LedData[27:24]));  // open: dp
  Hex_Digit_Display hex_digit_display_3 (.value(LedData[19:16]));  // open: dp
  Hex_Digit_Display hex_digit_display_4 (.value(LedData[23:20]));  // open: dp
  // Probe on {J_JAL_addr_EX, 2'b00}
  Hex_Digit_Display hex_digit_display_5 (.value(LedData[15:12]));  // open: dp
  Hex_Digit_Display hex_digit_display_6 (.value(LedData[11:8]));  // open: dp
  Hex_Digit_Display hex_digit_display_7 (.value(LedData[7:4]));  // open: dp
  Hex_Digit_Display hex_digit_display_8 (.value(LedData[3:0]));  // open: dp
  Clock clock_1 (.out(CLK));
  Multiplexer #(.width(32), .enable("false")) multiplexer_1 (
    .in0(adder_1_out), .in1(beqbneaddr_EX), .out(multiplexer_1_out), .sel(condbranch_EX));
  Multiplexer #(.width(32), .enable("false")) multiplexer_2 (
    .in0({J_JAL_addr_EX, 2'b00}), .in1(R1_EX), .out(multiplexer_2_out), .sel(JR_EX));
  Multiplexer #(.width(32), .enable("false")) multiplexer_3 (
    .in0(multiplexer_1_out), .in1(multiplexer_2_out), .out(multiplexer_3_out), .sel(JMP_EX));
  Register #(.width(32)) PC (.D(multiplexer_3_out), .en(and_1_out), .Q(IF_PC), .clk(CLK), .clr(RST));
  and and_1 (and_1_out, not_1_out, pcable);
  not not_1 (not_1_out, loaduse_ID);
  // Probe on \总周期数 
  // Probe on \无条件分支数 
  // Probe on \条件分支成功数 
  // Probe on \插入气泡数 
  // Probe on \LoadUse次数 
  Multiplexer #(.width(5), .enable("false")) multiplexer_4 (
    .in0(Rt_EX), .in1(Rd_EX), .out(multiplexer_4_out), .sel(RegDst_EX));
  Multiplexer #(.width(5), .enable("false")) multiplexer_5 (
    .in0(Rt_MEM), .in1(Rd_MEM), .out(multiplexer_5_out), .sel(RegDst_MEM));
  Comparator #(.width(32)) comparator_1 (.a(R1_first_use), .b(32'h22), .eq(comparator_1_eq));  // open: gt, lt
  // Probe on IF_PC[11:0]
  Multiplexer #(.width(5), .enable("false")) multiplexer_6 (
    .in0(multiplexer_4_out), .in1({5{1'b1}}), .out(multiplexer_6_out), .sel(JAL_EX));
  Multiplexer #(.width(5), .enable("false")) multiplexer_7 (
    .in0(multiplexer_5_out), .in1({5{1'b1}}), .out(multiplexer_7_out), .sel(JAL_MEM));
  not not_2 (not_2_out, comparator_1_eq);
  // Probe on ID_PC[11:0]
  // Probe on EX_PC[11:0]
  and and_2 (display_EX, comparator_1_eq, syscall_EX);
  and and_3 (pause_EX, syscall_EX, not_2_out);
  // Probe on MEM_PC[11:0]
  \重定向数据检测  \u_重定向数据检测_1  (
    .OP(IR_ID[31:26]), .EX_WriteReg_num(multiplexer_6_out), .EX_RegWrite(RegWrite_EX),
    .EX_MemToReg(MemToReg_EX), .forwardA(forwardA_ID), .MEM_WriteReg_num(multiplexer_7_out),
    .MEM_RegWrite(RegWrite_MEM), .load_use(loaduse_ID), .MEM_MemToReg(MemToReg_MEM), .Func(Func_ID),
    .ID_R1_num(R1__ID), .ID_R2_num(R2__ID), .forwardB(forwardB_ID));
  \数据相关检测  \u_数据相关检测_1  (
    .OP(IR_ID[31:26]), .EX_WriteReg_num(multiplexer_6_out), .EX_RegWrite(RegWrite_EX),
    .MEM_WriteReg_num(multiplexer_7_out), .MEM_RegWrite(RegWrite_MEM), .\数据相关 (data_related), .Func(Func_ID),
    .ID_R1_num(R1__ID), .ID_R2_num(R2__ID));
  // Probe on PC_WB[11:0]
  // Probe on forwardA_ID
  // Probe on forwardB_ID
  // Probe on loaduse_ID
  ROM #(.addrWidth(10), .dataWidth(32)) rom_1 (.addr(IF_PC[11:2]), .data(rom_1_data));  // open: sel
  // Probe on IF_PC
  // Probe on {IR_ID, Func_ID}
  and and_4 (and_4_out, not_3_out, pcable);
  not not_3 (not_3_out, loaduse_ID);
  IF_ID if_id_1 (
    .IRin(rom_1_data), .PCin(IF_PC), .IRout({IR_ID, Func_ID}), .PCout(ID_PC), .clk(CLK), .enable(and_4_out),
    .clear_tong(branch_EX), .clear_yi(RST));  // open: enable_out, Miss_in, Miss_out, predict_branch_in, predict_branch_out
  Register #(.width(32)) register_1 (.D(R2_first_use), .en(display_EX), .Q(LedData), .clk(CLK), .clr(RST));
  assign bit_extender_1_out = {{16{1'b0}}, {IR_ID[15:6], Func_ID}};  // Bit_Extender bit_extender_1
  assign bit_extender_2_out = {{16{IR_ID[15]}}, {IR_ID[15:6], Func_ID}};  // Bit_Extender bit_extender_2
  // Probe on ID_PC[11:0]
  // Probe on ID_PC[11:0]
  Multiplexer #(.width(32), .enable("false")) multiplexer_8 (
    .in0(bit_extender_1_out), .in1(bit_extender_2_out), .out(multiplexer_8_out), .sel(SignedExt_ID));
  Adder #(.width(32)) adder_1 (.a(IF_PC), .b(32'h4), .out(adder_1_out));  // open: cin, cout
  Multiplexer #(.width(5), .enable("false")) multiplexer_9 (
    .in0(IR_ID[25:21]), .in1(5'b00010), .out(R1__ID), .sel(syscall_ID));
  Multiplexer #(.width(5), .enable("false")) multiplexer_10 (
    .in0(IR_ID[20:16]), .in1(5'b00100), .out(R2__ID), .sel(syscall_ID));
  // Probe on R2__ID
  Multiplexer #(.width(5), .enable("false")) multiplexer_11 (
    .in0(Rt_WB), .in1(Rd_WB), .out(multiplexer_11_out), .sel(RegDst_WB));
  not not_4 (not_4_out, Go);
  // newcontrol 扩展指令译码: pin names not known; wires that end beside it: IR_ID[26], IR_ID[27], IR_ID[28], IR_ID[29], IR_ID[30], IR_ID[31], Func_ID[0], Func_ID[1], Func_ID[2], Func_ID[3], Func_ID[4], Func_ID[5], shamtsrc_ID, byteorword_ID, bltz_ID
  \硬布线控制器  \u_硬布线控制器_1  (
    .Func(Func_ID), .OP(IR_ID[31:26]), .ALU_OP(ALU_op_ID), .MemToReg(MemToReg_ID), .MemWrite(MemWrite_ID),
    .ALU_SRC(ALU_src_ID), .RegWrite(RegWrite_ID), .SysCALL(syscall_ID), .SignedExt(SignedExt_ID),
    .RegDst(RegDst_ID), .JR(JR_ID), .JMP(JMP_ID), .Beq(Beq_ID), .JAL(JAL_ID), .Bne(Bne_ID));
  // Probe on {IR_ID[25:6], Func_ID}
  // Probe on R1__ID
  Multiplexer #(.width(5), .enable("false")) multiplexer_12 (
    .in0(multiplexer_11_out), .in1({5{1'b1}}), .out(multiplexer_12_out), .sel(JAL_WB));
  // Probe on multiplexer_12_out
  Multiplexer #(.width(32), .enable("false")) multiplexer_13 (
    .in0(multiplexer_14_out), .in1(JAL_WB_Addr), .out(multiplexer_13_out), .sel(JAL_WB));
  Multiplexer #(.width(32), .enable("false")) multiplexer_14 (
    .in0(ALU_result_WB), .in1(MemData_WB), .out(multiplexer_14_out), .sel(MemToReg_WB));
  not not_5 (pcable, and_5_out);
  and and_5 (and_5_out, not_4_out, pause_EX);
  // Probe on {IR_ID[25:6], Func_ID}
  // Probe on multiplexer_13_out
  not not_6 (not_6_out, syscall_WB);
  MIPS_Regifile mips_regifile_1 (
    .Din(multiplexer_13_out), .Clk(CLK), .R1(R1_ID), .R2(R2_ID), .WE(RegWrite_WB),
    .W_num(multiplexer_12_out), .R1_num(R1__ID), .R2_num(R2__ID));
  or or_1 (or_1_out, pcable, not_6_out);
  // Probe on ID_PC
  Counter #(.width(16), .max('hffff)) counter_1 (
    .count(or_1_out), .Q(\总周期数 ), .clk(CLK), .clr(RST));  // open: load, D, carry
  ID_EX id_ex_1 (
    .RegDst_in(RegDst_ID), .JAL_in(JAL_ID), .RegWrite_in(RegWrite_ID), .MemToReg_in(MemToReg_ID),
    .MemWrite_in(MemWrite_ID), .ALU_OP_in(ALU_op_ID), .ALU_src_in(ALU_src_ID), .Bne_in(Bne_ID),
    .Beq_in(Beq_ID), .IRin({IR_ID, Func_ID}), .PCin(ID_PC), .R1in(R1_ID), .R2in(R2_ID),
    .IMMin(multiplexer_8_out), .RegDst_out(RegDst_EX), .JAL_out(JAL_EX), .RegWrite_out(RegWrite_EX),
    .MemToReg_out(MemToReg_EX), .MemWrite_out(MemWrite_EX), .ALU_OP_out(ALU_op_EX), .ALU_src_out(ALU_src_EX),
    .Bne_out(Bne_EX), .Beq_out(Beq_EX), .out_55(IR_EX), .PCout(EX_PC), .R1out(R1_EX), .R2out(R2_EX),
    .IMMout(Imm_EX), .enable(pcable), .clk(CLK), .clear_tong(or_2_out), .shamt_in(IR_ID[10:6]),
    .shamt_out(id_ex_1_shamt_out), .enable_out(id_ex_1_enable_out), .Rd_in(IR_ID[15:11]),
    .Rt_in(IR_ID[20:16]), .Rt_out(Rt_EX), .Rd_out(Rd_EX), .JMP_in(JMP_ID), .JR_in(JR_ID), .JMP_out(JMP_EX),
    .JR_out(JR_EX), .J_JAL_imm_in({IR_ID[25:6], Func_ID}), .J_JAL_imm_out(J_JAL_addr_EX[27:2]),
    .syscall_in(syscall_ID), .syscall_out(syscall_EX), .shamtsrc_in(shamtsrc_ID), .bltz_in(bltz_ID),
    .byteorword_in(byteorword_ID), .shamtsrc_out(shamtsrc_EX), .bltz_out(bltz_EX),
    .byteorword_out(byteorword_EX), .forwardB_in(forwardB_ID), .forwardA_in(forwardA_ID),
    .forwardB_out(forwardB_EX), .forwardA_out(forwardA_EX), .clear_yibu(RST));  // open: Miss_in, Miss_out, predict_branch_in, predict_branch_out
  or or_2 (or_2_out, loaduse_ID, branch_EX);
  // Probe on EX_PC
  // Probe on J_JAL_addr_EX[27:2]
  // Probe on EX_PC
  Adder #(.width(32)) adder_2 (.a(EX_PC), .b(32'h4), .out({J_JAL_addr_EX[31:28], adder_2_out}));  // open: cin, cout
  Shifter #(.width(32)) shifter_1 (.in(Imm_EX), .\dist (5'b00010), .out(shifter_1_out));
  // Probe on J_JAL_addr_EX[27:2]
  // Probe on J_JAL_addr_EX[27:2]
  or or_3 (branch_EX, JMP_EX, condbranch_EX);
  Counter #(.width(16), .max('hffff)) counter_2 (
    .count(JMP_EX), .Q(\无条件分支数 ), .clk(CLK), .clr(RST));  // open: load, D, carry
  // Probe on J_JAL_addr_EX[27:2]
  and and_6 (and_6_out, Beq_EX, mips_alu_1_equal);
  Multiplexer #(.select(2), .width(32), .enable("false")) multiplexer_15 (
    .in0(R1_EX), .in1(MemData_WB), .in2(ALU_result_WB), .in3(ALUresult_MEM), .out(R1_first_use),
    .sel(forwardA_EX));
  Multiplexer #(.select(2), .width(32), .enable("false")) multiplexer_16 (
    .in0(R2_EX), .in1(MemData_WB), .in2(ALU_result_WB), .in3(ALUresult_MEM), .out(R2_first_use),
    .sel(forwardB_EX));
  Adder #(.width(32)) adder_3 (
    .a({J_JAL_addr_EX[31:28], adder_2_out}), .b(shifter_1_out), .out(beqbneaddr_EX));  // open: cin, cout
  or or_4 (condbranch_EX, and_6_out, and_7_out, and_8_out);
  and and_7 (and_7_out, not_7_out, Bne_EX);
  not not_7 (not_7_out, mips_alu_1_equal);
  // Probe on R1_first_use
  Multiplexer #(.width(32), .enable("false")) multiplexer_17 (
    .in0(R2_first_use), .in1(Imm_EX), .out(multiplexer_17_out), .sel(ALU_src_EX));
  // Probe on R2_first_use
  Multiplexer #(.width(5), .enable("false")) multiplexer_18 (
    .in0(id_ex_1_shamt_out), .in1(R1_EX[4:0]), .out(multiplexer_18_out), .sel(shamtsrc_EX));
  // Probe on {J_JAL_addr_EX, 2'b00}
  // Probe on J_JAL_addr_EX[31:28]
  Counter #(.width(16), .max('hffff)) counter_3 (
    .count(condbranch_EX), .Q(\条件分支成功数 ), .clk(CLK), .clr(RST));  // open: load, D, carry
  and and_8 (and_8_out, bltz_EX, comparator_2_lt);
  MIPS_ALU mips_alu_1 (
    .X(R1_first_use), .Y(multiplexer_17_out), .AluOP(ALU_op_EX), .Equal(mips_alu_1_equal),
    .Result(mips_alu_1_result), .shamt(multiplexer_18_out));  // open: Result_2
  // Probe on multiplexer_17_out
  // Probe on {J_JAL_addr_EX, 2'b00}
  Comparator #(.width(32)) comparator_2 (.a(R1_first_use), .b({32{1'b0}}), .lt(comparator_2_lt));  // open: gt, eq
  // Probe on mips_alu_1_result
  // Probe on R2_first_use
  EX_MEM ex_mem_1 (
    .RegDst_in(RegDst_EX), .JAL_in(JAL_EX), .RegWrite_in(RegWrite_EX), .MemToReg_in(MemToReg_EX),
    .MemWrite_in(MemWrite_EX), .IRin(IR_EX), .PCin(EX_PC), .Rin(R2_first_use),
    .ALUresult_in(mips_alu_1_result), .RegDst_out(RegDst_MEM), .JAL_out(JAL_MEM),
    .RegWrite_out(RegWrite_MEM), .MemToReg_out(MemToReg_MEM), .MemWrite_out(MemWrite_MEM), .IRout(IR_MEM),
    .PCout(MEM_PC), .Rout(ex_mem_1_rout), .ALUresult_out(ALUresult_MEM), .enable(id_ex_1_enable_out),
    .clk(CLK), .clear(RST), .enable_out(ex_mem_1_enable_out), .Rt_in(Rt_EX), .Rd_in(Rd_EX), .Rd_out(Rd_MEM),
    .Rt_out(Rt_MEM), .syscal_in(syscall_EX), .syscall_out(ex_mem_1_syscall_out),
    .byteorword_out(byteorword_MEM), .byteorword_in(byteorword_EX));
  // Probe on {J_JAL_addr_EX[11:2], 2'b00}
  // Probe on ALUresult_MEM[11:2]
  // Probe on MEM_PC
  not not_8 (not_8_out, MemWrite_MEM);
  RAM #(.addrWidth(10), .dataWidth(32), .bus("separate")) ram_1 (
    .addr(ALUresult_MEM[11:2]), .din(ex_mem_1_rout), .data(ram_1_data), .str(MemWrite_MEM), .clk(CLK),
    .ld(not_8_out), .clr(RST));  // open: sel
  MEM_WB MEM_WB (
    .RegDst_in(RegDst_MEM), .JAL_in(JAL_MEM), .RegWrite_in(RegWrite_MEM), .MemToReg_in(MemToReg_MEM),
    .IRin(IR_MEM), .PCin(MEM_PC), .ALUresult_in(ALUresult_MEM), .MemData_in(ram_1_data),
    .RegDst_out(RegDst_WB), .JAL_out(JAL_WB), .RegWrite_out(RegWrite_WB), .MemToReg_out(MemToReg_WB),
    .IRout(IR_WB), .PCout(PC_WB), .ALUresult_out(ALU_result_WB), .MemData_out(MEM_WB_memdata_out),
    .enable(ex_mem_1_enable_out), .clk(CLK), .clear(RST), .enable_out(pcable_out), .Rt_out(Rt_WB),
    .Rd_out(Rd_WB), .Rt_in(Rt_MEM), .Rd_in(Rd_MEM), .syscall_in(ex_mem_1_syscall_out),
    .syscall_out(syscall_WB), .byteorword_in(byteorword_MEM), .byteorword_out(byteorword_WB));
  Adder #(.width(32)) adder_4 (.a(PC_WB), .b(32'h4), .out(JAL_WB_Addr));  // open: cin, cout
  // Probe on ALU_result_WB
  Shifter #(.width(32), .shift("lr")) shifter_2 (
    .in(MEM_WB_memdata_out), .\dist ({ALU_result_WB[1:0], 3'b000}), .out(shifter_2_out));
  assign and_9_out = shifter_2_out & 32'hff;  // AND_Gate and_9, 32 bits wide
  Multiplexer #(.width(32), .enable("false")) multiplexer_19 (
    .in0(MEM_WB_memdata_out), .in1(and_9_out), .out(MemData_WB), .sel(byteorword_WB));

  // Other names for the same wires on the sheet: IR_ID[5:0] = Func_ID; J_JAL_imm_ID[25:0] = {IR_ID[25:6], Func_ID};
  //   Rd_ID[4:0] = IR_ID[15:11]; OP_ID[5:0] = IR_ID[31:26]; J_JAL_imm_EX[25:0] = J_JAL_addr_EX[27:2];
  //   Rt_ID[4:0] = IR_ID[20:16]; PC_EX[31:0] = EX_PC; PC_ID[31:0] = ID_PC; PC_MEM[31:0] = MEM_PC; WB_PC[31:0] = PC_WB

  // Notes on the sheet:
  //   中断源
  //   中断等待指示
  //   数码管输出
  //   流水调试日志用
  //   指令存储器
  //   contents of rom_1 (hex, n*v repeats v):
  //   20110001 8100005 20110001 20120002 20130003 8100009 20110001 20120002 20130003 810000d 20110001
  //   20120002 20130003 8100011 20110001 20120002 20130003 c1000f8 20100001 20110001 118fc0 112020
  //   20020022 c 118882 12200001 8100015 112020 20020022 c 20110001 118880 112020 20020022 c 12200001
  //   810001f 20110001 118fc0 112020 20020022 c 1188c3 112020 20020022 c 118903 112020 20020022 c 118903
  //   112020 20020022 c 118903 112020 20020022 c 118903 112020 20020022 c 118903 112020 20020022 c 118903
  //   112020 20020022 c 118903 112020 20020022 c 20100001 109fc0 139fc3 8021 2012000c 24160003 26100001
  //   3210000f 20080008 20090001 139900 2709825 132020 20020022 c 1094022 1500fff9 22100001 2018000f
  //   2188024 108700 20080008 20090001 139902 2709825 132021 20020022 c 1094022 1500fff9 108702 2c9b022
  //   12c00001 8100050 4020 1084027 84400 3508ffff 82021 20020022 c 2010ffff 20110000 ae300000 22100001
  //   22310004 ae300000 22100001 22310004 ae300000 22100001 22310004 ae300000 22100001 22310004 ae300000
  //   22100001 22310004 ae300000 22100001 22310004 ae300000 22100001 22310004 ae300000 22100001 22310004
  //   ae300000 22100001 22310004 ae300000 22100001 22310004 ae300000 22100001 22310004 ae300000 22100001
  //   22310004 ae300000 22100001 22310004 ae300000 22100001 22310004 ae300000 22100001 22310004 ae300000
  //   22100001 22310004 22100001 8020 2011003c 8e130000 8e340000 274402a 11000002 ae330000 ae140000
  //   2231fffc 1611fff8 102020 20020022 c 22100004 2011003c 1611fff2 20020032 c 20080001 20090003 20110876
  //   112020 20020022 c 200b0008 1118804 1318804 112020 20020022 c 216bffff 1560fff9 2002000a c 2008ffff
  //   20117777 112020 20020022 c 200b0010 3a31ffff 112020 20020022 c 216bffff 1560fffa 2002000a c 20090000
  //   200b0010 34118483 20120404 118c00 129400 36318281 22520404 ad310000 2328820 21290004 216bffff
  //   1560fffb 200b0020 20090000 91310000 112020 20020022 c 21290001 216bffff 1560fff9 2002000a c 2011fff1
  //   112020 20020022 c 22310001 620fffb 2002000a c 2002000a c 20100000 22100001 102020 20020022 c
  //   22100002 102020 20020022 c 22100003 102020 20020022 c 22100004 102020 20020022 c 22100005 102020
  //   20020022 c 22100006 102020 20020022 c 22100007 102020 20020022 c 22100008 102020 20020022 20020022 c
  //   3e00008
  //   OP
  //   func
  //   rs
  //   rt
  //   rd
  //   数据寄存器
endmodule

// data_bypass
module \重定向数据检测  (
  input  [5:0] OP,
  input  [4:0] EX_WriteReg_num,
  input  EX_RegWrite,
  input  EX_MemToReg,
  input  [4:0] MEM_WriteReg_num,
  input  MEM_RegWrite,
  input  MEM_MemToReg,
  input  [5:0] Func,
  input  [4:0] ID_R1_num,
  input  [4:0] ID_R2_num,
  output [1:0] forwardA,
  output load_use,
  output [1:0] forwardB
);

  wire comparator_1_eq, comparator_2_eq, comparator_3_eq, comparator_4_eq, comparator_5_eq, comparator_6_eq,
       Mem_R1_MemData, not_1_out, not_2_out, R1_Ex_data_related, R1_loaduse, R1_MEM_data_related, R1_used,
       R2_EX_data_related, R2_loaduse, R2_MEM_data_related, R2_MEM_MemData, R2_used;
  wire [1:0] multiplexer_1_out, multiplexer_2_out, multiplexer_3_out, multiplexer_4_out;

  \源寄存器使用情况  \u_源寄存器使用情况_1  (
    .OP0(OP[0]), .OP1(OP[1]), .OP2(OP[2]), .OP3(OP[3]), .OP4(OP[4]), .OP5(OP[5]), .F0(Func[0]), .F1(Func[1]),
    .F2(Func[2]), .F3(Func[3]), .F4(Func[4]), .F5(Func[5]), .R1_Used(R1_used), .R2_Used(R2_used));
  Comparator #(.width(5)) comparator_1 (.a(ID_R1_num), .b({5{1'b0}}), .eq(comparator_1_eq));  // open: gt, lt
  not not_1 (not_1_out, comparator_1_eq);
  Comparator #(.width(5)) comparator_2 (.a(ID_R2_num), .b(EX_WriteReg_num), .eq(comparator_2_eq));  // open: gt, lt
  Comparator #(.width(5)) comparator_3 (.a(ID_R2_num), .b({5{1'b0}}), .eq(comparator_3_eq));  // open: gt, lt
  Comparator #(.width(5)) comparator_4 (.a(ID_R1_num), .b(EX_WriteReg_num), .eq(comparator_4_eq));  // open: gt, lt
  Comparator #(.width(5)) comparator_5 (.a(MEM_WriteReg_num), .b(ID_R1_num), .eq(comparator_5_eq));  // open: gt, lt
  not not_2 (not_2_out, comparator_3_eq);
  Comparator #(.width(5)) comparator_6 (.a(MEM_WriteReg_num), .b(ID_R2_num), .eq(comparator_6_eq));  // open: gt, lt
  and and_1 (R2_EX_data_related, comparator_2_eq, EX_RegWrite, not_2_out, R2_used);
  and and_2 (R2_MEM_data_related, R2_used, not_2_out, MEM_RegWrite, comparator_6_eq);
  and and_3 (R1_Ex_data_related, comparator_4_eq, EX_RegWrite, not_1_out, R1_used);
  and and_4 (R1_MEM_data_related, R1_used, not_1_out, MEM_RegWrite, comparator_5_eq);
  and and_5 (R2_loaduse, R2_EX_data_related, EX_MemToReg);
  and and_6 (R2_MEM_MemData, R2_MEM_data_related, MEM_MemToReg);
  and and_7 (R1_loaduse, R1_Ex_data_related, EX_MemToReg);
  and and_8 (Mem_R1_MemData, MEM_MemToReg, R1_MEM_data_related);
  Multiplexer #(.width(2), .enable("false")) multiplexer_1 (
    .in0(2'b00), .in1(2'b10), .out(multiplexer_1_out), .sel(R2_MEM_data_related));
  Multiplexer #(.width(2), .enable("false")) multiplexer_2 (
    .in0(2'b00), .in1(2'b10), .out(multiplexer_2_out), .sel(R1_MEM_data_related));
  Multiplexer #(.width(2), .enable("false")) multiplexer_3 (
    .in0(multiplexer_1_out), .in1(2'b01), .out(multiplexer_3_out), .sel(R2_MEM_MemData));
  Multiplexer #(.width(2), .enable("false")) multiplexer_4 (
    .in0(multiplexer_2_out), .in1(2'b01), .out(multiplexer_4_out), .sel(Mem_R1_MemData));
  or or_1 (load_use, R1_loaduse, R2_loaduse);
  Multiplexer #(.width(2), .enable("false")) multiplexer_5 (
    .in0(multiplexer_3_out), .in1(2'b11), .out(forwardB), .sel(R2_EX_data_related));
  Multiplexer #(.width(2), .enable("false")) multiplexer_6 (
    .in0(multiplexer_4_out), .in1(2'b11), .out(forwardA), .sel(R1_Ex_data_related));

  // Other names for the same wires on the sheet: OP_CODE[5:0] = OP
endmodule

// hc
module \分支预测历史位状态机  (
  input  h1,
  input  h0,
  input  branch,
  output h1_new,
  output h0_new
);

  wire and_1_out, and_2_out, and_3_out, and_4_out, not_1_out, not_2_out, not_3_out, not_4_out, not_5_out;

  not not_1 (not_1_out, h0);
  not not_2 (not_2_out, h1);
  not not_3 (not_3_out, h0);
  not not_4 (not_4_out, h0);
  not not_5 (not_5_out, branch);
  and and_1 (and_1_out, h0, branch);
  and and_2 (and_2_out, h1, not_1_out);
  and and_3 (and_3_out, not_2_out, not_3_out, branch);
  and and_4 (and_4_out, h1, not_4_out, not_5_out);
  or or_1 (h1_new, and_1_out, and_2_out);
  or or_2 (h0_new, and_3_out, and_4_out);
endmodule

module BHT (
  input  branch_success_EX,
  input  Enable,
  input  [31:0] PC_IF,
  input  Miss_EX,
  input  [31:0] branchaddr_EX,
  input  [31:0] PC_EX,
  input  branch_EX,
  input  CLK,
  output Miss,
  output [1:0] predict_IF,
  output [31:0] predictaddr_IF
);

  wire and_2_out, clear_tong0, clear_tong1, clear_tong2, clear_tong3, clear_tong4, clear_tong5, clear_tong6,
       clear_tong7, comparator_1_eq, comparator_2_eq, comparator_3_eq, comparator_4_eq, comparator_5_eq,
       comparator_6_eq, comparator_7_eq, comparator_8_eq, decoder_1_out0, decoder_1_out1, decoder_1_out2,
       decoder_1_out3, decoder_1_out4, decoder_1_out5, decoder_1_out6, decoder_1_out7, full, hit0_IF,
       hit1_IF, hit2_IF, hit3_IF, hit4_IF, hit5_IF, hit6_IF, hit7_IF, hit_IF, max3_1_p7, max3_1_p8,
       max3_2_p2, max3_2_p3, max3_2_p4, max3_3_p6, max3_4_p5, max3_4_p6, max3_5_p3, max3_5_p4, max3_6_p5,
       max3_6_p6, not_2_out, not_3_out, not_4_out, not_5_out, not_6_out, not_7_out, not_8_out, not_9_out,
       valid0, valid1, valid2, valid3, valid4, valid5, valid6, valid7, w0, w1, w2, w3, w4, w5, w6, w7;
  wire [1:0] history0_q, history1_q, history2_q, history3_q, history4_q, history5_q, history6_q, history7_q,
       multiplexer_2_out, multiplexer_3_out, multiplexer_4_out, multiplexer_5_out, multiplexer_6_out,
       multiplexer_7_out, multiplexer_8_out, multiplexer_9_out, \分支预测历史位状态机_1_h0_new , \分支预测历史位状态机_2_h0_new ,
       \分支预测历史位状态机_3_h0_new , \分支预测历史位状态机_4_h0_new , \分支预测历史位状态机_5_h0_new , \分支预测历史位状态机_6_h0_new ,
       \分支预测历史位状态机_7_h0_new , \分支预测历史位状态机_8_h0_new ;
  wire [2:0] main_1_p7, max3_7_p5, multiplexer_1_out;
  wire [15:0] time0, time1, time2, time3, time4, time5, time6, time7;
  wire [31:0] branchaddr0_q, branchaddr1_q, branchaddr2_q, branchaddr3_q, branchaddr4_q, branchaddr5_q,
       branchaddr6_q, branchaddr7_q, PC0_q, PC1_q, PC2_q, PC3_q, PC4_q, PC5_q, PC6_q, PC7_q, valid_2_q,
       valid_q;

  Register #(.width(1)) u_valid0 (.D(1'b1), .en(w0), .Q(valid0), .clk(CLK));  // open: clr
  Register #(.width(1)) u_valid1 (.D(1'b1), .en(w1), .Q(valid1), .clk(CLK));  // open: clr
  Register #(.width(1)) u_valid2 (.D(1'b1), .en(w2), .Q(valid2), .clk(CLK));  // open: clr
  Register #(.width(1)) u_valid3 (.D(1'b1), .en(w3), .Q(valid3), .clk(CLK));  // open: clr
  Register #(.width(1)) u_valid4 (.D(1'b1), .en(w4), .Q(valid4), .clk(CLK));  // open: clr
  Register #(.width(1)) u_valid5 (.D(1'b1), .en(w5), .Q(valid5), .clk(CLK));  // open: clr
  Register #(.width(1)) u_valid6 (.D(1'b1), .en(w6), .Q(valid6), .clk(CLK));  // open: clr
  Register #(.width(1)) u_valid7 (.D(1'b1), .en(w7), .Q(valid7), .clk(CLK));  // open: clr
  // unfull_main main_1: pin names not known; wires that end beside it: valid0, valid1, valid2, valid3, valid4, valid5, main_1_p7[0], main_1_p7[1], main_1_p7[2]
  // Max3 max3_1: pin names not known; wires that end beside it: valid6, valid7, time0, 3'b000, time1, 3'b001, max3_1_p7, max3_1_p8, max3_1_p7
  // Max3 max3_2: pin names not known; wires that end beside it: max3_1_p8, max3_2_p2, max3_2_p3, max3_2_p4
  // Max3 max3_3: pin names not known; wires that end beside it: time2, 3'b010, time3, 3'b011, max3_2_p2, max3_3_p6, max3_3_p6
  // Max3 max3_4: pin names not known; wires that end beside it: time4, 3'b100, time5, 3'b101, max3_4_p5, max3_4_p6
  // Max3 max3_5: pin names not known; wires that end beside it: max3_4_p5, max3_4_p6, max3_5_p3, max3_5_p4
  // Max3 max3_6: pin names not known; wires that end beside it: time6, 3'b110, time7, 3'b111, max3_6_p5, max3_6_p6, max3_6_p5, max3_6_p6
  and and_1 (full, valid0, valid1, valid2, valid3, valid4, valid5, valid6, valid7);
  // Max3 max3_7: pin names not known; wires that end beside it: max3_2_p3, max3_2_p4, max3_5_p3, max3_5_p4, max3_7_p5
  Multiplexer #(.width(3), .enable("false")) multiplexer_1 (
    .in0(main_1_p7), .in1(max3_7_p5), .out(multiplexer_1_out), .sel(full));
  // Probe on max3_7_p5
  Register #(.width(32)) PC0 (.D(PC_EX), .en(w0), .Q(PC0_q), .clk(CLK));  // open: clr
  // Probe on PC0_q
  Register #(.width(32)) PC1 (.D(PC_EX), .en(w1), .Q(PC1_q), .clk(CLK));  // open: clr
  // Probe on PC1_q
  Register #(.width(32)) PC2 (.D(PC_EX), .en(w2), .Q(PC2_q), .clk(CLK));  // open: clr
  // Probe on PC2_q
  Register #(.width(32)) PC3 (.D(PC_EX), .en(w3), .Q(PC3_q), .clk(CLK));  // open: clr
  // Probe on PC3_q
  Register #(.width(32)) PC4 (.D(PC_EX), .en(w4), .Q(PC4_q), .clk(CLK));  // open: clr
  // Probe on PC4_q
  Register #(.width(32)) PC5 (.D(PC_EX), .en(w5), .Q(PC5_q), .clk(CLK));  // open: clr
  // Probe on PC5_q
  Register #(.width(32)) PC6 (.D(PC_EX), .en(w6), .Q(PC6_q), .clk(CLK));  // open: clr
  // Probe on PC6_q
  Register #(.width(32)) PC7 (.D(PC_EX), .en(w7), .Q(PC7_q), .clk(CLK));  // open: clr
  // Probe on PC7_q
  Decoder #(.select(3), .enable("false")) decoder_1 (
    .out0(decoder_1_out0), .out1(decoder_1_out1), .out2(decoder_1_out2), .out3(decoder_1_out3),
    .out4(decoder_1_out4), .out5(decoder_1_out5), .out6(decoder_1_out6), .out7(decoder_1_out7),
    .sel(multiplexer_1_out));
  and and_2 (and_2_out, branch_EX, Miss_EX, Enable, branch_success_EX);
  nor nor_1 (Miss, hit0_IF, hit1_IF, hit2_IF, hit3_IF, hit4_IF, hit5_IF, hit6_IF, hit7_IF);
  not not_1 (hit_IF, Miss);
  and and_3 (w7, and_2_out, decoder_1_out7);
  and and_4 (w6, and_2_out, decoder_1_out6);
  // Probe on PC_IF
  Comparator #(.width(32)) comparator_1 (.a(PC0_q), .b(PC_IF), .eq(comparator_1_eq));  // open: gt, lt
  Comparator #(.width(32)) comparator_2 (.a(PC1_q), .b(PC_IF), .eq(comparator_2_eq));  // open: gt, lt
  Comparator #(.width(32)) comparator_3 (.a(PC2_q), .b(PC_IF), .eq(comparator_3_eq));  // open: gt, lt
  Comparator #(.width(32)) comparator_4 (.a(PC3_q), .b(PC_IF), .eq(comparator_4_eq));  // open: gt, lt
  Comparator #(.width(32)) comparator_5 (.a(PC4_q), .b(PC_IF), .eq(comparator_5_eq));  // open: gt, lt
  Comparator #(.width(32)) comparator_6 (.a(PC5_q), .b(PC_IF), .eq(comparator_6_eq));  // open: gt, lt
  Comparator #(.width(32)) comparator_7 (.a(PC6_q), .b(PC_IF), .eq(comparator_7_eq));  // open: gt, lt
  Comparator #(.width(32)) comparator_8 (.a(PC7_q), .b(PC_IF), .eq(comparator_8_eq));  // open: gt, lt
  and and_5 (w4, and_2_out, decoder_1_out4);
  and and_6 (w5, and_2_out, decoder_1_out5);
  Register #(.width(32)) valid (.D(PC_IF), .Q(valid_q), .clk(CLK));  // open: en, clr
  and and_7 (hit0_IF, valid0, comparator_1_eq);
  and and_8 (hit1_IF, valid1, comparator_2_eq);
  and and_9 (hit2_IF, valid2, comparator_3_eq);
  and and_10 (hit3_IF, valid3, comparator_4_eq);
  and and_11 (hit4_IF, valid4, comparator_5_eq);
  and and_12 (hit5_IF, valid5, comparator_6_eq);
  and and_13 (hit6_IF, valid6, comparator_7_eq);
  and and_14 (hit7_IF, valid7, comparator_8_eq);
  and and_15 (w3, and_2_out, decoder_1_out3);
  and and_16 (w2, and_2_out, decoder_1_out2);
  or or_1 (clear_tong0, w0, hit0_IF);
  or or_2 (clear_tong1, w1, hit1_IF);
  or or_3 (clear_tong2, w2, hit2_IF);
  or or_4 (clear_tong3, w3, hit3_IF);
  or or_5 (clear_tong4, w4, hit4_IF);
  or or_6 (clear_tong5, w5, hit5_IF);
  or or_7 (clear_tong6, w6, hit6_IF);
  or or_8 (clear_tong7, w7, hit7_IF);
  Register #(.width(32)) valid_2 (.D(valid_q), .Q(valid_2_q), .clk(CLK));  // open: en, clr
  and and_17 (w1, and_2_out, decoder_1_out1);
  and and_18 (w0, and_2_out, decoder_1_out0);
  // Probe on valid_2_q
  not not_2 (not_2_out, clear_tong0);
  not not_3 (not_3_out, clear_tong1);
  not not_4 (not_4_out, clear_tong2);
  not not_5 (not_5_out, clear_tong3);
  not not_6 (not_6_out, clear_tong4);
  not not_7 (not_7_out, clear_tong5);
  not not_8 (not_8_out, clear_tong6);
  not not_9 (not_9_out, clear_tong7);
  // Probe on time0
  Counter #(.width(16), .max('hffff)) u_time0 (
    .load(clear_tong0), .D({16{1'b0}}), .count(not_2_out), .Q(time0), .clk(CLK));  // open: carry, clr
  // Probe on time1
  Counter #(.width(16), .max('hffff)) u_time1 (
    .load(clear_tong1), .D({16{1'b0}}), .count(not_3_out), .Q(time1), .clk(CLK));  // open: carry, clr
  // Probe on time2
  Counter #(.width(16), .max('hffff)) u_time2 (
    .load(clear_tong2), .D({16{1'b0}}), .count(not_4_out), .Q(time2), .clk(CLK));  // open: carry, clr
  // Probe on time3
  Counter #(.width(16), .max('hffff)) u_time3 (
    .load(clear_tong3), .D({16{1'b0}}), .count(not_5_out), .Q(time3), .clk(CLK));  // open: carry, clr
  // Probe on time4
  Counter #(.width(16), .max('hffff)) u_time4 (
    .load(clear_tong4), .D({16{1'b0}}), .count(not_6_out), .Q(time4), .clk(CLK));  // open: carry, clr
  // Probe on time5
  Counter #(.width(16), .max('hffff)) u_time5 (
    .load(clear_tong5), .D({16{1'b0}}), .count(not_7_out), .Q(time5), .clk(CLK));  // open: carry, clr
  // Probe on time6
  Counter #(.width(16), .max('hffff)) u_time6 (
    .load(clear_tong6), .D({16{1'b0}}), .count(not_8_out), .Q(time6), .clk(CLK));  // open: carry, clr
  // Probe on time7
  Counter #(.width(16), .max('hffff)) u_time7 (
    .load(clear_tong7), .D({16{1'b0}}), .count(not_9_out), .Q(time7), .clk(CLK));  // open: carry, clr
  Register #(.width(32)) branchaddr0 (.D(branchaddr_EX), .en(w0), .Q(branchaddr0_q), .clk(CLK));  // open: clr
  assign predictaddr_IF = hit0_IF ? branchaddr0_q : 32'bz;  // Controlled_Buffer controlled_buffer_1
  assign predictaddr_IF = hit1_IF ? branchaddr1_q : 32'bz;  // Controlled_Buffer controlled_buffer_2
  Register #(.width(32)) branchaddr1 (.D(branchaddr_EX), .en(w1), .Q(branchaddr1_q), .clk(CLK));  // open: clr
  assign predictaddr_IF = hit2_IF ? branchaddr2_q : 32'bz;  // Controlled_Buffer controlled_buffer_3
  Register #(.width(32)) branchaddr2 (.D(branchaddr_EX), .en(w2), .Q(branchaddr2_q), .clk(CLK));  // open: clr
  assign predictaddr_IF = hit3_IF ? branchaddr3_q : 32'bz;  // Controlled_Buffer controlled_buffer_4
  Register #(.width(32)) branchaddr3 (.D(branchaddr_EX), .en(w3), .Q(branchaddr3_q), .clk(CLK));  // open: clr
  Register #(.width(32)) branchaddr4 (.D(branchaddr_EX), .en(w4), .Q(branchaddr4_q), .clk(CLK));  // open: clr
  assign predictaddr_IF = hit4_IF ? branchaddr4_q : 32'bz;  // Controlled_Buffer controlled_buffer_5
  assign predictaddr_IF = hit5_IF ? branchaddr5_q : 32'bz;  // Controlled_Buffer controlled_buffer_6
  Register #(.width(32)) branchaddr5 (.D(branchaddr_EX), .en(w5), .Q(branchaddr5_q), .clk(CLK));  // open: clr
  assign predictaddr_IF = hit6_IF ? branchaddr6_q : 32'bz;  // Controlled_Buffer controlled_buffer_7
  Register #(.width(32)) branchaddr6 (.D(branchaddr_EX), .en(w6), .Q(branchaddr6_q), .clk(CLK));  // open: clr
  assign predictaddr_IF = hit7_IF ? branchaddr7_q : 32'bz;  // Controlled_Buffer controlled_buffer_8
  Register #(.width(32)) branchaddr7 (.D(branchaddr_EX), .en(w7), .Q(branchaddr7_q), .clk(CLK));  // open: clr
  // Probe on branchaddr_EX
  Register #(.width(2)) history0 (.D(multiplexer_2_out), .en(branch_EX), .Q(history0_q), .clk(CLK));  // open: clr
  Multiplexer #(.width(2), .enable("false")) multiplexer_2 (
    .in0(\分支预测历史位状态机_1_h0_new ), .in1(2'b00), .out(multiplexer_2_out), .sel(w0));
  Multiplexer #(.width(2), .enable("false")) multiplexer_3 (
    .in0(\分支预测历史位状态机_2_h0_new ), .in1(2'b00), .out(multiplexer_3_out), .sel(w1));
  Register #(.width(2)) history1 (.D(multiplexer_3_out), .en(branch_EX), .Q(history1_q), .clk(CLK));  // open: clr
  Register #(.width(2)) history2 (.D(multiplexer_4_out), .en(branch_EX), .Q(history2_q), .clk(CLK));  // open: clr
  Multiplexer #(.width(2), .enable("false")) multiplexer_4 (
    .in0(\分支预测历史位状态机_3_h0_new ), .in1(2'b00), .out(multiplexer_4_out), .sel(w2));
  Multiplexer #(.width(2), .enable("false")) multiplexer_5 (
    .in0(\分支预测历史位状态机_4_h0_new ), .in1(2'b00), .out(multiplexer_5_out), .sel(w3));
  Register #(.width(2)) history3 (.D(multiplexer_5_out), .en(branch_EX), .Q(history3_q), .clk(CLK));  // open: clr
  Register #(.width(2)) history4 (.D(multiplexer_6_out), .en(branch_EX), .Q(history4_q), .clk(CLK));  // open: clr
  Multiplexer #(.width(2), .enable("false")) multiplexer_6 (
    .in0(\分支预测历史位状态机_5_h0_new ), .in1(2'b00), .out(multiplexer_6_out), .sel(w4));
  Multiplexer #(.width(2), .enable("false")) multiplexer_7 (
    .in0(\分支预测历史位状态机_6_h0_new ), .in1(2'b00), .out(multiplexer_7_out), .sel(w5));
  Register #(.width(2)) history5 (.D(multiplexer_7_out), .en(branch_EX), .Q(history5_q), .clk(CLK));  // open: clr
  Register #(.width(2)) history6 (.D(multiplexer_8_out), .en(branch_EX), .Q(history6_q), .clk(CLK));  // open: clr
  Multiplexer #(.width(2), .enable("false")) multiplexer_8 (
    .in0(\分支预测历史位状态机_7_h0_new ), .in1(2'b00), .out(multiplexer_8_out), .sel(w6));
  Multiplexer #(.width(2), .enable("false")) multiplexer_9 (
    .in0(\分支预测历史位状态机_8_h0_new ), .in1(2'b00), .out(multiplexer_9_out), .sel(w7));
  Register #(.width(2)) history7 (.D(multiplexer_9_out), .en(branch_EX), .Q(history7_q), .clk(CLK));  // open: clr
  \分支预测历史位状态机  \u_分支预测历史位状态机_1  (
    .h1(history0_q[1]), .h0(history0_q[0]), .branch(branch_success_EX), .h1_new(\分支预测历史位状态机_1_h0_new [1]),
    .h0_new(\分支预测历史位状态机_1_h0_new [0]));
  \分支预测历史位状态机  \u_分支预测历史位状态机_2  (
    .h1(history1_q[1]), .h0(history1_q[0]), .branch(branch_success_EX), .h1_new(\分支预测历史位状态机_2_h0_new [1]),
    .h0_new(\分支预测历史位状态机_2_h0_new [0]));
  \分支预测历史位状态机  \u_分支预测历史位状态机_3  (
    .h1(history2_q[1]), .h0(history2_q[0]), .branch(branch_success_EX), .h1_new(\分支预测历史位状态机_3_h0_new [1]),
    .h0_new(\分支预测历史位状态机_3_h0_new [0]));
  \分支预测历史位状态机  \u_分支预测历史位状态机_4  (
    .h1(history3_q[1]), .h0(history3_q[0]), .branch(branch_success_EX), .h1_new(\分支预测历史位状态机_4_h0_new [1]),
    .h0_new(\分支预测历史位状态机_4_h0_new [0]));
  \分支预测历史位状态机  \u_分支预测历史位状态机_5  (
    .h1(history4_q[1]), .h0(history4_q[0]), .branch(branch_success_EX), .h1_new(\分支预测历史位状态机_5_h0_new [1]),
    .h0_new(\分支预测历史位状态机_5_h0_new [0]));
  \分支预测历史位状态机  \u_分支预测历史位状态机_6  (
    .h1(history5_q[1]), .h0(history5_q[0]), .branch(branch_success_EX), .h1_new(\分支预测历史位状态机_6_h0_new [1]),
    .h0_new(\分支预测历史位状态机_6_h0_new [0]));
  \分支预测历史位状态机  \u_分支预测历史位状态机_7  (
    .h1(history6_q[1]), .h0(history6_q[0]), .branch(branch_success_EX), .h1_new(\分支预测历史位状态机_7_h0_new [1]),
    .h0_new(\分支预测历史位状态机_7_h0_new [0]));
  \分支预测历史位状态机  \u_分支预测历史位状态机_8  (
    .h1(history7_q[1]), .h0(history7_q[0]), .branch(branch_success_EX), .h1_new(\分支预测历史位状态机_8_h0_new [1]),
    .h0_new(\分支预测历史位状态机_8_h0_new [0]));
  assign predict_IF = hit0_IF ? history0_q : 2'bz;  // Controlled_Buffer controlled_buffer_9
  assign predict_IF = hit1_IF ? history1_q : 2'bz;  // Controlled_Buffer controlled_buffer_10
  assign predict_IF = hit2_IF ? history2_q : 2'bz;  // Controlled_Buffer controlled_buffer_11
  assign predict_IF = hit3_IF ? history3_q : 2'bz;  // Controlled_Buffer controlled_buffer_12
  assign predict_IF = hit4_IF ? history4_q : 2'bz;  // Controlled_Buffer controlled_buffer_13
  assign predict_IF = hit5_IF ? history5_q : 2'bz;  // Controlled_Buffer controlled_buffer_14
  assign predict_IF = hit6_IF ? history6_q : 2'bz;  // Controlled_Buffer controlled_buffer_15
  assign predict_IF = hit7_IF ? history7_q : 2'bz;  // Controlled_Buffer controlled_buffer_16
  // Probe on predict_IF

  // Other names for the same wires on the sheet: DataOut[31:0] = predictaddr_IF; En = Enable; Miss_IF = Miss

  // Notes on the sheet:
  //   请勿增改引脚，请勿修改子电路封装
  //   电路功能：利用上面给定的隧道构建8行的Cache，cache映射方式自选
  //   输入引脚区
  //   68
  //   不论满还是不满
  //   载入数据的cache行号
  //   请在下方利用上方输入输出引脚的隧道信号构建电路，ctrl+d复制选择部件
  //   输出引脚区
endmodule

module \动态分支预测  (
);

  wire ALU_src_EX, ALU_src_ID, and_1_out, and_2_out, and_3_out, and_5_out, and_6_out, and_8_out, and_11_out,
       and_12_out, and_13_out, Beq_EX, Beq_ID, bltz_EX, bltz_ID, Bne_EX, Bne_ID, branch_EX, branchsuccess_EX,
       byteorword_EX, byteorword_ID, byteorword_MEM, byteorword_WB, CLK, comparator_2_eq, comparator_3_lt,
       condbranch_EX, data_related, display_EX, ex_mem_1_enable_out, ex_mem_1_syscall_out, Go,
       id_ex_1_enable_out, IR1, IR2, IR3, JAL_EX, JAL_ID, JAL_MEM, JAL_WB, JMP_EX, JMP_ID, JR_EX, JR_ID,
       loaduse_ID, MemToReg_EX, MemToReg_ID, MemToReg_MEM, MemToReg_WB, MemWrite_EX, MemWrite_ID,
       MemWrite_MEM, mips_alu_1_equal, Miss_EX, Miss_ID, Miss_IF, not_1_out, not_2_out, not_3_out, not_4_out,
       not_5_out, not_7_out, not_8_out, not_10_out, not_11_out, not_12_out, or_3_out, or_4_out, or_5_out,
       pause_EX, pcable, pcable_out, predict_branch_EX, predict_branch_ID, predict_fail_EX,
       predict_success_EX, predictbranch_IF, RegDst_EX, RegDst_ID, RegDst_MEM, RegDst_WB, RegWrite_EX,
       RegWrite_ID, RegWrite_MEM, RegWrite_WB, RST, shamtsrc_EX, shamtsrc_ID, SignedExt_ID, syscall_EX,
       syscall_ID, syscall_WB, W1, W2, W3, xor_1_out, \清零 ;
  wire [1:0] forwardA_EX, forwardA_ID, forwardB_EX, forwardB_ID, predict_IF;
  wire [3:0] ALU_op_EX, ALU_op_ID;
  wire [4:0] id_ex_1_shamt_out, multiplexer_4_out, multiplexer_5_out, multiplexer_6_out, multiplexer_7_out,
       multiplexer_13_out, multiplexer_14_out, multiplexer_20_out, R1__ID, R2__ID, Rd_EX, Rd_MEM, Rd_WB,
       Rt_EX, Rt_MEM, Rt_WB;
  wire [5:0] Func_ID;
  wire [15:0] \LoadUse次数 , \总周期数 , \插入气泡数 , \无条件分支数 , \条件分支成功数 ;
  wire [27:0] adder_3_out;
  wire [31:0] adder_1_out, ALU_result_WB, ALUresult_MEM, and_14_out, beqbneaddr_EX, bit_extender_1_out,
       bit_extender_2_out, branchaddr_EX, ex_mem_1_rout, EX_PC, ID_PC, IF_PC, Imm_EX, IR_EX, IR_MEM, IR_WB,
       JAL_WB_Addr, LedData, MEM_PC, MEM_WB_memdata_out, MemData_WB, mips_alu_1_result, multiplexer_1_out,
       multiplexer_2_out, multiplexer_8_out, multiplexer_9_out, multiplexer_10_out, multiplexer_15_out,
       multiplexer_16_out, multiplexer_19_out, PC_IF_4, PC_WB, predictaddr_IF, R1_EX, R1_first_use, R1_ID,
       R2_EX, R2_first_use, R2_ID, ram_1_data, rom_1_data, shifter_1_out, shifter_2_out;
  wire [31:2] J_JAL_addr_EX;
  wire [31:6] IR_ID;

  Button \u_总复位  (.out(RST));
  Button _1 (.out(IR1));
  Button _2 (.out(IR2));
  Button _3 (.out(IR3));
  Button \u_继续运行  (.out(Go));
  LED led_1 (.in(W1));
  LED led_2 (.in(W2));
  LED led_3 (.in(W3));
  Hex_Digit_Display hex_digit_display_1 (.value(LedData[31:28]));  // open: dp
  Hex_Digit_Display hex_digit_display_2 (.value(LedData[23:20]));  // open: dp
  Hex_Digit_Display hex_digit_display_3 (.value(LedData[27:24]));  // open: dp
  // Probe on {J_JAL_addr_EX, 2'b00}
  Hex_Digit_Display hex_digit_display_4 (.value(LedData[15:12]));  // open: dp
  Hex_Digit_Display hex_digit_display_5 (.value(LedData[19:16]));  // open: dp
  Hex_Digit_Display hex_digit_display_6 (.value(LedData[7:4]));  // open: dp
  Hex_Digit_Display hex_digit_display_7 (.value(LedData[11:8]));  // open: dp
  Clock clock_1 (.out(CLK));
  Multiplexer #(.width(32), .enable("false")) multiplexer_1 (
    .in0(adder_1_out), .in1(beqbneaddr_EX), .out(multiplexer_1_out), .sel(condbranch_EX));
  Multiplexer #(.width(32), .enable("false")) multiplexer_2 (
    .in0({J_JAL_addr_EX, 2'b00}), .in1(R1_first_use), .out(multiplexer_2_out), .sel(JR_EX));
  // Probe on multiplexer_9_out
  or or_1 (branchsuccess_EX, condbranch_EX, JMP_EX);
  Hex_Digit_Display hex_digit_display_8 (.value(LedData[3:0]));  // open: dp
  Multiplexer #(.width(32), .enable("false")) multiplexer_3 (
    .in0(multiplexer_1_out), .in1(multiplexer_2_out), .out(branchaddr_EX), .sel(JMP_EX));
  or or_2 (branch_EX, JMP_EX, Beq_EX, Bne_EX);
  and and_1 (and_1_out, not_1_out, pcable);
  not not_1 (not_1_out, loaduse_ID);
  // Probe on \总周期数 
  // Probe on \无条件分支数 
  // Probe on \条件分支成功数 
  // Probe on \插入气泡数 
  // Probe on \LoadUse次数 
  Multiplexer #(.width(5), .enable("false")) multiplexer_4 (
    .in0(Rt_EX), .in1(Rd_EX), .out(multiplexer_4_out), .sel(RegDst_EX));
  Multiplexer #(.width(5), .enable("false")) multiplexer_5 (
    .in0(Rt_MEM), .in1(Rd_MEM), .out(multiplexer_5_out), .sel(RegDst_MEM));
  // Probe on IF_PC
  Register #(.width(32)) PC (.D(multiplexer_9_out), .en(and_1_out), .Q(IF_PC), .clk(CLK), .clr(RST));
  BHT bht_1 (
    .branch_success_EX(branchsuccess_EX), .Enable(pcable), .PC_IF(IF_PC), .branchaddr_EX(branchaddr_EX),
    .PC_EX(EX_PC), .branch_EX(branch_EX), .CLK(CLK), .Miss(Miss_IF), .predict_IF(predict_IF),
    .predictaddr_IF(predictaddr_IF), .Miss_EX(Miss_EX));
  // Probe on IF_PC[11:0]
  Multiplexer #(.width(5), .enable("false")) multiplexer_6 (
    .in0(multiplexer_4_out), .in1({5{1'b1}}), .out(multiplexer_6_out), .sel(JAL_EX));
  Multiplexer #(.width(5), .enable("false")) multiplexer_7 (
    .in0(multiplexer_5_out), .in1({5{1'b1}}), .out(multiplexer_7_out), .sel(JAL_MEM));
  not not_2 (not_2_out, Miss_IF);
  and and_2 (and_2_out, not_2_out, predictbranch_IF);
  Multiplexer #(.width(32), .enable("false")) multiplexer_8 (
    .in0(PC_IF_4), .in1(predictaddr_IF), .out(multiplexer_8_out), .sel(and_2_out));
  // Probe on ID_PC[11:0]
  and and_3 (and_3_out, predict_fail_EX, not_3_out);
  // Probe on multiplexer_8_out
  // Probe on predictaddr_IF
  Comparator #(.width(2), .mode("unsigned")) comparator_1 (
    .a(predict_IF), .b(2'b01), .gt(predictbranch_IF));  // open: eq, lt
  // Probe on EX_PC[11:0]
  // Probe on MEM_PC[11:0]
  not not_3 (not_3_out, Miss_EX);
  or or_3 (or_3_out, and_3_out, and_5_out);
  and and_4 (\清零 , or_3_out, branch_EX);
  Multiplexer #(.width(32), .enable("false")) multiplexer_9 (
    .in0(multiplexer_8_out), .in1(branchaddr_EX), .out(multiplexer_9_out), .sel(\清零 ));
  // Probe on branchaddr_EX
  // Probe on predict_IF
  // Probe on PC_WB[11:0]
  // Probe on forwardA_ID
  // Probe on forwardB_ID
  \重定向数据检测  \u_重定向数据检测_1  (
    .OP(IR_ID[31:26]), .EX_WriteReg_num(multiplexer_6_out), .EX_RegWrite(RegWrite_EX),
    .EX_MemToReg(MemToReg_EX), .forwardA(forwardA_ID), .MEM_WriteReg_num(multiplexer_7_out),
    .MEM_RegWrite(RegWrite_MEM), .load_use(loaduse_ID), .MEM_MemToReg(MemToReg_MEM), .Func(Func_ID),
    .ID_R1_num(R1__ID), .ID_R2_num(R2__ID), .forwardB(forwardB_ID));
  // Probe on loaduse_ID
  \数据相关检测  \u_数据相关检测_1  (
    .OP(IR_ID[31:26]), .EX_WriteReg_num(multiplexer_6_out), .EX_RegWrite(RegWrite_EX),
    .MEM_WriteReg_num(multiplexer_7_out), .MEM_RegWrite(RegWrite_MEM), .\数据相关 (data_related), .Func(Func_ID),
    .ID_R1_num(R1__ID), .ID_R2_num(R2__ID));
  and and_5 (and_5_out, branchsuccess_EX, Miss_EX);
  ROM #(.addrWidth(10), .dataWidth(32)) rom_1 (.addr(IF_PC[11:2]), .data(rom_1_data));  // open: sel
  // Probe on {IR_ID, Func_ID}
  // Probe on IF_PC
  and and_6 (and_6_out, not_4_out, pcable);
  not not_4 (not_4_out, loaduse_ID);
  IF_ID if_id_1 (
    .IRin(rom_1_data), .PCin(IF_PC), .IRout({IR_ID, Func_ID}), .PCout(ID_PC), .clk(CLK), .enable(and_6_out),
    .clear_tong(\清零 ), .clear_yi(RST), .Miss_in(Miss_IF), .Miss_out(Miss_ID),
    .predict_branch_in(predictbranch_IF), .predict_branch_out(predict_branch_ID));  // open: enable_out
  xor xor_1 (xor_1_out, branchsuccess_EX, predict_branch_EX);
  Register #(.width(32)) register_1 (.D(R2_first_use), .en(display_EX), .Q(LedData), .clk(CLK), .clr(RST));
  not not_5 (not_5_out, Miss_EX);
  and and_7 (predict_fail_EX, xor_1_out, not_5_out);
  Adder #(.width(32)) adder_1 (.a(EX_PC), .b(32'h4), .out(adder_1_out));  // open: cin, cout
  not not_6 (predict_success_EX, predict_fail_EX);
  // Probe on ID_PC[11:0]
  // Probe on ID_PC[11:0]
  assign bit_extender_1_out = {{16{1'b0}}, {IR_ID[15:6], Func_ID}};  // Bit_Extender bit_extender_1
  Multiplexer #(.width(32), .enable("false")) multiplexer_10 (
    .in0(bit_extender_1_out), .in1(bit_extender_2_out), .out(multiplexer_10_out), .sel(SignedExt_ID));
  assign bit_extender_2_out = {{16{IR_ID[15]}}, {IR_ID[15:6], Func_ID}};  // Bit_Extender bit_extender_2
  Adder #(.width(32)) adder_2 (.a(IF_PC), .b(32'h4), .out(PC_IF_4));  // open: cin, cout
  Comparator #(.width(32)) comparator_2 (.a(R1_first_use), .b(32'h22), .eq(comparator_2_eq));  // open: gt, lt
  Multiplexer #(.width(5), .enable("false")) multiplexer_11 (
    .in0(IR_ID[25:21]), .in1(5'b00010), .out(R1__ID), .sel(syscall_ID));
  Multiplexer #(.width(5), .enable("false")) multiplexer_12 (
    .in0(IR_ID[20:16]), .in1(5'b00100), .out(R2__ID), .sel(syscall_ID));
  // Probe on R2__ID
  Multiplexer #(.width(5), .enable("false")) multiplexer_13 (
    .in0(Rt_WB), .in1(Rd_WB), .out(multiplexer_13_out), .sel(RegDst_WB));
  not not_7 (not_7_out, Go);
  not not_8 (not_8_out, comparator_2_eq);
  // newcontrol 扩展指令译码: pin names not known; wires that end beside it: IR_ID[26], IR_ID[27], IR_ID[28], IR_ID[29], IR_ID[30], IR_ID[31], Func_ID[0], Func_ID[1], Func_ID[2], Func_ID[3], Func_ID[4], Func_ID[5], shamtsrc_ID, byteorword_ID, bltz_ID
  \硬布线控制器  \u_硬布线控制器_1  (
    .Func(Func_ID), .OP(IR_ID[31:26]), .ALU_OP(ALU_op_ID), .MemToReg(MemToReg_ID), .MemWrite(MemWrite_ID),
    .ALU_SRC(ALU_src_ID), .RegWrite(RegWrite_ID), .SysCALL(syscall_ID), .SignedExt(SignedExt_ID),
    .RegDst(RegDst_ID), .JR(JR_ID), .JMP(JMP_ID), .Beq(Beq_ID), .JAL(JAL_ID), .Bne(Bne_ID));
  // Probe on {IR_ID[25:6], Func_ID}
  // Probe on R1__ID
  Multiplexer #(.width(5), .enable("false")) multiplexer_14 (
    .in0(multiplexer_13_out), .in1({5{1'b1}}), .out(multiplexer_14_out), .sel(JAL_WB));
  // Probe on multiplexer_14_out
  Multiplexer #(.width(32), .enable("false")) multiplexer_15 (
    .in0(multiplexer_16_out), .in1(JAL_WB_Addr), .out(multiplexer_15_out), .sel(JAL_WB));
  Multiplexer #(.width(32), .enable("false")) multiplexer_16 (
    .in0(ALU_result_WB), .in1(MemData_WB), .out(multiplexer_16_out), .sel(MemToReg_WB));
  not not_9 (pcable, and_8_out);
  and and_8 (and_8_out, not_7_out, pause_EX);
  and and_9 (display_EX, comparator_2_eq, syscall_EX);
  and and_10 (pause_EX, syscall_EX, not_8_out);
  // Probe on {IR_ID[25:6], Func_ID}
  // Probe on multiplexer_15_out
  not not_10 (not_10_out, syscall_WB);
  MIPS_Regifile mips_regifile_1 (
    .Din(multiplexer_15_out), .Clk(CLK), .R1(R1_ID), .R2(R2_ID), .WE(RegWrite_WB),
    .W_num(multiplexer_14_out), .R1_num(R1__ID), .R2_num(R2__ID));
  or or_4 (or_4_out, pcable, not_10_out);
  // Probe on ID_PC
  Counter #(.width(16), .max('hffff)) counter_1 (
    .count(or_4_out), .Q(\总周期数 ), .clk(CLK), .clr(RST));  // open: load, D, carry
  ID_EX id_ex_1 (
    .RegDst_in(RegDst_ID), .JAL_in(JAL_ID), .RegWrite_in(RegWrite_ID), .MemToReg_in(MemToReg_ID),
    .MemWrite_in(MemWrite_ID), .ALU_OP_in(ALU_op_ID), .ALU_src_in(ALU_src_ID), .Bne_in(Bne_ID),
    .Beq_in(Beq_ID), .IRin({IR_ID, Func_ID}), .PCin(ID_PC), .R1in(R1_ID), .R2in(R2_ID),
    .IMMin(multiplexer_10_out), .RegDst_out(RegDst_EX), .JAL_out(JAL_EX), .RegWrite_out(RegWrite_EX),
    .MemToReg_out(MemToReg_EX), .MemWrite_out(MemWrite_EX), .ALU_OP_out(ALU_op_EX), .ALU_src_out(ALU_src_EX),
    .Bne_out(Bne_EX), .Beq_out(Beq_EX), .out_55(IR_EX), .PCout(EX_PC), .R1out(R1_EX), .R2out(R2_EX),
    .IMMout(Imm_EX), .enable(pcable), .clk(CLK), .clear_tong(or_5_out), .shamt_in(IR_ID[10:6]),
    .shamt_out(id_ex_1_shamt_out), .enable_out(id_ex_1_enable_out), .Rd_in(IR_ID[15:11]),
    .Rt_in(IR_ID[20:16]), .Rt_out(Rt_EX), .Rd_out(Rd_EX), .JMP_in(JMP_ID), .JR_in(JR_ID), .JMP_out(JMP_EX),
    .JR_out(JR_EX), .J_JAL_imm_in({IR_ID[25:6], Func_ID}), .J_JAL_imm_out(J_JAL_addr_EX[27:2]),
    .syscall_in(syscall_ID), .syscall_out(syscall_EX), .shamtsrc_in(shamtsrc_ID), .bltz_in(bltz_ID),
    .byteorword_in(byteorword_ID), .shamtsrc_out(shamtsrc_EX), .bltz_out(bltz_EX),
    .byteorword_out(byteorword_EX), .forwardB_in(forwardB_ID), .forwardA_in(forwardA_ID),
    .forwardB_out(forwardB_EX), .forwardA_out(forwardA_EX), .clear_yibu(RST), .Miss_in(Miss_ID),
    .Miss_out(Miss_EX), .predict_branch_in(predict_branch_ID), .predict_branch_out(predict_branch_EX));
  or or_5 (or_5_out, \清零 , loaduse_ID);
  // Probe on EX_PC
  // Probe on J_JAL_addr_EX[27:2]
  // Probe on EX_PC
  Adder #(.width(32)) adder_3 (.a(EX_PC), .b(32'h4), .out({J_JAL_addr_EX[31:28], adder_3_out}));  // open: cin, cout
  Shifter #(.width(32)) shifter_1 (.in(Imm_EX), .\dist (5'b00010), .out(shifter_1_out));
  // Probe on J_JAL_addr_EX[27:2]
  // Probe on J_JAL_addr_EX[27:2]
  Counter #(.width(16), .max('hffff)) counter_2 (
    .count(JMP_EX), .Q(\无条件分支数 ), .clk(CLK), .clr(RST));  // open: load, D, carry
  // Probe on J_JAL_addr_EX[27:2]
  Multiplexer #(.select(2), .width(32), .enable("false")) multiplexer_17 (
    .in0(R2_EX), .in1(MemData_WB), .in2(ALU_result_WB), .in3(ALUresult_MEM), .out(R2_first_use),
    .sel(forwardB_EX));
  Adder #(.width(32)) adder_4 (
    .a({J_JAL_addr_EX[31:28], adder_3_out}), .b(shifter_1_out), .out(beqbneaddr_EX));  // open: cin, cout
  or or_6 (condbranch_EX, and_12_out, and_11_out, and_13_out);
  and and_11 (and_11_out, not_11_out, Bne_EX);
  and and_12 (and_12_out, Beq_EX, mips_alu_1_equal);
  not not_11 (not_11_out, mips_alu_1_equal);
  Multiplexer #(.select(2), .width(32), .enable("false")) multiplexer_18 (
    .in0(R1_EX), .in1(MemData_WB), .in2(ALU_result_WB), .in3(ALUresult_MEM), .out(R1_first_use),
    .sel(forwardA_EX));
  // Probe on R1_first_use
  Multiplexer #(.width(32), .enable("false")) multiplexer_19 (
    .in0(R2_first_use), .in1(Imm_EX), .out(multiplexer_19_out), .sel(ALU_src_EX));
  // Probe on R2_first_use
  // Probe on {J_JAL_addr_EX, 2'b00}
  // Probe on J_JAL_addr_EX[31:28]
  Counter #(.width(16), .max('hffff)) counter_3 (
    .count(condbranch_EX), .Q(\条件分支成功数 ), .clk(CLK), .clr(RST));  // open: load, D, carry
  and and_13 (and_13_out, bltz_EX, comparator_3_lt);
  MIPS_ALU mips_alu_1 (
    .X(R1_first_use), .Y(multiplexer_19_out), .AluOP(ALU_op_EX), .Equal(mips_alu_1_equal),
    .Result(mips_alu_1_result), .shamt(multiplexer_20_out));  // open: Result_2
  // Probe on multiplexer_19_out
  Multiplexer #(.width(5), .enable("false")) multiplexer_20 (
    .in0(id_ex_1_shamt_out), .in1(R1_first_use[4:0]), .out(multiplexer_20_out), .sel(shamtsrc_EX));
  // Probe on {J_JAL_addr_EX, 2'b00}
  Comparator #(.width(32)) comparator_3 (.a(R1_first_use), .b({32{1'b0}}), .lt(comparator_3_lt));  // open: gt, eq
  // Probe on mips_alu_1_result
  // Probe on R2_first_use
  EX_MEM ex_mem_1 (
    .RegDst_in(RegDst_EX), .JAL_in(JAL_EX), .RegWrite_in(RegWrite_EX), .MemToReg_in(MemToReg_EX),
    .MemWrite_in(MemWrite_EX), .IRin(IR_EX), .PCin(EX_PC), .Rin(R2_first_use),
    .ALUresult_in(mips_alu_1_result), .RegDst_out(RegDst_MEM), .JAL_out(JAL_MEM),
    .RegWrite_out(RegWrite_MEM), .MemToReg_out(MemToReg_MEM), .MemWrite_out(MemWrite_MEM), .IRout(IR_MEM),
    .PCout(MEM_PC), .Rout(ex_mem_1_rout), .ALUresult_out(ALUresult_MEM), .enable(id_ex_1_enable_out),
    .clk(CLK), .clear(RST), .enable_out(ex_mem_1_enable_out), .Rt_in(Rt_EX), .Rd_in(Rd_EX), .Rd_out(Rd_MEM),
    .Rt_out(Rt_MEM), .syscal_in(syscall_EX), .syscall_out(ex_mem_1_syscall_out),
    .byteorword_out(byteorword_MEM), .byteorword_in(byteorword_EX));
  // Probe on {J_JAL_addr_EX[11:2], 2'b00}
  // Probe on MEM_PC
  // Probe on ALUresult_MEM[11:2]
  not not_12 (not_12_out, MemWrite_MEM);
  RAM #(.addrWidth(10), .dataWidth(32), .bus("separate")) ram_1 (
    .addr(ALUresult_MEM[11:2]), .din(ex_mem_1_rout), .data(ram_1_data), .str(MemWrite_MEM), .clk(CLK),
    .ld(not_12_out), .clr(RST));  // open: sel
  MEM_WB MEM_WB (
    .RegDst_in(RegDst_MEM), .JAL_in(JAL_MEM), .RegWrite_in(RegWrite_MEM), .MemToReg_in(MemToReg_MEM),
    .IRin(IR_MEM), .PCin(MEM_PC), .ALUresult_in(ALUresult_MEM), .MemData_in(ram_1_data),
    .RegDst_out(RegDst_WB), .JAL_out(JAL_WB), .RegWrite_out(RegWrite_WB), .MemToReg_out(MemToReg_WB),
    .IRout(IR_WB), .PCout(PC_WB), .ALUresult_out(ALU_result_WB), .MemData_out(MEM_WB_memdata_out),
    .enable(ex_mem_1_enable_out), .clk(CLK), .clear(RST), .enable_out(pcable_out), .Rt_out(Rt_WB),
    .Rd_out(Rd_WB), .Rt_in(Rt_MEM), .Rd_in(Rd_MEM), .syscall_in(ex_mem_1_syscall_out),
    .syscall_out(syscall_WB), .byteorword_in(byteorword_MEM), .byteorword_out(byteorword_WB));
  Adder #(.width(32)) adder_5 (.a(PC_WB), .b(32'h4), .out(JAL_WB_Addr));  // open: cin, cout
  // Probe on ALU_result_WB
  Shifter #(.width(32), .shift("lr")) shifter_2 (
    .in(MEM_WB_memdata_out), .\dist ({ALU_result_WB[1:0], 3'b000}), .out(shifter_2_out));
  assign and_14_out = shifter_2_out & 32'hff;  // AND_Gate and_14, 32 bits wide
  Multiplexer #(.width(32), .enable("false")) multiplexer_21 (
    .in0(MEM_WB_memdata_out), .in1(and_14_out), .out(MemData_WB), .sel(byteorword_WB));

  // Other names for the same wires on the sheet: IR_ID[5:0] = Func_ID; J_JAL_imm_ID[25:0] = {IR_ID[25:6], Func_ID};
  //   Rd_ID[4:0] = IR_ID[15:11]; OP_ID[5:0] = IR_ID[31:26]; J_JAL_imm_EX[25:0] = J_JAL_addr_EX[27:2];
  //   Rt_ID[4:0] = IR_ID[20:16]; PC_EX[31:0] = EX_PC; PC_ID[31:0] = ID_PC; PC_IF[31:0] = IF_PC; PC_MEM[31:0] = MEM_PC;
  //   WB_PC[31:0] = PC_WB

  // Notes on the sheet:
  //   中断源
  //   中断等待指示
  //   数码管输出
  //   80-88
  //   流水调试日志用
  //   指令存储器
  //   contents of rom_1 (hex, n*v repeats v):
  //   20110001 8000c05 20110001 20120002 20130003 8000c09 20110001 20120002 20130003 8000c0d 20110001
  //   20120002 20130003 8000c11 20110001 20120002 20130003 c000cbb 20100001 20110001 118fc0 112020
  //   20020022 c 118882 12200001 8000c15 112020 20020022 c 20110001 118880 112020 20020022 c 12200001
  //   8000c1f 20110001 118fc0 112020 20020022 c 1188c3 112020 20020022 c 118903 112020 20020022 c 118903
  //   112020 20020022 c 118903 112020 20020022 c 118903 112020 20020022 c 118903 112020 20020022 c 118903
  //   112020 20020022 c 118903 112020 20020022 c 20100001 109fc0 139fc3 8021 2012000c 24160003 26100001
  //   3210000f 20080008 20090001 139900 2709825 132020 20020022 c 1094022 1500fff9 22100001 2018000f
  //   2188024 108700 20080008 20090001 139902 2709825 132021 20020022 c 1094022 1500fff9 108702 2c9b022
  //   12c00001 8000c50 4020 1084027 84400 3508ffff 82021 20020022 c 2010ffff 20110000 ae300000 22100001
  //   22310004 ae300000 22100001 22310004 ae300000 22100001 22310004 ae300000 22100001 22310004 ae300000
  //   22100001 22310004 ae300000 22100001 22310004 ae300000 22100001 22310004 ae300000 22100001 22310004
  //   ae300000 22100001 22310004 ae300000 22100001 22310004 ae300000 22100001 22310004 ae300000 22100001
  //   22310004 ae300000 22100001 22310004 ae300000 22100001 22310004 ae300000 22100001 22310004 ae300000
  //   22100001 22310004 22100001 8020 2011003c 8e130000 8e340000 274402a 11000002 ae330000 ae140000
  //   2231fffc 1611fff8 102020 20020022 c 22100004 2011003c 1611fff2 20020032 c 8000c00 2002000a c
  //   20100000 22100001 102020 20020022 c 22100002 102020 20020022 c 22100003 102020 20020022 c 22100004
  //   102020 20020022 c 22100005 102020 20020022 c 22100006 102020 20020022 c 22100007 102020 20020022 c
  //   22100008 102020 20020022 20020022 c 3e00008
  //   OP
  //   func
  //   rs
  //   rt
  //   rd
  //   数据寄存器
endmodule
